// Logisim project 8bit_riscvCPU.circ as structural Verilog: 15 circuits, main circuit main
module main (
);

  wire A_out, alu_1_b___a, alu_1_zero, and_1_out, clock_1_out, control_unit_1_alumux, control_unit_1_dataen,
       control_unit_1_datar_w, control_unit_1_flag, control_unit_1_halt, control_unit_1_immmux,
       control_unit_1_push_pop, control_unit_1_regen, control_unit_1_stacken, controls_1_p8, controls_1_p9,
       controls_1_p10, controls_1_p11, D_out, data_memory_1_out_11, flags_1_b_a, flags_1_zero_2,
       led_display_module_1_pixel_info, not_1_out, not_2_out, number_display_module_1_negative, S_out, W_out,
       xnor_1_out, xnor_2_out;
  wire [0:0] multiplexer_7_out;
  wire [1:0] control_unit_1_dmux, control_unit_1_pcmux, control_unit_1_wmux, data_memory_1_numdisp_settings,
       multiplexer_2_out;
  wire [2:0] control_unit_1_alucode, data_memory_1_chardisp_settings;
  wire [3:0] data_memory_1_screen_settings, multiplexer_3_out, number_display_module_1_hundred,
       number_display_module_1_one, number_display_module_1_ten;
  wire [4:0] data_memory_1_pixelx, data_memory_1_pixely;
  wire [6:0] character_display_module_1_out_3, character_display_module_1_out_4,
       character_display_module_1_out_5, character_display_module_1_out_6, character_display_module_1_out_7,
       character_display_module_1_out_8, character_display_module_1_out_9, character_display_module_1_out_10,
       character_display_module_1_out_11, character_display_module_1_out_12,
       character_display_module_1_out_13, character_display_module_1_out_14,
       character_display_module_1_out_15, character_display_module_1_out_16,
       character_display_module_1_out_17, character_display_module_1_out_18,
       character_display_module_1_out_19, character_display_module_1_out_20,
       character_display_module_1_out_21, character_display_module_1_out_22,
       character_display_module_1_out_23, character_display_module_1_out_24,
       character_display_module_1_out_25, character_display_module_1_out_26,
       character_display_module_1_out_27, character_display_module_1_out_28,
       character_display_module_1_out_29, character_display_module_1_out_30,
       character_display_module_1_out_31, character_display_module_1_out_32,
       character_display_module_1_out_33, character_display_module_1_out_34,
       character_display_module_1_out_35, character_display_module_1_out_36,
       character_display_module_1_out_37, character_display_module_1_out_38,
       character_display_module_1_out_39, character_display_module_1_out_40,
       character_display_module_1_out_41, character_display_module_1_out_42,
       character_display_module_1_out_43, character_display_module_1_out_44,
       character_display_module_1_out_45, character_display_module_1_out_46,
       character_display_module_1_out_47, character_display_module_1_out_48,
       character_display_module_1_out_49, character_display_module_1_out_50,
       character_display_module_1_out_51, character_display_module_1_out_52;
  wire [7:0] alu_1_out_5, controls_1_p1, data_memory_1_chardisp_data, data_memory_1_numdisp_data,
       data_memory_1_out_8, multiplexer_4_out, multiplexer_5_out, multiplexer_6_out, registers_1_r1_2,
       registers_1_r2_2;
  wire [9:0] adder_1_out, bit_extender_1_out, call_stack_1_addrout, instruction_memory_1_out_2,
       multiplexer_1_out, pc_1_out_3;
  wire [15:10] instruction_memory_1_out_2_2;
  wire [31:0] led_display_module_1_out_5, led_display_module_1_out_6, led_display_module_1_out_7,
       led_display_module_1_out_8, led_display_module_1_out_9, led_display_module_1_out_10,
       led_display_module_1_out_11, led_display_module_1_out_12, led_display_module_1_out_13,
       led_display_module_1_out_14, led_display_module_1_out_15, led_display_module_1_out_16,
       led_display_module_1_out_17, led_display_module_1_out_18, led_display_module_1_out_19,
       led_display_module_1_out_20, led_display_module_1_out_21, led_display_module_1_out_22,
       led_display_module_1_out_23, led_display_module_1_out_24, led_display_module_1_out_25,
       led_display_module_1_out_26, led_display_module_1_out_27, led_display_module_1_out_28,
       led_display_module_1_out_29, led_display_module_1_out_30, led_display_module_1_out_31,
       led_display_module_1_out_32, led_display_module_1_out_33, led_display_module_1_out_34,
       led_display_module_1_out_35, led_display_module_1_out_36;

  assign bit_extender_1_out = {{9{1'b0}}, 1'b1};  // Bit_Extender bit_extender_1
  Clock clock_1 (.out(clock_1_out));
  not not_1 (not_1_out, control_unit_1_halt);
  Adder #(.width(10)) adder_1 (.a(bit_extender_1_out), .b(pc_1_out_3), .out(adder_1_out));  // open: cin, cout
  Call_Stack call_stack_1 (
    .Push_Pop(control_unit_1_push_pop), .Addr(adder_1_out), .CLK(and_1_out), .En(control_unit_1_stacken),
    .AddrOut(call_stack_1_addrout));
  and and_1 (and_1_out, clock_1_out, not_1_out);
  Multiplexer #(.select(2), .width(10)) multiplexer_1 (
    .in0(adder_1_out), .in1(instruction_memory_1_out_2), .in2(call_stack_1_addrout), .out(multiplexer_1_out),
    .sel(multiplexer_2_out));  // open: in3, en
  Multiplexer #(.select(2), .width(2)) multiplexer_2 (
    .in0(2'b00), .in1(2'b01), .in2({1'b0, multiplexer_7_out[0]}), .in3(2'b10), .out(multiplexer_2_out),
    .sel(control_unit_1_pcmux));  // open: en
  PC pc_1 (.CLK(and_1_out), .in_2(multiplexer_1_out), .out_3(pc_1_out_3));
  Control_Unit control_unit_1 (
    .in_1(instruction_memory_1_out_2_2[15:12]), .PCmux(control_unit_1_pcmux), .Wmux(control_unit_1_wmux),
    .Dmux(control_unit_1_dmux), .ImmMux(control_unit_1_immmux), .ALUMux(control_unit_1_alumux),
    .Flag(control_unit_1_flag), .ALUcode(control_unit_1_alucode), .Push_Pop(control_unit_1_push_pop),
    .StackEn(control_unit_1_stacken), .RegEn(control_unit_1_regen), .DataR_W(control_unit_1_datar_w),
    .DataEn(control_unit_1_dataen), .Halt(control_unit_1_halt));
  Instruction_Memory instruction_memory_1 (
    .in_1(pc_1_out_3), .out_2({instruction_memory_1_out_2_2, instruction_memory_1_out_2}));
  Multiplexer #(.select(2), .width(4)) multiplexer_3 (
    .in0(instruction_memory_1_out_2[3:0]),
    .in1({instruction_memory_1_out_2_2[11:10], instruction_memory_1_out_2[9:8]}),
    .in2(instruction_memory_1_out_2[7:4]), .in3(4'b0000), .out(multiplexer_3_out), .sel(control_unit_1_wmux));  // open: en
  Multiplexer #(.select(2), .width(8)) multiplexer_4 (
    .in0(alu_1_out_5), .in1(instruction_memory_1_out_2[7:0]), .in2(data_memory_1_out_8),
    .out(multiplexer_4_out), .sel(control_unit_1_dmux));  // open: in3, en
  Multiplexer #(.width(8)) multiplexer_5 (
    .in0(instruction_memory_1_out_2[7:0]), .in1({4'b0000, instruction_memory_1_out_2[3:0]}),
    .out(multiplexer_5_out), .sel(control_unit_1_immmux));  // open: en
  Registers registers_1 (
    .R1({instruction_memory_1_out_2_2[11:10], instruction_memory_1_out_2[9:8]}),
    .R2(instruction_memory_1_out_2[7:4]), .W(multiplexer_3_out), .D(multiplexer_4_out), .CLK(and_1_out),
    .En(control_unit_1_regen), .R1_2(registers_1_r1_2), .R2_2(registers_1_r2_2));
  Multiplexer #(.width(8)) multiplexer_6 (
    .in0(registers_1_r2_2), .in1(multiplexer_5_out), .out(multiplexer_6_out), .sel(control_unit_1_alumux));  // open: en
  not not_2 (not_2_out, instruction_memory_1_out_2_2[10]);
  Flags flags_1 (
    .Zero(alu_1_zero), .B___A(alu_1_b___a), .Set_flag(control_unit_1_flag), .CLK(and_1_out),
    .Zero_2(flags_1_zero_2), .B_A(flags_1_b_a));
  ALU alu_1 (
    .in_1(control_unit_1_alucode), .in_2(registers_1_r1_2), .in_3(multiplexer_6_out), .B___A(alu_1_b___a),
    .out_5(alu_1_out_5), .Zero(alu_1_zero));
  xnor xnor_1 (xnor_1_out, not_2_out, flags_1_zero_2);
  xnor xnor_2 (xnor_2_out, instruction_memory_1_out_2_2[10], flags_1_b_a);
  Data_Memory data_memory_1 (
    .Data(registers_1_r2_2), .Addr(alu_1_out_5), .R_W(control_unit_1_datar_w), .CLK(and_1_out),
    .En(control_unit_1_dataen), .Cntrl_Input(controls_1_p1), .Screen_Input(led_display_module_1_pixel_info),
    .out_8(data_memory_1_out_8), .PixelX(data_memory_1_pixelx), .PixelY(data_memory_1_pixely),
    .NumDisp_Settings(data_memory_1_numdisp_settings), .NumDisp_Data(data_memory_1_numdisp_data),
    .CharDisp_Settings(data_memory_1_chardisp_settings), .CharDisp_Data(data_memory_1_chardisp_data),
    .Screen_Settings(data_memory_1_screen_settings), .out_11(data_memory_1_out_11));
  Multiplexer multiplexer_7 (
    .in0(xnor_1_out), .in1(xnor_2_out), .out(multiplexer_7_out[0]), .sel(instruction_memory_1_out_2_2[11]));  // open: en
  DotMatrix dotmatrix_1 (
    .col0(character_display_module_1_out_3), .col1(character_display_module_1_out_4),
    .col2(character_display_module_1_out_5), .col3(character_display_module_1_out_6),
    .col4(character_display_module_1_out_7));
  DotMatrix dotmatrix_2 (
    .col0(character_display_module_1_out_13), .col1(character_display_module_1_out_14),
    .col2(character_display_module_1_out_15), .col3(character_display_module_1_out_16),
    .col4(character_display_module_1_out_17));
  DotMatrix dotmatrix_3 (
    .col0(character_display_module_1_out_8), .col1(character_display_module_1_out_9),
    .col2(character_display_module_1_out_10), .col3(character_display_module_1_out_11),
    .col4(character_display_module_1_out_12));
  DotMatrix #(.matrixcols(32), .matrixrows(32)) dotmatrix_4 (
    .col0(led_display_module_1_out_5), .col1(led_display_module_1_out_6), .col2(led_display_module_1_out_7),
    .col3(led_display_module_1_out_8), .col4(led_display_module_1_out_9), .col5(led_display_module_1_out_10),
    .col6(led_display_module_1_out_11), .col7(led_display_module_1_out_12),
    .col8(led_display_module_1_out_13), .col9(led_display_module_1_out_14),
    .col10(led_display_module_1_out_15), .col11(led_display_module_1_out_16),
    .col12(led_display_module_1_out_17), .col13(led_display_module_1_out_18),
    .col14(led_display_module_1_out_19), .col15(led_display_module_1_out_20),
    .col16(led_display_module_1_out_21), .col17(led_display_module_1_out_22),
    .col18(led_display_module_1_out_23), .col19(led_display_module_1_out_24),
    .col20(led_display_module_1_out_25), .col21(led_display_module_1_out_26),
    .col22(led_display_module_1_out_27), .col23(led_display_module_1_out_28),
    .col24(led_display_module_1_out_29), .col25(led_display_module_1_out_30),
    .col26(led_display_module_1_out_31), .col27(led_display_module_1_out_32),
    .col28(led_display_module_1_out_33), .col29(led_display_module_1_out_34),
    .col30(led_display_module_1_out_35), .col31(led_display_module_1_out_36));
  DotMatrix dotmatrix_5 (
    .col0(character_display_module_1_out_18), .col1(character_display_module_1_out_19),
    .col2(character_display_module_1_out_20), .col3(character_display_module_1_out_21),
    .col4(character_display_module_1_out_22));
  LED_display_module led_display_module_1 (
    .PixelX(data_memory_1_pixely), .PixelX_2(data_memory_1_pixelx), .CLK(and_1_out),
    .Settings(data_memory_1_screen_settings), .out_5(led_display_module_1_out_5),
    .out_6(led_display_module_1_out_6), .out_7(led_display_module_1_out_7),
    .out_8(led_display_module_1_out_8), .out_9(led_display_module_1_out_9),
    .out_10(led_display_module_1_out_10), .out_11(led_display_module_1_out_11),
    .out_12(led_display_module_1_out_12), .out_13(led_display_module_1_out_13),
    .out_14(led_display_module_1_out_14), .out_15(led_display_module_1_out_15),
    .out_16(led_display_module_1_out_16), .out_17(led_display_module_1_out_17),
    .out_18(led_display_module_1_out_18), .out_19(led_display_module_1_out_19),
    .out_20(led_display_module_1_out_20), .out_21(led_display_module_1_out_21),
    .out_22(led_display_module_1_out_22), .out_23(led_display_module_1_out_23),
    .out_24(led_display_module_1_out_24), .out_25(led_display_module_1_out_25),
    .out_26(led_display_module_1_out_26), .out_27(led_display_module_1_out_27),
    .out_28(led_display_module_1_out_28), .out_29(led_display_module_1_out_29),
    .out_30(led_display_module_1_out_30), .out_31(led_display_module_1_out_31),
    .out_32(led_display_module_1_out_32), .out_33(led_display_module_1_out_33),
    .out_34(led_display_module_1_out_34), .out_35(led_display_module_1_out_35),
    .out_36(led_display_module_1_out_36), .Pixel_Info(led_display_module_1_pixel_info));
  DotMatrix dotmatrix_6 (
    .col0(character_display_module_1_out_23), .col1(character_display_module_1_out_24),
    .col2(character_display_module_1_out_25), .col3(character_display_module_1_out_26),
    .col4(character_display_module_1_out_27));
  DotMatrix #(.matrixcols(3), .matrixrows(1)) dotmatrix_7 (
    .col0(number_display_module_1_negative), .col1(number_display_module_1_negative),
    .col2(number_display_module_1_negative));
  Number_display_module number_display_module_1 (
    .Settings(data_memory_1_numdisp_settings), .Number(data_memory_1_numdisp_data),
    .Negative(number_display_module_1_negative), .Hundred(number_display_module_1_hundred),
    .Ten(number_display_module_1_ten), .One(number_display_module_1_one));
  Hex_Digit_Display hex_digit_display_1 (.value(number_display_module_1_hundred));  // open: dp
  DotMatrix dotmatrix_8 (
    .col0(character_display_module_1_out_33), .col1(character_display_module_1_out_34),
    .col2(character_display_module_1_out_35), .col3(character_display_module_1_out_36),
    .col4(character_display_module_1_out_37));
  DotMatrix dotmatrix_9 (
    .col0(character_display_module_1_out_28), .col1(character_display_module_1_out_29),
    .col2(character_display_module_1_out_30), .col3(character_display_module_1_out_31),
    .col4(character_display_module_1_out_32));
  Hex_Digit_Display hex_digit_display_2 (.value(number_display_module_1_ten));  // open: dp
  Hex_Digit_Display hex_digit_display_3 (.value(number_display_module_1_one));  // open: dp
  DotMatrix dotmatrix_10 (
    .col0(character_display_module_1_out_38), .col1(character_display_module_1_out_39),
    .col2(character_display_module_1_out_40), .col3(character_display_module_1_out_41),
    .col4(character_display_module_1_out_42));
  DotMatrix dotmatrix_11 (
    .col0(character_display_module_1_out_43), .col1(character_display_module_1_out_44),
    .col2(character_display_module_1_out_45), .col3(character_display_module_1_out_46),
    .col4(character_display_module_1_out_47));
  Button W (.out(W_out));
  Button A (.out(A_out));
  Button S (.out(S_out));
  DotMatrix dotmatrix_12 (
    .col0(character_display_module_1_out_48), .col1(character_display_module_1_out_49),
    .col2(character_display_module_1_out_50), .col3(character_display_module_1_out_51),
    .col4(character_display_module_1_out_52));
  Character_display_module character_display_module_1 (
    .Settings(data_memory_1_chardisp_settings), .Code(data_memory_1_chardisp_data),
    .out_3(character_display_module_1_out_3), .out_4(character_display_module_1_out_4),
    .out_5(character_display_module_1_out_5), .out_6(character_display_module_1_out_6),
    .out_7(character_display_module_1_out_7), .out_8(character_display_module_1_out_8),
    .out_9(character_display_module_1_out_9), .out_10(character_display_module_1_out_10),
    .out_11(character_display_module_1_out_11), .out_12(character_display_module_1_out_12),
    .out_13(character_display_module_1_out_13), .out_14(character_display_module_1_out_14),
    .out_15(character_display_module_1_out_15), .out_16(character_display_module_1_out_16),
    .out_17(character_display_module_1_out_17), .out_18(character_display_module_1_out_18),
    .out_19(character_display_module_1_out_19), .out_20(character_display_module_1_out_20),
    .out_21(character_display_module_1_out_21), .out_22(character_display_module_1_out_22),
    .out_23(character_display_module_1_out_23), .out_24(character_display_module_1_out_24),
    .out_25(character_display_module_1_out_25), .out_26(character_display_module_1_out_26),
    .out_27(character_display_module_1_out_27), .out_28(character_display_module_1_out_28),
    .out_29(character_display_module_1_out_29), .out_30(character_display_module_1_out_30),
    .out_31(character_display_module_1_out_31), .out_32(character_display_module_1_out_32),
    .out_33(character_display_module_1_out_33), .out_34(character_display_module_1_out_34),
    .out_35(character_display_module_1_out_35), .out_36(character_display_module_1_out_36),
    .out_37(character_display_module_1_out_37), .out_38(character_display_module_1_out_38),
    .out_39(character_display_module_1_out_39), .out_40(character_display_module_1_out_40),
    .out_41(character_display_module_1_out_41), .out_42(character_display_module_1_out_42),
    .out_43(character_display_module_1_out_43), .out_44(character_display_module_1_out_44),
    .out_45(character_display_module_1_out_45), .out_46(character_display_module_1_out_46),
    .out_47(character_display_module_1_out_47), .out_48(character_display_module_1_out_48),
    .out_49(character_display_module_1_out_49), .out_50(character_display_module_1_out_50),
    .out_51(character_display_module_1_out_51), .out_52(character_display_module_1_out_52));
  Button D (.out(D_out));
  // Controls controls_1: pin names not known; wires that end beside it: controls_1_p1, and_1_out, data_memory_1_out_11, W_out, A_out, S_out, D_out, controls_1_p8, controls_1_p9, controls_1_p10, controls_1_p11
  Button R (.out(controls_1_p9));
  Button S_2 (.out(controls_1_p8));
  Button A_2 (.out(controls_1_p10));
  Button B (.out(controls_1_p11));
endmodule

module PC (
  input  CLK,
  input  [9:0] in_2,
  output [9:0] out_3
);

  Register #(.width(10)) register_1 (.D(in_2), .Q(out_3), .clk(CLK));  // open: en, clr
endmodule

module Instruction_Memory (
  input  [9:0] in_1,
  output [15:0] out_2
);

  RAM #(.addrWidth(10), .dataWidth(16)) ram_1 (.addr(in_1), .data(out_2));  // open: sel, clk, ld, clr
endmodule

module Registers (
  input  [3:0] R1,
  input  [3:0] R2,
  input  [3:0] W,
  input  [7:0] D,
  input  CLK,
  input  En,
  output [7:0] R1_2,
  output [7:0] R2_2
);

  wire and_1_out, button_1_out, demultiplexer_1_out0, demultiplexer_1_out1, demultiplexer_1_out2,
       demultiplexer_1_out3, demultiplexer_1_out4, demultiplexer_1_out5, demultiplexer_1_out6,
       demultiplexer_1_out7, demultiplexer_1_out8, demultiplexer_1_out9, demultiplexer_1_out10,
       demultiplexer_1_out11, demultiplexer_1_out12, demultiplexer_1_out13, demultiplexer_1_out14,
       demultiplexer_1_out15, not_1_out;
  wire [7:0] multiplexer_1_out, multiplexer_2_out, register_1_q, register_2_q, register_3_q, register_4_q,
       register_5_q, register_6_q, register_7_q, register_8_q, register_9_q, register_10_q, register_11_q,
       register_12_q, register_13_q, register_14_q, register_15_q;

  and and_1 (and_1_out, CLK, En);
  Demultiplexer #(.select(4)) demultiplexer_1 (
    .out0(demultiplexer_1_out0), .out1(demultiplexer_1_out1), .out2(demultiplexer_1_out2),
    .out3(demultiplexer_1_out3), .out4(demultiplexer_1_out4), .out5(demultiplexer_1_out5),
    .out6(demultiplexer_1_out6), .out7(demultiplexer_1_out7), .out8(demultiplexer_1_out8),
    .out9(demultiplexer_1_out9), .out10(demultiplexer_1_out10), .out11(demultiplexer_1_out11),
    .out12(demultiplexer_1_out12), .out13(demultiplexer_1_out13), .out14(demultiplexer_1_out14),
    .out15(demultiplexer_1_out15), .in(not_1_out), .sel(W));  // open: en
  not not_1 (not_1_out, and_1_out);
  Register register_1 (.D(D), .Q(register_1_q), .clk(demultiplexer_1_out8), .clr(button_1_out));  // open: en
  Register register_2 (.D(D), .Q(register_2_q), .clk(demultiplexer_1_out1), .clr(button_1_out));  // open: en
  Register register_3 (.D(D), .Q(register_3_q), .clk(demultiplexer_1_out9), .clr(button_1_out));  // open: en
  Register register_4 (.D(D), .Q(register_4_q), .clk(demultiplexer_1_out2), .clr(button_1_out));  // open: en
  Register register_5 (.D(D), .Q(register_5_q), .clk(demultiplexer_1_out10), .clr(button_1_out));  // open: en
  Register register_6 (.D(D), .Q(register_6_q), .clk(demultiplexer_1_out3), .clr(button_1_out));  // open: en
  Register register_7 (.D(D), .Q(register_7_q), .clk(demultiplexer_1_out11), .clr(button_1_out));  // open: en
  Register register_8 (.D(D), .Q(register_8_q), .clk(demultiplexer_1_out4), .clr(button_1_out));  // open: en
  Register register_9 (.D(D), .Q(register_9_q), .clk(demultiplexer_1_out12), .clr(button_1_out));  // open: en
  Register register_10 (.D(D), .Q(register_10_q), .clk(demultiplexer_1_out5), .clr(button_1_out));  // open: en
  Register register_11 (.D(D), .Q(register_11_q), .clk(demultiplexer_1_out13), .clr(button_1_out));  // open: en
  Register register_12 (.D(D), .Q(register_12_q), .clk(demultiplexer_1_out6), .clr(button_1_out));  // open: en
  Register register_13 (.D(D), .Q(register_13_q), .clk(demultiplexer_1_out14), .clr(button_1_out));  // open: en
  Register register_14 (.D(D), .Q(register_14_q), .clk(demultiplexer_1_out7), .clr(button_1_out));  // open: en
  Register register_15 (.D(D), .Q(register_15_q), .clk(demultiplexer_1_out15), .clr(button_1_out));  // open: en
  Button button_1 (.out(button_1_out));
  Multiplexer #(.select(4), .width(8)) multiplexer_1 (
    .in0({8{1'b0}}), .in1(register_2_q), .in2(register_4_q), .in3(register_6_q), .in4(register_8_q),
    .in5(register_10_q), .in6(register_12_q), .in7(register_14_q), .in8(register_1_q), .in9(register_3_q),
    .in10(register_5_q), .in11(register_7_q), .in12(register_9_q), .in13(register_11_q),
    .in14(register_13_q), .in15(register_15_q), .out(multiplexer_1_out), .sel(R1));  // open: en
  Multiplexer #(.select(4), .width(8)) multiplexer_2 (
    .in0({8{1'b0}}), .in1(register_2_q), .in2(register_4_q), .in3(register_6_q), .in4(register_8_q),
    .in5(register_10_q), .in6(register_12_q), .in7(register_14_q), .in8(register_1_q), .in9(register_3_q),
    .in10(register_5_q), .in11(register_7_q), .in12(register_9_q), .in13(register_11_q),
    .in14(register_13_q), .in15(register_15_q), .out(multiplexer_2_out), .sel(R2));  // open: en
  assign R1_2 = multiplexer_1_out & {8{En}};  // AND_Gate and_2, 8 bits wide
  assign R2_2 = multiplexer_2_out & {8{En}};  // AND_Gate and_3, 8 bits wide
endmodule

module ALU (
  input  [2:0] in_1,
  input  [7:0] in_2,
  input  [7:0] in_3,
  output B___A,
  output [7:0] out_5,
  output Zero
);

  wire not_1_out, not_2_out, not_3_out, not_4_out, not_5_out, not_6_out, not_7_out, not_8_out;
  wire [6:0] adder_2_out;
  wire [7:0] adder_1_out, and_1_out, bit_extender_1_out, bit_extender_2_out, nor_1_out, xor_1_out, xor_2_out;

  assign bit_extender_1_out = {{7{1'b0}}, in_1[0]};  // Bit_Extender bit_extender_1
  assign bit_extender_2_out = {{7{in_1[0]}}, in_1[0]};  // Bit_Extender bit_extender_2
  assign xor_1_out = in_3 ^ bit_extender_2_out;  // XOR_Gate xor_1, 8 bits wide
  assign nor_1_out = ~(in_2 | in_3);  // NOR_Gate nor_1, 8 bits wide
  assign and_1_out = in_2 & in_3;  // AND_Gate and_1, 8 bits wide
  assign xor_2_out = in_2 ^ in_3;  // XOR_Gate xor_2, 8 bits wide
  Adder adder_1 (.a(bit_extender_1_out), .b(xor_1_out), .out(adder_1_out));  // open: cin, cout
  not not_1 (not_1_out, xor_2_out[0]);
  not not_2 (not_2_out, xor_2_out[1]);
  not not_3 (not_3_out, xor_2_out[2]);
  not not_4 (not_4_out, xor_2_out[3]);
  not not_5 (not_5_out, xor_2_out[4]);
  not not_6 (not_6_out, xor_2_out[5]);
  not not_7 (not_7_out, xor_2_out[6]);
  not not_8 (not_8_out, xor_2_out[7]);
  Adder adder_2 (.a(in_2), .b(adder_1_out), .out({B___A, adder_2_out}));  // open: cin, cout
  and and_2 (Zero, not_1_out, not_2_out, not_3_out, not_4_out, not_6_out, not_7_out, not_8_out, not_5_out);
  Multiplexer #(.select(3), .width(8)) multiplexer_1 (
    .in0({B___A, adder_2_out}), .in1({B___A, adder_2_out}), .in2(nor_1_out), .in3(and_1_out),
    .in4(xor_2_out), .in5({in_1[1], in_2[7:1]}), .out(out_5), .sel(in_1));  // open: in6, in7, en
endmodule

module Number_display_module (
  input  [1:0] Settings,
  input  [7:0] Number,
  output Negative,
  output [3:0] Hundred,
  output [3:0] Ten,
  output [3:0] One
);

  wire and_1_out, and_2_out, and_3_out, and_4_out, and_5_out, and_6_out, and_7_out, or_1_out, or_2_out,
       or_3_out, or_4_out, or_5_out, or_6_out, or_7_out, or_8_out, or_9_out, or_10_out, or_11_out, or_12_out,
       or_13_out, or_14_out;
  wire [0:0] xor_1_out_2, xor_1_out_3, xor_1_out_4;
  wire [2:0] multiplexer_4_out;
  wire [2:2] multiplexer_4_out_2;
  wire [3:0] adder_2_out, adder_3_out, adder_4_out, adder_5_out, adder_6_out, adder_7_out, adder_8_out,
       multiplexer_5_out, multiplexer_6_out, multiplexer_7_out, multiplexer_8_out, multiplexer_9_out,
       multiplexer_10_out;
  wire [7:0] adder_1_out, bit_extender_1_out, xor_1_out;

  Adder adder_1 (.a(Number), .b(bit_extender_1_out), .out(adder_1_out));  // open: cin, cout
  assign bit_extender_1_out = {{7{Settings[1]}}, Settings[1]};  // Bit_Extender bit_extender_1
  Multiplexer #(.width(4)) multiplexer_1 (
    .in0({2'b00, multiplexer_8_out[3], multiplexer_10_out[3]}), .out(Hundred), .sel(Settings[0]));  // open: in1, en
  assign {xor_1_out[7:4], xor_1_out_2[0], xor_1_out_3[0], xor_1_out_4[0], xor_1_out[0]} = adder_1_out ^ bit_extender_1_out;  // XOR_Gate xor_1, 8 bits wide
  Multiplexer #(.width(4)) multiplexer_2 (
    .in0({multiplexer_10_out[2:0], multiplexer_9_out[3]}), .out(Ten), .sel(Settings[0]));  // open: in1, en
  Multiplexer #(.width(4)) multiplexer_3 (
    .in0({multiplexer_9_out[2:0], xor_1_out[0]}), .out(One), .sel(Settings[0]));  // open: in1, en
  or or_1 (or_1_out, xor_1_out[5], xor_1_out[6]);
  and and_1 (and_1_out, or_1_out, xor_1_out[7]);
  or or_2 (or_2_out, and_1_out, 1'b0);
  Multiplexer #(.width(4)) multiplexer_4 (
    .in0({1'b0, xor_1_out[7:5]}), .in1(adder_2_out), .out({multiplexer_4_out_2[2], multiplexer_4_out}),
    .sel(or_2_out));  // open: en
  Adder #(.width(4)) adder_2 (.a({1'b0, xor_1_out[7:5]}), .b(4'b0011), .out(adder_2_out));  // open: cin, cout
  or or_3 (or_3_out, xor_1_out[4], multiplexer_4_out[0]);
  and and_2 (and_2_out, or_3_out, multiplexer_4_out[1]);
  or or_4 (or_4_out, and_2_out, multiplexer_4_out[2]);
  Adder #(.width(4)) adder_3 (
    .a({multiplexer_4_out, xor_1_out[4]}), .b(4'b0011), .out(adder_3_out));  // open: cin, cout
  Multiplexer #(.width(4)) multiplexer_5 (
    .in0({multiplexer_4_out, xor_1_out[4]}), .in1(adder_3_out), .out(multiplexer_5_out), .sel(or_4_out));  // open: en
  or or_5 (or_5_out, xor_1_out_2[0], multiplexer_5_out[0]);
  and and_3 (and_3_out, or_5_out, multiplexer_5_out[1]);
  or or_6 (or_6_out, and_3_out, multiplexer_5_out[2]);
  Adder #(.width(4)) adder_4 (
    .a({multiplexer_5_out[2:0], xor_1_out_2[0]}), .b(4'b0011), .out(adder_4_out));  // open: cin, cout
  Multiplexer #(.width(4)) multiplexer_6 (
    .in0({multiplexer_5_out[2:0], xor_1_out_2[0]}), .in1(adder_4_out), .out(multiplexer_6_out), .sel(or_6_out));  // open: en
  or or_7 (or_7_out, xor_1_out_3[0], multiplexer_6_out[0]);
  or or_8 (or_8_out, multiplexer_6_out[3], multiplexer_5_out[3]);
  and and_4 (and_4_out, or_7_out, multiplexer_6_out[1]);
  or or_9 (or_9_out, and_4_out, multiplexer_6_out[2]);
  Adder #(.width(4)) adder_5 (
    .a({multiplexer_6_out[2:0], xor_1_out_3[0]}), .b(4'b0011), .out(adder_5_out));  // open: cin, cout
  and and_5 (and_5_out, or_8_out, multiplexer_4_out_2[2]);
  or or_10 (or_10_out, and_5_out, 1'b0);
  Adder #(.width(4)) adder_6 (
    .a({1'b0, multiplexer_4_out_2[2], multiplexer_5_out[3], multiplexer_6_out[3]}), .b(4'b0011),
    .out(adder_6_out));  // open: cin, cout
  Multiplexer #(.width(4)) multiplexer_7 (
    .in0({multiplexer_6_out[2:0], xor_1_out_3[0]}), .in1(adder_5_out), .out(multiplexer_7_out), .sel(or_9_out));  // open: en
  Multiplexer #(.width(4)) multiplexer_8 (
    .in0({1'b0, multiplexer_4_out_2[2], multiplexer_5_out[3], multiplexer_6_out[3]}), .in1(adder_6_out),
    .out(multiplexer_8_out), .sel(or_10_out));  // open: en
  or or_11 (or_11_out, xor_1_out_4[0], multiplexer_7_out[0]);
  or or_12 (or_12_out, multiplexer_7_out[3], multiplexer_8_out[0]);
  and and_6 (and_6_out, or_11_out, multiplexer_7_out[1]);
  Adder #(.width(4)) adder_7 (
    .a({multiplexer_7_out[2:0], xor_1_out_4[0]}), .b(4'b0011), .out(adder_7_out));  // open: cin, cout
  and and_7 (and_7_out, or_12_out, multiplexer_8_out[1]);
  Adder #(.width(4)) adder_8 (
    .a({multiplexer_8_out[2:0], multiplexer_7_out[3]}), .b(4'b0011), .out(adder_8_out));  // open: cin, cout
  or or_13 (or_13_out, and_6_out, multiplexer_7_out[2]);
  Multiplexer #(.width(4)) multiplexer_9 (
    .in0({multiplexer_7_out[2:0], xor_1_out_4[0]}), .in1(adder_7_out), .out(multiplexer_9_out),
    .sel(or_13_out));  // open: en
  or or_14 (or_14_out, and_7_out, multiplexer_8_out[2]);
  Multiplexer #(.width(4)) multiplexer_10 (
    .in0({multiplexer_8_out[2:0], multiplexer_7_out[3]}), .in1(adder_8_out), .out(multiplexer_10_out),
    .sel(or_14_out));  // open: en

  assign Negative = Settings[1];
endmodule

module Data_Memory (
  input  [7:0] Data,
  input  [7:0] Addr,
  input  R_W,
  input  CLK,
  input  En,
  input  [7:0] Cntrl_Input,
  input  Screen_Input,
  output [7:0] out_8,
  output [4:0] PixelX,
  output [4:0] PixelY,
  output out_11,
  output [1:0] NumDisp_Settings,
  output [7:0] NumDisp_Data,
  output [2:0] CharDisp_Settings,
  output [7:0] CharDisp_Data,
  output [3:0] Screen_Settings
);

  wire and_2_out, and_3_out, button_1_out, demultiplexer_4_out0, demultiplexer_4_out1, demultiplexer_4_out2,
       demultiplexer_4_out3, demultiplexer_4_out4, demultiplexer_4_out10, demultiplexer_4_out11,
       demultiplexer_4_out12, demultiplexer_4_out13, demultiplexer_4_out14, multiplexer_1_out,
       multiplexer_4_out, not_1_out, not_2_out, not_3_out, not_4_out, or_1_out, t_ff_1_qn, xor_1_out,
       xor_2_out, xor_3_out, xor_4_out;
  wire [2:0] register_1_q;
  wire [3:0] demultiplexer_5_out0, demultiplexer_5_out1;
  wire [4:0] demultiplexer_3_out0, demultiplexer_3_out1;
  wire [5:0] demultiplexer_2_out0, demultiplexer_2_out1;
  wire [6:0] demultiplexer_1_out0, demultiplexer_1_out1;
  wire [7:0] and_1_out, bit_extender_1_out, multiplexer_2_out, multiplexer_3_out, multiplexer_5_out,
       multiplexer_6_out, multiplexer_7_out, ram_1_data, ram_2_data, ram_3_data, ram_4_data, random_1_out,
       register_2_q, register_3_q, register_4_q, register_5_q, register_7_q, register_8_q, register_9_q,
       register_10_q, register_11_q, register_12_q, register_13_q, register_14_q, register_16_q;

  assign and_1_out = Addr & {8{En}};  // AND_Gate and_1, 8 bits wide
  Demultiplexer #(.width(7)) demultiplexer_1 (
    .out0(demultiplexer_1_out0), .out1(demultiplexer_1_out1), .in(and_1_out[6:0]), .sel(and_1_out[7]));  // open: en
  Demultiplexer #(.width(6)) demultiplexer_2 (
    .out0(demultiplexer_2_out0), .out1(demultiplexer_2_out1), .in(demultiplexer_1_out1[5:0]),
    .sel(demultiplexer_1_out1[6]));  // open: en
  Demultiplexer #(.width(5)) demultiplexer_3 (
    .out0(demultiplexer_3_out0), .out1(demultiplexer_3_out1), .in(demultiplexer_2_out1[4:0]),
    .sel(demultiplexer_2_out1[5]));  // open: en
  Demultiplexer #(.select(4)) demultiplexer_4 (
    .out0(demultiplexer_4_out0), .out1(demultiplexer_4_out1), .out2(demultiplexer_4_out2),
    .out3(demultiplexer_4_out3), .out4(demultiplexer_4_out4), .out5(Screen_Settings[2]),
    .out6(Screen_Settings[3]), .out7(CharDisp_Settings[2]), .out8(CharDisp_Settings[1]),
    .out9(CharDisp_Settings[0]), .out10(demultiplexer_4_out10), .out11(demultiplexer_4_out11),
    .out12(demultiplexer_4_out12), .out13(demultiplexer_4_out13), .out14(demultiplexer_4_out14),
    .out15(out_11), .in(not_1_out), .sel(demultiplexer_5_out1));  // open: en
  not not_1 (not_1_out, CLK);
  Button button_1 (.out(button_1_out));
  assign bit_extender_1_out = {{7{Screen_Input}}, Screen_Input};  // Bit_Extender bit_extender_1
  Demultiplexer #(.width(4)) demultiplexer_5 (
    .out0(demultiplexer_5_out0), .out1(demultiplexer_5_out1), .in(demultiplexer_3_out1[3:0]),
    .sel(demultiplexer_3_out1[4]));  // open: en
  Register register_1 (
    .D(Data), .Q({register_1_q, PixelX}), .clk(demultiplexer_4_out0), .clr(button_1_out));  // open: en
  Register register_2 (.D(Data), .Q(register_2_q), .clk(CharDisp_Settings[1]), .clr(button_1_out));  // open: en
  not not_2 (not_2_out, and_1_out[7]);
  xor xor_1 (xor_1_out, and_1_out[7], demultiplexer_1_out1[6]);
  xor xor_2 (xor_2_out, demultiplexer_1_out1[6], demultiplexer_2_out1[5]);
  xor xor_3 (xor_3_out, demultiplexer_2_out1[5], demultiplexer_3_out1[4]);
  Register register_3 (.D(Data), .Q(register_3_q), .clk(demultiplexer_4_out1), .clr(button_1_out));  // open: en
  Register register_4 (.D(Data), .Q(register_4_q), .clk(CharDisp_Settings[0]), .clr(button_1_out));  // open: en
  Pull_Resistor pull_resistor_1 (.node(CharDisp_Settings[2]));
  Pull_Resistor pull_resistor_2 (.node(CharDisp_Settings[1]));
  Register register_5 (.D(Data), .Q(register_5_q), .clk(demultiplexer_4_out2), .clr(button_1_out));  // open: en
  Register register_6 (.D(Data), .Q(NumDisp_Data), .clk(demultiplexer_4_out10), .clr(button_1_out));  // open: en
  Pull_Resistor pull_resistor_3 (.node(demultiplexer_4_out2));
  Pull_Resistor pull_resistor_4 (.node(demultiplexer_4_out3));
  Pull_Resistor pull_resistor_5 (.node(CharDisp_Settings[0]));
  RAM #(.addrWidth(7), .bus("separate")) ram_1 (
    .addr(demultiplexer_1_out0), .din(Data), .data(ram_1_data), .str(R_W), .sel(not_2_out), .clk(not_1_out));  // open: ld, clr
  RAM #(.addrWidth(6), .bus("separate")) ram_2 (
    .addr(demultiplexer_2_out0), .din(Data), .data(ram_2_data), .str(R_W), .sel(xor_1_out), .clk(not_1_out));  // open: ld, clr
  RAM #(.addrWidth(5), .bus("separate")) ram_3 (
    .addr(demultiplexer_3_out0), .din(Data), .data(ram_3_data), .str(R_W), .sel(xor_2_out), .clk(not_1_out));  // open: ld, clr
  RAM #(.addrWidth(4), .bus("separate")) ram_4 (
    .addr(demultiplexer_5_out0), .din(Data), .data(ram_4_data), .str(R_W), .sel(xor_3_out), .clk(not_1_out));  // open: ld, clr
  Register register_7 (
    .D(bit_extender_1_out), .Q(register_7_q), .clk(demultiplexer_4_out4), .clr(button_1_out));  // open: en
  Register register_8 (.D(Data), .Q(register_8_q), .clk(demultiplexer_4_out3), .clr(button_1_out));  // open: en
  Register register_9 (.D(Data), .Q(register_9_q), .clk(demultiplexer_4_out11), .clr(button_1_out));  // open: en
  Register register_10 (.D(Data), .Q(register_10_q), .clk(demultiplexer_4_out12), .clr(button_1_out));  // open: en
  Random random_1 (.clk(not_1_out), .out(random_1_out));  // open: next, clr
  not not_3 (not_3_out, Screen_Settings[0]);
  Pull_Resistor pull_resistor_6 (.node(Screen_Settings[2]));
  Pull_Resistor pull_resistor_7 (.node(Screen_Settings[3]));
  Register register_11 (.D(Data), .Q(register_11_q), .clk(Screen_Settings[2]), .clr(button_1_out));  // open: en
  Register register_12 (.D(Data), .Q(register_12_q), .clk(demultiplexer_4_out13), .clr(button_1_out));  // open: en
  and and_2 (and_2_out, t_ff_1_qn, and_3_out);
  and and_3 (and_3_out, not_3_out, demultiplexer_4_out3);
  Register register_13 (.D(Data), .Q(register_13_q), .clk(Screen_Settings[3]), .clr(button_1_out));  // open: en
  Register register_14 (
    .D(random_1_out), .Q(register_14_q), .clk(demultiplexer_4_out14), .clr(button_1_out));  // open: en
  Multiplexer multiplexer_1 (
    .in0(and_2_out), .in1(Screen_Settings[1]), .out(multiplexer_1_out), .sel(demultiplexer_4_out2));  // open: en
  not not_4 (not_4_out, demultiplexer_4_out3);
  Register register_15 (.D(Data), .Q(CharDisp_Data), .clk(CharDisp_Settings[2]), .clr(button_1_out));  // open: en
  Register register_16 (.D(Cntrl_Input), .Q(register_16_q), .clk(out_11), .clr(button_1_out));  // open: en
  T_Flip_Flop t_ff_1 (
    .clk(not_1_out), .T(multiplexer_1_out), .Q(Screen_Settings[1]), .Qn(t_ff_1_qn));  // open: preset, reset, en
  or or_1 (or_1_out, demultiplexer_4_out2, not_4_out);
  S_R_Flip_Flop s_r_ff_1 (
    .S(demultiplexer_4_out12), .clk(not_1_out), .R(demultiplexer_4_out13), .Q(NumDisp_Settings[1]));  // open: Qn, preset, reset, en
  xor xor_4 (xor_4_out, Screen_Settings[0], t_ff_1_qn);
  Multiplexer #(.width(8)) multiplexer_2 (
    .in0(ram_4_data), .in1(multiplexer_3_out), .out(multiplexer_2_out), .sel(demultiplexer_3_out1[4]));  // open: en
  Multiplexer #(.select(4), .width(8)) multiplexer_3 (
    .in0({register_1_q, PixelX}), .in1(register_3_q), .in2(register_5_q), .in3(register_8_q),
    .in4(register_7_q), .in5(register_11_q), .in6(register_13_q), .in7(CharDisp_Data), .in8(register_2_q),
    .in9(register_4_q), .in10(NumDisp_Data), .in11(register_9_q), .in12(register_10_q), .in13(register_12_q),
    .in14(register_14_q), .in15(register_16_q), .out(multiplexer_3_out), .sel(demultiplexer_5_out1));  // open: en
  T_Flip_Flop t_ff_2 (
    .clk(demultiplexer_4_out11), .T(demultiplexer_4_out11), .Q(NumDisp_Settings[0]));  // open: Qn, preset, reset, en
  T_Flip_Flop t_ff_3 (.clk(not_1_out), .T(multiplexer_4_out), .Q(Screen_Settings[0]));  // open: Qn, preset, reset, en
  Multiplexer multiplexer_4 (
    .in0(Screen_Settings[0]), .in1(xor_4_out), .out(multiplexer_4_out), .sel(or_1_out));  // open: en
  Multiplexer #(.width(8)) multiplexer_5 (
    .in0(ram_3_data), .in1(multiplexer_2_out), .out(multiplexer_5_out), .sel(demultiplexer_2_out1[5]));  // open: en
  Multiplexer #(.width(8)) multiplexer_6 (
    .in0(ram_1_data), .in1(multiplexer_7_out), .out(multiplexer_6_out), .sel(and_1_out[7]));  // open: en
  Multiplexer #(.width(8)) multiplexer_7 (
    .in0(ram_2_data), .in1(multiplexer_5_out), .out(multiplexer_7_out), .sel(demultiplexer_1_out1[6]));  // open: en
  assign out_8 = multiplexer_6_out & {8{En}};  // AND_Gate and_4, 8 bits wide

  assign PixelY = PixelX;
endmodule

module Call_Stack (
  input  Push_Pop,
  input  [9:0] Addr,
  input  CLK,
  input  En,
  output [9:0] AddrOut
);

  wire and_1_out, button_1_out, not_1_out;
  wire [9:0] multiplexer_1_out, multiplexer_2_out, multiplexer_3_out, multiplexer_4_out, multiplexer_5_out,
       multiplexer_6_out, multiplexer_7_out, multiplexer_8_out, multiplexer_9_out, multiplexer_10_out,
       multiplexer_11_out, multiplexer_12_out, multiplexer_13_out, multiplexer_14_out, multiplexer_15_out,
       multiplexer_16_out, register_1_q, register_2_q, register_3_q, register_4_q, register_5_q,
       register_6_q, register_7_q, register_8_q, register_9_q, register_10_q, register_11_q, register_12_q,
       register_13_q, register_14_q, register_15_q, register_16_q;

  and and_1 (and_1_out, CLK, En);
  not not_1 (not_1_out, and_1_out);
  Multiplexer #(.width(10)) multiplexer_1 (
    .in0(register_2_q), .in1(register_3_q), .out(multiplexer_1_out), .sel(Push_Pop));  // open: en
  Multiplexer #(.width(10)) multiplexer_2 (
    .in0(Addr), .in1(register_1_q), .out(multiplexer_2_out), .sel(Push_Pop));  // open: en
  Register #(.width(10)) register_1 (
    .D(multiplexer_1_out), .Q(register_1_q), .clk(not_1_out), .clr(button_1_out));  // open: en
  Register #(.width(10)) register_2 (
    .D(multiplexer_2_out), .Q(register_2_q), .clk(not_1_out), .clr(button_1_out));  // open: en
  assign AddrOut = register_2_q & {10{En}};  // AND_Gate and_2, 10 bits wide
  Multiplexer #(.width(10)) multiplexer_3 (
    .in0(register_1_q), .in1(register_4_q), .out(multiplexer_3_out), .sel(Push_Pop));  // open: en
  Register #(.width(10)) register_3 (
    .D(multiplexer_3_out), .Q(register_3_q), .clk(not_1_out), .clr(button_1_out));  // open: en
  Multiplexer #(.width(10)) multiplexer_4 (
    .in0(register_3_q), .in1(register_5_q), .out(multiplexer_4_out), .sel(Push_Pop));  // open: en
  Register #(.width(10)) register_4 (
    .D(multiplexer_4_out), .Q(register_4_q), .clk(not_1_out), .clr(button_1_out));  // open: en
  Multiplexer #(.width(10)) multiplexer_5 (
    .in0(register_4_q), .in1(register_6_q), .out(multiplexer_5_out), .sel(Push_Pop));  // open: en
  Register #(.width(10)) register_5 (
    .D(multiplexer_5_out), .Q(register_5_q), .clk(not_1_out), .clr(button_1_out));  // open: en
  Multiplexer #(.width(10)) multiplexer_6 (
    .in0(register_5_q), .in1(register_7_q), .out(multiplexer_6_out), .sel(Push_Pop));  // open: en
  Register #(.width(10)) register_6 (
    .D(multiplexer_6_out), .Q(register_6_q), .clk(not_1_out), .clr(button_1_out));  // open: en
  Multiplexer #(.width(10)) multiplexer_7 (
    .in0(register_6_q), .in1(register_8_q), .out(multiplexer_7_out), .sel(Push_Pop));  // open: en
  Register #(.width(10)) register_7 (
    .D(multiplexer_7_out), .Q(register_7_q), .clk(not_1_out), .clr(button_1_out));  // open: en
  Multiplexer #(.width(10)) multiplexer_8 (
    .in0(register_7_q), .in1(register_9_q), .out(multiplexer_8_out), .sel(Push_Pop));  // open: en
  Register #(.width(10)) register_8 (
    .D(multiplexer_8_out), .Q(register_8_q), .clk(not_1_out), .clr(button_1_out));  // open: en
  Multiplexer #(.width(10)) multiplexer_9 (
    .in0(register_9_q), .in1(register_11_q), .out(multiplexer_9_out), .sel(Push_Pop));  // open: en
  Multiplexer #(.width(10)) multiplexer_10 (
    .in0(register_8_q), .in1(register_10_q), .out(multiplexer_10_out), .sel(Push_Pop));  // open: en
  Register #(.width(10)) register_9 (
    .D(multiplexer_10_out), .Q(register_9_q), .clk(not_1_out), .clr(button_1_out));  // open: en
  Register #(.width(10)) register_10 (
    .D(multiplexer_9_out), .Q(register_10_q), .clk(not_1_out), .clr(button_1_out));  // open: en
  Multiplexer #(.width(10)) multiplexer_11 (
    .in0(register_10_q), .in1(register_12_q), .out(multiplexer_11_out), .sel(Push_Pop));  // open: en
  Register #(.width(10)) register_11 (
    .D(multiplexer_11_out), .Q(register_11_q), .clk(not_1_out), .clr(button_1_out));  // open: en
  Multiplexer #(.width(10)) multiplexer_12 (
    .in0(register_11_q), .in1(register_13_q), .out(multiplexer_12_out), .sel(Push_Pop));  // open: en
  Register #(.width(10)) register_12 (
    .D(multiplexer_12_out), .Q(register_12_q), .clk(not_1_out), .clr(button_1_out));  // open: en
  Button button_1 (.out(button_1_out));
  Multiplexer #(.width(10)) multiplexer_13 (
    .in0(register_12_q), .in1(register_14_q), .out(multiplexer_13_out), .sel(Push_Pop));  // open: en
  Register #(.width(10)) register_13 (
    .D(multiplexer_13_out), .Q(register_13_q), .clk(not_1_out), .clr(button_1_out));  // open: en
  Multiplexer #(.width(10)) multiplexer_14 (
    .in0(register_13_q), .in1(register_15_q), .out(multiplexer_14_out), .sel(Push_Pop));  // open: en
  Register #(.width(10)) register_14 (
    .D(multiplexer_14_out), .Q(register_14_q), .clk(not_1_out), .clr(button_1_out));  // open: en
  Multiplexer #(.width(10)) multiplexer_15 (
    .in0(register_14_q), .in1(register_16_q), .out(multiplexer_15_out), .sel(Push_Pop));  // open: en
  Register #(.width(10)) register_15 (
    .D(multiplexer_15_out), .Q(register_15_q), .clk(not_1_out), .clr(button_1_out));  // open: en
  Multiplexer #(.width(10)) multiplexer_16 (
    .in0(register_15_q), .in1({10{1'b0}}), .out(multiplexer_16_out), .sel(Push_Pop));  // open: en
  Register #(.width(10)) register_16 (
    .D(multiplexer_16_out), .Q(register_16_q), .clk(not_1_out), .clr(button_1_out));  // open: en
endmodule

module Flags (
  input  Zero,
  input  B___A,
  input  Set_flag,
  input  CLK,
  output Zero_2,
  output B_A
);

  wire not_1_out;

  not not_1 (not_1_out, CLK);
  Register #(.width(1)) register_1 (.D(Zero), .en(Set_flag), .Q(Zero_2), .clk(not_1_out));  // open: clr
  Register #(.width(1)) register_2 (.D(B___A), .en(Set_flag), .Q(B_A), .clk(not_1_out));  // open: clr
endmodule
module LED_display_module (
  input  [4:0] PixelX,
  input  [4:0] PixelX_2,
  input  CLK,
  input  [3:0] Settings,
  output [31:0] out_5,
  output [31:0] out_6,
  output [31:0] out_7,
  output [31:0] out_8,
  output [31:0] out_9,
  output [31:0] out_10,
  output [31:0] out_11,
  output [31:0] out_12,
  output [31:0] out_13,
  output [31:0] out_14,
  output [31:0] out_15,
  output [31:0] out_16,
  output [31:0] out_17,
  output [31:0] out_18,
  output [31:0] out_19,
  output [31:0] out_20,
  output [31:0] out_21,
  output [31:0] out_22,
  output [31:0] out_23,
  output [31:0] out_24,
  output [31:0] out_25,
  output [31:0] out_26,
  output [31:0] out_27,
  output [31:0] out_28,
  output [31:0] out_29,
  output [31:0] out_30,
  output [31:0] out_31,
  output [31:0] out_32,
  output [31:0] out_33,
  output [31:0] out_34,
  output [31:0] out_35,
  output [31:0] out_36,
  output Pixel_Info
);

  wire demultiplexer_1_out0, demultiplexer_1_out1, demultiplexer_1_out2, demultiplexer_1_out3,
       demultiplexer_1_out4, demultiplexer_1_out5, demultiplexer_1_out6, demultiplexer_1_out7,
       demultiplexer_1_out8, demultiplexer_1_out9, demultiplexer_1_out10, demultiplexer_1_out11,
       demultiplexer_1_out12, demultiplexer_1_out13, demultiplexer_1_out14, demultiplexer_1_out15,
       demultiplexer_1_out16, demultiplexer_1_out17, demultiplexer_1_out18, demultiplexer_1_out19,
       demultiplexer_1_out20, demultiplexer_1_out21, demultiplexer_1_out22, demultiplexer_1_out23,
       demultiplexer_1_out24, demultiplexer_1_out25, demultiplexer_1_out26, demultiplexer_1_out27,
       demultiplexer_1_out28, demultiplexer_1_out29, demultiplexer_1_out30, demultiplexer_1_out31,
       demultiplexer_2_out0, demultiplexer_2_out1, demultiplexer_2_out2, demultiplexer_2_out3,
       demultiplexer_2_out4, demultiplexer_2_out5, demultiplexer_2_out6, demultiplexer_2_out7,
       demultiplexer_2_out8, demultiplexer_2_out9, demultiplexer_2_out10, demultiplexer_2_out11,
       demultiplexer_2_out12, demultiplexer_2_out13, demultiplexer_2_out14, demultiplexer_2_out15,
       demultiplexer_2_out16, demultiplexer_2_out17, demultiplexer_2_out18, demultiplexer_2_out19,
       demultiplexer_2_out20, demultiplexer_2_out21, demultiplexer_2_out22, demultiplexer_2_out23,
       demultiplexer_2_out24, demultiplexer_2_out25, demultiplexer_2_out26, demultiplexer_2_out27,
       demultiplexer_2_out28, demultiplexer_2_out29, demultiplexer_2_out30, demultiplexer_2_out31,
       led_32x_array_1_out_39, led_32x_array_1_out_40, led_32x_array_1_out_41, led_32x_array_1_out_42,
       led_32x_array_1_out_43, led_32x_array_1_out_44, led_32x_array_1_out_45, led_32x_array_1_out_46,
       led_32x_array_1_out_47, led_32x_array_1_out_48, led_32x_array_1_out_49, led_32x_array_1_out_50,
       led_32x_array_1_out_51, led_32x_array_1_out_52, led_32x_array_1_out_53, led_32x_array_1_out_54,
       led_32x_array_1_out_55, led_32x_array_1_out_56, led_32x_array_1_out_57, led_32x_array_1_out_58,
       led_32x_array_1_out_59, led_32x_array_1_out_60, led_32x_array_1_out_61, led_32x_array_1_out_62,
       led_32x_array_1_out_63, led_32x_array_1_out_64, led_32x_array_1_out_65, led_32x_array_1_out_66,
       led_32x_array_1_out_67, led_32x_array_1_out_68, led_32x_array_1_out_69, led_32x_array_1_out_70,
       led_32x_array_1_pixel_info, led_32x_array_2_out_39, led_32x_array_2_out_40, led_32x_array_2_out_41,
       led_32x_array_2_out_42, led_32x_array_2_out_43, led_32x_array_2_out_44, led_32x_array_2_out_45,
       led_32x_array_2_out_46, led_32x_array_2_out_47, led_32x_array_2_out_48, led_32x_array_2_out_49,
       led_32x_array_2_out_50, led_32x_array_2_out_51, led_32x_array_2_out_52, led_32x_array_2_out_53,
       led_32x_array_2_out_54, led_32x_array_2_out_55, led_32x_array_2_out_56, led_32x_array_2_out_57,
       led_32x_array_2_out_58, led_32x_array_2_out_59, led_32x_array_2_out_60, led_32x_array_2_out_61,
       led_32x_array_2_out_62, led_32x_array_2_out_63, led_32x_array_2_out_64, led_32x_array_2_out_65,
       led_32x_array_2_out_66, led_32x_array_2_out_67, led_32x_array_2_out_68, led_32x_array_2_out_69,
       led_32x_array_2_out_70, led_32x_array_2_pixel_info, led_32x_array_3_out_39, led_32x_array_3_out_40,
       led_32x_array_3_out_41, led_32x_array_3_out_42, led_32x_array_3_out_43, led_32x_array_3_out_44,
       led_32x_array_3_out_45, led_32x_array_3_out_46, led_32x_array_3_out_47, led_32x_array_3_out_48,
       led_32x_array_3_out_49, led_32x_array_3_out_50, led_32x_array_3_out_51, led_32x_array_3_out_52,
       led_32x_array_3_out_53, led_32x_array_3_out_54, led_32x_array_3_out_55, led_32x_array_3_out_56,
       led_32x_array_3_out_57, led_32x_array_3_out_58, led_32x_array_3_out_59, led_32x_array_3_out_60,
       led_32x_array_3_out_61, led_32x_array_3_out_62, led_32x_array_3_out_63, led_32x_array_3_out_64,
       led_32x_array_3_out_65, led_32x_array_3_out_66, led_32x_array_3_out_67, led_32x_array_3_out_68,
       led_32x_array_3_out_69, led_32x_array_3_out_70, led_32x_array_3_pixel_info, led_32x_array_4_out_39,
       led_32x_array_4_out_40, led_32x_array_4_out_41, led_32x_array_4_out_42, led_32x_array_4_out_43,
       led_32x_array_4_out_44, led_32x_array_4_out_45, led_32x_array_4_out_46, led_32x_array_4_out_47,
       led_32x_array_4_out_48, led_32x_array_4_out_49, led_32x_array_4_out_50, led_32x_array_4_out_51,
       led_32x_array_4_out_52, led_32x_array_4_out_53, led_32x_array_4_out_54, led_32x_array_4_out_55,
       led_32x_array_4_out_56, led_32x_array_4_out_57, led_32x_array_4_out_58, led_32x_array_4_out_59,
       led_32x_array_4_out_60, led_32x_array_4_out_61, led_32x_array_4_out_62, led_32x_array_4_out_63,
       led_32x_array_4_out_64, led_32x_array_4_out_65, led_32x_array_4_out_66, led_32x_array_4_out_67,
       led_32x_array_4_out_68, led_32x_array_4_out_69, led_32x_array_4_out_70, led_32x_array_4_pixel_info,
       led_32x_array_5_out_39, led_32x_array_5_out_40, led_32x_array_5_out_41, led_32x_array_5_out_42,
       led_32x_array_5_out_43, led_32x_array_5_out_44, led_32x_array_5_out_45, led_32x_array_5_out_46,
       led_32x_array_5_out_47, led_32x_array_5_out_48, led_32x_array_5_out_49, led_32x_array_5_out_50,
       led_32x_array_5_out_51, led_32x_array_5_out_52, led_32x_array_5_out_53, led_32x_array_5_out_54,
       led_32x_array_5_out_55, led_32x_array_5_out_56, led_32x_array_5_out_57, led_32x_array_5_out_58,
       led_32x_array_5_out_59, led_32x_array_5_out_60, led_32x_array_5_out_61, led_32x_array_5_out_62,
       led_32x_array_5_out_63, led_32x_array_5_out_64, led_32x_array_5_out_65, led_32x_array_5_out_66,
       led_32x_array_5_out_67, led_32x_array_5_out_68, led_32x_array_5_out_69, led_32x_array_5_out_70,
       led_32x_array_5_pixel_info, led_32x_array_6_out_39, led_32x_array_6_out_40, led_32x_array_6_out_41,
       led_32x_array_6_out_42, led_32x_array_6_out_43, led_32x_array_6_out_44, led_32x_array_6_out_45,
       led_32x_array_6_out_46, led_32x_array_6_out_47, led_32x_array_6_out_48, led_32x_array_6_out_49,
       led_32x_array_6_out_50, led_32x_array_6_out_51, led_32x_array_6_out_52, led_32x_array_6_out_53,
       led_32x_array_6_out_54, led_32x_array_6_out_55, led_32x_array_6_out_56, led_32x_array_6_out_57,
       led_32x_array_6_out_58, led_32x_array_6_out_59, led_32x_array_6_out_60, led_32x_array_6_out_61,
       led_32x_array_6_out_62, led_32x_array_6_out_63, led_32x_array_6_out_64, led_32x_array_6_out_65,
       led_32x_array_6_out_66, led_32x_array_6_out_67, led_32x_array_6_out_68, led_32x_array_6_out_69,
       led_32x_array_6_out_70, led_32x_array_6_pixel_info, led_32x_array_7_out_39, led_32x_array_7_out_40,
       led_32x_array_7_out_41, led_32x_array_7_out_42, led_32x_array_7_out_43, led_32x_array_7_out_44,
       led_32x_array_7_out_45, led_32x_array_7_out_46, led_32x_array_7_out_47, led_32x_array_7_out_48,
       led_32x_array_7_out_49, led_32x_array_7_out_50, led_32x_array_7_out_51, led_32x_array_7_out_52,
       led_32x_array_7_out_53, led_32x_array_7_out_54, led_32x_array_7_out_55, led_32x_array_7_out_56,
       led_32x_array_7_out_57, led_32x_array_7_out_58, led_32x_array_7_out_59, led_32x_array_7_out_60,
       led_32x_array_7_out_61, led_32x_array_7_out_62, led_32x_array_7_out_63, led_32x_array_7_out_64,
       led_32x_array_7_out_65, led_32x_array_7_out_66, led_32x_array_7_out_67, led_32x_array_7_out_68,
       led_32x_array_7_out_69, led_32x_array_7_out_70, led_32x_array_7_pixel_info, led_32x_array_8_out_39,
       led_32x_array_8_out_40, led_32x_array_8_out_41, led_32x_array_8_out_42, led_32x_array_8_out_43,
       led_32x_array_8_out_44, led_32x_array_8_out_45, led_32x_array_8_out_46, led_32x_array_8_out_47,
       led_32x_array_8_out_48, led_32x_array_8_out_49, led_32x_array_8_out_50, led_32x_array_8_out_51,
       led_32x_array_8_out_52, led_32x_array_8_out_53, led_32x_array_8_out_54, led_32x_array_8_out_55,
       led_32x_array_8_out_56, led_32x_array_8_out_57, led_32x_array_8_out_58, led_32x_array_8_out_59,
       led_32x_array_8_out_60, led_32x_array_8_out_61, led_32x_array_8_out_62, led_32x_array_8_out_63,
       led_32x_array_8_out_64, led_32x_array_8_out_65, led_32x_array_8_out_66, led_32x_array_8_out_67,
       led_32x_array_8_out_68, led_32x_array_8_out_69, led_32x_array_8_out_70, led_32x_array_8_pixel_info,
       led_32x_array_9_out_39, led_32x_array_9_out_40, led_32x_array_9_out_41, led_32x_array_9_out_42,
       led_32x_array_9_out_43, led_32x_array_9_out_44, led_32x_array_9_out_45, led_32x_array_9_out_46,
       led_32x_array_9_out_47, led_32x_array_9_out_48, led_32x_array_9_out_49, led_32x_array_9_out_50,
       led_32x_array_9_out_51, led_32x_array_9_out_52, led_32x_array_9_out_53, led_32x_array_9_out_54,
       led_32x_array_9_out_55, led_32x_array_9_out_56, led_32x_array_9_out_57, led_32x_array_9_out_58,
       led_32x_array_9_out_59, led_32x_array_9_out_60, led_32x_array_9_out_61, led_32x_array_9_out_62,
       led_32x_array_9_out_63, led_32x_array_9_out_64, led_32x_array_9_out_65, led_32x_array_9_out_66,
       led_32x_array_9_out_67, led_32x_array_9_out_68, led_32x_array_9_out_69, led_32x_array_9_out_70,
       led_32x_array_9_pixel_info, led_32x_array_10_out_39, led_32x_array_10_out_40, led_32x_array_10_out_41,
       led_32x_array_10_out_42, led_32x_array_10_out_43, led_32x_array_10_out_44, led_32x_array_10_out_45,
       led_32x_array_10_out_46, led_32x_array_10_out_47, led_32x_array_10_out_48, led_32x_array_10_out_49,
       led_32x_array_10_out_50, led_32x_array_10_out_51, led_32x_array_10_out_52, led_32x_array_10_out_53,
       led_32x_array_10_out_54, led_32x_array_10_out_55, led_32x_array_10_out_56, led_32x_array_10_out_57,
       led_32x_array_10_out_58, led_32x_array_10_out_59, led_32x_array_10_out_60, led_32x_array_10_out_61,
       led_32x_array_10_out_62, led_32x_array_10_out_63, led_32x_array_10_out_64, led_32x_array_10_out_65,
       led_32x_array_10_out_66, led_32x_array_10_out_67, led_32x_array_10_out_68, led_32x_array_10_out_69,
       led_32x_array_10_out_70, led_32x_array_10_pixel_info, led_32x_array_11_out_39,
       led_32x_array_11_out_40, led_32x_array_11_out_41, led_32x_array_11_out_42, led_32x_array_11_out_43,
       led_32x_array_11_out_44, led_32x_array_11_out_45, led_32x_array_11_out_46, led_32x_array_11_out_47,
       led_32x_array_11_out_48, led_32x_array_11_out_49, led_32x_array_11_out_50, led_32x_array_11_out_51,
       led_32x_array_11_out_52, led_32x_array_11_out_53, led_32x_array_11_out_54, led_32x_array_11_out_55,
       led_32x_array_11_out_56, led_32x_array_11_out_57, led_32x_array_11_out_58, led_32x_array_11_out_59,
       led_32x_array_11_out_60, led_32x_array_11_out_61, led_32x_array_11_out_62, led_32x_array_11_out_63,
       led_32x_array_11_out_64, led_32x_array_11_out_65, led_32x_array_11_out_66, led_32x_array_11_out_67,
       led_32x_array_11_out_68, led_32x_array_11_out_69, led_32x_array_11_out_70,
       led_32x_array_11_pixel_info, led_32x_array_12_out_39, led_32x_array_12_out_40,
       led_32x_array_12_out_41, led_32x_array_12_out_42, led_32x_array_12_out_43, led_32x_array_12_out_44,
       led_32x_array_12_out_45, led_32x_array_12_out_46, led_32x_array_12_out_47, led_32x_array_12_out_48,
       led_32x_array_12_out_49, led_32x_array_12_out_50, led_32x_array_12_out_51, led_32x_array_12_out_52,
       led_32x_array_12_out_53, led_32x_array_12_out_54, led_32x_array_12_out_55, led_32x_array_12_out_56,
       led_32x_array_12_out_57, led_32x_array_12_out_58, led_32x_array_12_out_59, led_32x_array_12_out_60,
       led_32x_array_12_out_61, led_32x_array_12_out_62, led_32x_array_12_out_63, led_32x_array_12_out_64,
       led_32x_array_12_out_65, led_32x_array_12_out_66, led_32x_array_12_out_67, led_32x_array_12_out_68,
       led_32x_array_12_out_69, led_32x_array_12_out_70, led_32x_array_12_pixel_info,
       led_32x_array_13_out_39, led_32x_array_13_out_40, led_32x_array_13_out_41, led_32x_array_13_out_42,
       led_32x_array_13_out_43, led_32x_array_13_out_44, led_32x_array_13_out_45, led_32x_array_13_out_46,
       led_32x_array_13_out_47, led_32x_array_13_out_48, led_32x_array_13_out_49, led_32x_array_13_out_50,
       led_32x_array_13_out_51, led_32x_array_13_out_52, led_32x_array_13_out_53, led_32x_array_13_out_54,
       led_32x_array_13_out_55, led_32x_array_13_out_56, led_32x_array_13_out_57, led_32x_array_13_out_58,
       led_32x_array_13_out_59, led_32x_array_13_out_60, led_32x_array_13_out_61, led_32x_array_13_out_62,
       led_32x_array_13_out_63, led_32x_array_13_out_64, led_32x_array_13_out_65, led_32x_array_13_out_66,
       led_32x_array_13_out_67, led_32x_array_13_out_68, led_32x_array_13_out_69, led_32x_array_13_out_70,
       led_32x_array_13_pixel_info, led_32x_array_14_out_39, led_32x_array_14_out_40,
       led_32x_array_14_out_41, led_32x_array_14_out_42, led_32x_array_14_out_43, led_32x_array_14_out_44,
       led_32x_array_14_out_45, led_32x_array_14_out_46, led_32x_array_14_out_47, led_32x_array_14_out_48,
       led_32x_array_14_out_49, led_32x_array_14_out_50, led_32x_array_14_out_51, led_32x_array_14_out_52,
       led_32x_array_14_out_53, led_32x_array_14_out_54, led_32x_array_14_out_55, led_32x_array_14_out_56,
       led_32x_array_14_out_57, led_32x_array_14_out_58, led_32x_array_14_out_59, led_32x_array_14_out_60,
       led_32x_array_14_out_61, led_32x_array_14_out_62, led_32x_array_14_out_63, led_32x_array_14_out_64,
       led_32x_array_14_out_65, led_32x_array_14_out_66, led_32x_array_14_out_67, led_32x_array_14_out_68,
       led_32x_array_14_out_69, led_32x_array_14_out_70, led_32x_array_14_pixel_info,
       led_32x_array_15_out_39, led_32x_array_15_out_40, led_32x_array_15_out_41, led_32x_array_15_out_42,
       led_32x_array_15_out_43, led_32x_array_15_out_44, led_32x_array_15_out_45, led_32x_array_15_out_46,
       led_32x_array_15_out_47, led_32x_array_15_out_48, led_32x_array_15_out_49, led_32x_array_15_out_50,
       led_32x_array_15_out_51, led_32x_array_15_out_52, led_32x_array_15_out_53, led_32x_array_15_out_54,
       led_32x_array_15_out_55, led_32x_array_15_out_56, led_32x_array_15_out_57, led_32x_array_15_out_58,
       led_32x_array_15_out_59, led_32x_array_15_out_60, led_32x_array_15_out_61, led_32x_array_15_out_62,
       led_32x_array_15_out_63, led_32x_array_15_out_64, led_32x_array_15_out_65, led_32x_array_15_out_66,
       led_32x_array_15_out_67, led_32x_array_15_out_68, led_32x_array_15_out_69, led_32x_array_15_out_70,
       led_32x_array_15_pixel_info, led_32x_array_16_out_39, led_32x_array_16_out_40,
       led_32x_array_16_out_41, led_32x_array_16_out_42, led_32x_array_16_out_43, led_32x_array_16_out_44,
       led_32x_array_16_out_45, led_32x_array_16_out_46, led_32x_array_16_out_47, led_32x_array_16_out_48,
       led_32x_array_16_out_49, led_32x_array_16_out_50, led_32x_array_16_out_51, led_32x_array_16_out_52,
       led_32x_array_16_out_53, led_32x_array_16_out_54, led_32x_array_16_out_55, led_32x_array_16_out_56,
       led_32x_array_16_out_57, led_32x_array_16_out_58, led_32x_array_16_out_59, led_32x_array_16_out_60,
       led_32x_array_16_out_61, led_32x_array_16_out_62, led_32x_array_16_out_63, led_32x_array_16_out_64,
       led_32x_array_16_out_65, led_32x_array_16_out_66, led_32x_array_16_out_67, led_32x_array_16_out_68,
       led_32x_array_16_out_69, led_32x_array_16_out_70, led_32x_array_16_pixel_info,
       led_32x_array_17_out_39, led_32x_array_17_out_40, led_32x_array_17_out_41, led_32x_array_17_out_42,
       led_32x_array_17_out_43, led_32x_array_17_out_44, led_32x_array_17_out_45, led_32x_array_17_out_46,
       led_32x_array_17_out_47, led_32x_array_17_out_48, led_32x_array_17_out_49, led_32x_array_17_out_50,
       led_32x_array_17_out_51, led_32x_array_17_out_52, led_32x_array_17_out_53, led_32x_array_17_out_54,
       led_32x_array_17_out_55, led_32x_array_17_out_56, led_32x_array_17_out_57, led_32x_array_17_out_58,
       led_32x_array_17_out_59, led_32x_array_17_out_60, led_32x_array_17_out_61, led_32x_array_17_out_62,
       led_32x_array_17_out_63, led_32x_array_17_out_64, led_32x_array_17_out_65, led_32x_array_17_out_66,
       led_32x_array_17_out_67, led_32x_array_17_out_68, led_32x_array_17_out_69, led_32x_array_17_out_70,
       led_32x_array_17_pixel_info, led_32x_array_18_out_39, led_32x_array_18_out_40,
       led_32x_array_18_out_41, led_32x_array_18_out_42, led_32x_array_18_out_43, led_32x_array_18_out_44,
       led_32x_array_18_out_45, led_32x_array_18_out_46, led_32x_array_18_out_47, led_32x_array_18_out_48,
       led_32x_array_18_out_49, led_32x_array_18_out_50, led_32x_array_18_out_51, led_32x_array_18_out_52,
       led_32x_array_18_out_53, led_32x_array_18_out_54, led_32x_array_18_out_55, led_32x_array_18_out_56,
       led_32x_array_18_out_57, led_32x_array_18_out_58, led_32x_array_18_out_59, led_32x_array_18_out_60,
       led_32x_array_18_out_61, led_32x_array_18_out_62, led_32x_array_18_out_63, led_32x_array_18_out_64,
       led_32x_array_18_out_65, led_32x_array_18_out_66, led_32x_array_18_out_67, led_32x_array_18_out_68,
       led_32x_array_18_out_69, led_32x_array_18_out_70, led_32x_array_18_pixel_info,
       led_32x_array_19_out_39, led_32x_array_19_out_40, led_32x_array_19_out_41, led_32x_array_19_out_42,
       led_32x_array_19_out_43, led_32x_array_19_out_44, led_32x_array_19_out_45, led_32x_array_19_out_46,
       led_32x_array_19_out_47, led_32x_array_19_out_48, led_32x_array_19_out_49, led_32x_array_19_out_50,
       led_32x_array_19_out_51, led_32x_array_19_out_52, led_32x_array_19_out_53, led_32x_array_19_out_54,
       led_32x_array_19_out_55, led_32x_array_19_out_56, led_32x_array_19_out_57, led_32x_array_19_out_58,
       led_32x_array_19_out_59, led_32x_array_19_out_60, led_32x_array_19_out_61, led_32x_array_19_out_62,
       led_32x_array_19_out_63, led_32x_array_19_out_64, led_32x_array_19_out_65, led_32x_array_19_out_66,
       led_32x_array_19_out_67, led_32x_array_19_out_68, led_32x_array_19_out_69, led_32x_array_19_out_70,
       led_32x_array_19_pixel_info, led_32x_array_20_out_39, led_32x_array_20_out_40,
       led_32x_array_20_out_41, led_32x_array_20_out_42, led_32x_array_20_out_43, led_32x_array_20_out_44,
       led_32x_array_20_out_45, led_32x_array_20_out_46, led_32x_array_20_out_47, led_32x_array_20_out_48,
       led_32x_array_20_out_49, led_32x_array_20_out_50, led_32x_array_20_out_51, led_32x_array_20_out_52,
       led_32x_array_20_out_53, led_32x_array_20_out_54, led_32x_array_20_out_55, led_32x_array_20_out_56,
       led_32x_array_20_out_57, led_32x_array_20_out_58, led_32x_array_20_out_59, led_32x_array_20_out_60,
       led_32x_array_20_out_61, led_32x_array_20_out_62, led_32x_array_20_out_63, led_32x_array_20_out_64,
       led_32x_array_20_out_65, led_32x_array_20_out_66, led_32x_array_20_out_67, led_32x_array_20_out_68,
       led_32x_array_20_out_69, led_32x_array_20_out_70, led_32x_array_20_pixel_info,
       led_32x_array_21_out_39, led_32x_array_21_out_40, led_32x_array_21_out_41, led_32x_array_21_out_42,
       led_32x_array_21_out_43, led_32x_array_21_out_44, led_32x_array_21_out_45, led_32x_array_21_out_46,
       led_32x_array_21_out_47, led_32x_array_21_out_48, led_32x_array_21_out_49, led_32x_array_21_out_50,
       led_32x_array_21_out_51, led_32x_array_21_out_52, led_32x_array_21_out_53, led_32x_array_21_out_54,
       led_32x_array_21_out_55, led_32x_array_21_out_56, led_32x_array_21_out_57, led_32x_array_21_out_58,
       led_32x_array_21_out_59, led_32x_array_21_out_60, led_32x_array_21_out_61, led_32x_array_21_out_62,
       led_32x_array_21_out_63, led_32x_array_21_out_64, led_32x_array_21_out_65, led_32x_array_21_out_66,
       led_32x_array_21_out_67, led_32x_array_21_out_68, led_32x_array_21_out_69, led_32x_array_21_out_70,
       led_32x_array_21_pixel_info, led_32x_array_22_out_39, led_32x_array_22_out_40,
       led_32x_array_22_out_41, led_32x_array_22_out_42, led_32x_array_22_out_43, led_32x_array_22_out_44,
       led_32x_array_22_out_45, led_32x_array_22_out_46, led_32x_array_22_out_47, led_32x_array_22_out_48,
       led_32x_array_22_out_49, led_32x_array_22_out_50, led_32x_array_22_out_51, led_32x_array_22_out_52,
       led_32x_array_22_out_53, led_32x_array_22_out_54, led_32x_array_22_out_55, led_32x_array_22_out_56,
       led_32x_array_22_out_57, led_32x_array_22_out_58, led_32x_array_22_out_59, led_32x_array_22_out_60,
       led_32x_array_22_out_61, led_32x_array_22_out_62, led_32x_array_22_out_63, led_32x_array_22_out_64,
       led_32x_array_22_out_65, led_32x_array_22_out_66, led_32x_array_22_out_67, led_32x_array_22_out_68,
       led_32x_array_22_out_69, led_32x_array_22_out_70, led_32x_array_22_pixel_info,
       led_32x_array_23_out_39, led_32x_array_23_out_40, led_32x_array_23_out_41, led_32x_array_23_out_42,
       led_32x_array_23_out_43, led_32x_array_23_out_44, led_32x_array_23_out_45, led_32x_array_23_out_46,
       led_32x_array_23_out_47, led_32x_array_23_out_48, led_32x_array_23_out_49, led_32x_array_23_out_50,
       led_32x_array_23_out_51, led_32x_array_23_out_52, led_32x_array_23_out_53, led_32x_array_23_out_54,
       led_32x_array_23_out_55, led_32x_array_23_out_56, led_32x_array_23_out_57, led_32x_array_23_out_58,
       led_32x_array_23_out_59, led_32x_array_23_out_60, led_32x_array_23_out_61, led_32x_array_23_out_62,
       led_32x_array_23_out_63, led_32x_array_23_out_64, led_32x_array_23_out_65, led_32x_array_23_out_66,
       led_32x_array_23_out_67, led_32x_array_23_out_68, led_32x_array_23_out_69, led_32x_array_23_out_70,
       led_32x_array_23_pixel_info, led_32x_array_24_out_39, led_32x_array_24_out_40,
       led_32x_array_24_out_41, led_32x_array_24_out_42, led_32x_array_24_out_43, led_32x_array_24_out_44,
       led_32x_array_24_out_45, led_32x_array_24_out_46, led_32x_array_24_out_47, led_32x_array_24_out_48,
       led_32x_array_24_out_49, led_32x_array_24_out_50, led_32x_array_24_out_51, led_32x_array_24_out_52,
       led_32x_array_24_out_53, led_32x_array_24_out_54, led_32x_array_24_out_55, led_32x_array_24_out_56,
       led_32x_array_24_out_57, led_32x_array_24_out_58, led_32x_array_24_out_59, led_32x_array_24_out_60,
       led_32x_array_24_out_61, led_32x_array_24_out_62, led_32x_array_24_out_63, led_32x_array_24_out_64,
       led_32x_array_24_out_65, led_32x_array_24_out_66, led_32x_array_24_out_67, led_32x_array_24_out_68,
       led_32x_array_24_out_69, led_32x_array_24_out_70, led_32x_array_24_pixel_info,
       led_32x_array_25_out_39, led_32x_array_25_out_40, led_32x_array_25_out_41, led_32x_array_25_out_42,
       led_32x_array_25_out_43, led_32x_array_25_out_44, led_32x_array_25_out_45, led_32x_array_25_out_46,
       led_32x_array_25_out_47, led_32x_array_25_out_48, led_32x_array_25_out_49, led_32x_array_25_out_50,
       led_32x_array_25_out_51, led_32x_array_25_out_52, led_32x_array_25_out_53, led_32x_array_25_out_54,
       led_32x_array_25_out_55, led_32x_array_25_out_56, led_32x_array_25_out_57, led_32x_array_25_out_58,
       led_32x_array_25_out_59, led_32x_array_25_out_60, led_32x_array_25_out_61, led_32x_array_25_out_62,
       led_32x_array_25_out_63, led_32x_array_25_out_64, led_32x_array_25_out_65, led_32x_array_25_out_66,
       led_32x_array_25_out_67, led_32x_array_25_out_68, led_32x_array_25_out_69, led_32x_array_25_out_70,
       led_32x_array_25_pixel_info, led_32x_array_26_out_39, led_32x_array_26_out_40,
       led_32x_array_26_out_41, led_32x_array_26_out_42, led_32x_array_26_out_43, led_32x_array_26_out_44,
       led_32x_array_26_out_45, led_32x_array_26_out_46, led_32x_array_26_out_47, led_32x_array_26_out_48,
       led_32x_array_26_out_49, led_32x_array_26_out_50, led_32x_array_26_out_51, led_32x_array_26_out_52,
       led_32x_array_26_out_53, led_32x_array_26_out_54, led_32x_array_26_out_55, led_32x_array_26_out_56,
       led_32x_array_26_out_57, led_32x_array_26_out_58, led_32x_array_26_out_59, led_32x_array_26_out_60,
       led_32x_array_26_out_61, led_32x_array_26_out_62, led_32x_array_26_out_63, led_32x_array_26_out_64,
       led_32x_array_26_out_65, led_32x_array_26_out_66, led_32x_array_26_out_67, led_32x_array_26_out_68,
       led_32x_array_26_out_69, led_32x_array_26_out_70, led_32x_array_26_pixel_info,
       led_32x_array_27_out_39, led_32x_array_27_out_40, led_32x_array_27_out_41, led_32x_array_27_out_42,
       led_32x_array_27_out_43, led_32x_array_27_out_44, led_32x_array_27_out_45, led_32x_array_27_out_46,
       led_32x_array_27_out_47, led_32x_array_27_out_48, led_32x_array_27_out_49, led_32x_array_27_out_50,
       led_32x_array_27_out_51, led_32x_array_27_out_52, led_32x_array_27_out_53, led_32x_array_27_out_54,
       led_32x_array_27_out_55, led_32x_array_27_out_56, led_32x_array_27_out_57, led_32x_array_27_out_58,
       led_32x_array_27_out_59, led_32x_array_27_out_60, led_32x_array_27_out_61, led_32x_array_27_out_62,
       led_32x_array_27_out_63, led_32x_array_27_out_64, led_32x_array_27_out_65, led_32x_array_27_out_66,
       led_32x_array_27_out_67, led_32x_array_27_out_68, led_32x_array_27_out_69, led_32x_array_27_out_70,
       led_32x_array_27_pixel_info, led_32x_array_28_out_39, led_32x_array_28_out_40,
       led_32x_array_28_out_41, led_32x_array_28_out_42, led_32x_array_28_out_43, led_32x_array_28_out_44,
       led_32x_array_28_out_45, led_32x_array_28_out_46, led_32x_array_28_out_47, led_32x_array_28_out_48,
       led_32x_array_28_out_49, led_32x_array_28_out_50, led_32x_array_28_out_51, led_32x_array_28_out_52,
       led_32x_array_28_out_53, led_32x_array_28_out_54, led_32x_array_28_out_55, led_32x_array_28_out_56,
       led_32x_array_28_out_57, led_32x_array_28_out_58, led_32x_array_28_out_59, led_32x_array_28_out_60,
       led_32x_array_28_out_61, led_32x_array_28_out_62, led_32x_array_28_out_63, led_32x_array_28_out_64,
       led_32x_array_28_out_65, led_32x_array_28_out_66, led_32x_array_28_out_67, led_32x_array_28_out_68,
       led_32x_array_28_out_69, led_32x_array_28_out_70, led_32x_array_28_pixel_info,
       led_32x_array_29_out_39, led_32x_array_29_out_40, led_32x_array_29_out_41, led_32x_array_29_out_42,
       led_32x_array_29_out_43, led_32x_array_29_out_44, led_32x_array_29_out_45, led_32x_array_29_out_46,
       led_32x_array_29_out_47, led_32x_array_29_out_48, led_32x_array_29_out_49, led_32x_array_29_out_50,
       led_32x_array_29_out_51, led_32x_array_29_out_52, led_32x_array_29_out_53, led_32x_array_29_out_54,
       led_32x_array_29_out_55, led_32x_array_29_out_56, led_32x_array_29_out_57, led_32x_array_29_out_58,
       led_32x_array_29_out_59, led_32x_array_29_out_60, led_32x_array_29_out_61, led_32x_array_29_out_62,
       led_32x_array_29_out_63, led_32x_array_29_out_64, led_32x_array_29_out_65, led_32x_array_29_out_66,
       led_32x_array_29_out_67, led_32x_array_29_out_68, led_32x_array_29_out_69, led_32x_array_29_out_70,
       led_32x_array_29_pixel_info, led_32x_array_30_out_39, led_32x_array_30_out_40,
       led_32x_array_30_out_41, led_32x_array_30_out_42, led_32x_array_30_out_43, led_32x_array_30_out_44,
       led_32x_array_30_out_45, led_32x_array_30_out_46, led_32x_array_30_out_47, led_32x_array_30_out_48,
       led_32x_array_30_out_49, led_32x_array_30_out_50, led_32x_array_30_out_51, led_32x_array_30_out_52,
       led_32x_array_30_out_53, led_32x_array_30_out_54, led_32x_array_30_out_55, led_32x_array_30_out_56,
       led_32x_array_30_out_57, led_32x_array_30_out_58, led_32x_array_30_out_59, led_32x_array_30_out_60,
       led_32x_array_30_out_61, led_32x_array_30_out_62, led_32x_array_30_out_63, led_32x_array_30_out_64,
       led_32x_array_30_out_65, led_32x_array_30_out_66, led_32x_array_30_out_67, led_32x_array_30_out_68,
       led_32x_array_30_out_69, led_32x_array_30_out_70, led_32x_array_30_pixel_info,
       led_32x_array_31_out_39, led_32x_array_31_out_40, led_32x_array_31_out_41, led_32x_array_31_out_42,
       led_32x_array_31_out_43, led_32x_array_31_out_44, led_32x_array_31_out_45, led_32x_array_31_out_46,
       led_32x_array_31_out_47, led_32x_array_31_out_48, led_32x_array_31_out_49, led_32x_array_31_out_50,
       led_32x_array_31_out_51, led_32x_array_31_out_52, led_32x_array_31_out_53, led_32x_array_31_out_54,
       led_32x_array_31_out_55, led_32x_array_31_out_56, led_32x_array_31_out_57, led_32x_array_31_out_58,
       led_32x_array_31_out_59, led_32x_array_31_out_60, led_32x_array_31_out_61, led_32x_array_31_out_62,
       led_32x_array_31_out_63, led_32x_array_31_out_64, led_32x_array_31_out_65, led_32x_array_31_out_66,
       led_32x_array_31_out_67, led_32x_array_31_out_68, led_32x_array_31_out_69, led_32x_array_31_out_70,
       led_32x_array_31_pixel_info, led_32x_array_32_out_39, led_32x_array_32_out_40,
       led_32x_array_32_out_41, led_32x_array_32_out_42, led_32x_array_32_out_43, led_32x_array_32_out_44,
       led_32x_array_32_out_45, led_32x_array_32_out_46, led_32x_array_32_out_47, led_32x_array_32_out_48,
       led_32x_array_32_out_49, led_32x_array_32_out_50, led_32x_array_32_out_51, led_32x_array_32_out_52,
       led_32x_array_32_out_53, led_32x_array_32_out_54, led_32x_array_32_out_55, led_32x_array_32_out_56,
       led_32x_array_32_out_57, led_32x_array_32_out_58, led_32x_array_32_out_59, led_32x_array_32_out_60,
       led_32x_array_32_out_61, led_32x_array_32_out_62, led_32x_array_32_out_63, led_32x_array_32_out_64,
       led_32x_array_32_out_65, led_32x_array_32_out_66, led_32x_array_32_out_67, led_32x_array_32_out_68,
       led_32x_array_32_out_69, led_32x_array_32_out_70, led_32x_array_32_pixel_info, not_1_out,
       pull_resistor_1_node;

  not not_1 (not_1_out, CLK);
  Demultiplexer #(.select(5)) demultiplexer_1 (
    .out0(demultiplexer_1_out0), .out1(demultiplexer_1_out1), .out2(demultiplexer_1_out2),
    .out3(demultiplexer_1_out3), .out4(demultiplexer_1_out4), .out5(demultiplexer_1_out5),
    .out6(demultiplexer_1_out6), .out7(demultiplexer_1_out7), .out8(demultiplexer_1_out8),
    .out9(demultiplexer_1_out9), .out10(demultiplexer_1_out10), .out11(demultiplexer_1_out11),
    .out12(demultiplexer_1_out12), .out13(demultiplexer_1_out13), .out14(demultiplexer_1_out14),
    .out15(demultiplexer_1_out15), .out16(demultiplexer_1_out16), .out17(demultiplexer_1_out17),
    .out18(demultiplexer_1_out18), .out19(demultiplexer_1_out19), .out20(demultiplexer_1_out20),
    .out21(demultiplexer_1_out21), .out22(demultiplexer_1_out22), .out23(demultiplexer_1_out23),
    .out24(demultiplexer_1_out24), .out25(demultiplexer_1_out25), .out26(demultiplexer_1_out26),
    .out27(demultiplexer_1_out27), .out28(demultiplexer_1_out28), .out29(demultiplexer_1_out29),
    .out30(demultiplexer_1_out30), .out31(demultiplexer_1_out31), .in(not_1_out), .sel(PixelX));  // open: en
  Demultiplexer #(.select(5)) demultiplexer_2 (
    .out0(demultiplexer_2_out0), .out1(demultiplexer_2_out1), .out2(demultiplexer_2_out2),
    .out3(demultiplexer_2_out3), .out4(demultiplexer_2_out4), .out5(demultiplexer_2_out5),
    .out6(demultiplexer_2_out6), .out7(demultiplexer_2_out7), .out8(demultiplexer_2_out8),
    .out9(demultiplexer_2_out9), .out10(demultiplexer_2_out10), .out11(demultiplexer_2_out11),
    .out12(demultiplexer_2_out12), .out13(demultiplexer_2_out13), .out14(demultiplexer_2_out14),
    .out15(demultiplexer_2_out15), .out16(demultiplexer_2_out16), .out17(demultiplexer_2_out17),
    .out18(demultiplexer_2_out18), .out19(demultiplexer_2_out19), .out20(demultiplexer_2_out20),
    .out21(demultiplexer_2_out21), .out22(demultiplexer_2_out22), .out23(demultiplexer_2_out23),
    .out24(demultiplexer_2_out24), .out25(demultiplexer_2_out25), .out26(demultiplexer_2_out26),
    .out27(demultiplexer_2_out27), .out28(demultiplexer_2_out28), .out29(demultiplexer_2_out29),
    .out30(demultiplexer_2_out30), .out31(demultiplexer_2_out31), .in(not_1_out), .sel(PixelX_2));  // open: en
  LED_32x_array led_32x_array_1 (
    .in_1(demultiplexer_1_out0), .in_2(demultiplexer_1_out1), .in_3(demultiplexer_1_out2),
    .in_4(demultiplexer_1_out3), .in_5(demultiplexer_1_out4), .in_6(demultiplexer_1_out5),
    .in_7(demultiplexer_1_out6), .in_8(demultiplexer_1_out7), .in_9(demultiplexer_1_out8),
    .in_10(demultiplexer_1_out9), .in_11(demultiplexer_1_out10), .in_12(demultiplexer_1_out11),
    .in_13(demultiplexer_1_out12), .in_14(demultiplexer_1_out13), .in_15(demultiplexer_1_out14),
    .in_16(demultiplexer_1_out15), .in_17(demultiplexer_1_out16), .in_18(demultiplexer_1_out17),
    .in_19(demultiplexer_1_out18), .in_20(demultiplexer_1_out19), .in_21(demultiplexer_1_out20),
    .in_22(demultiplexer_1_out21), .in_23(demultiplexer_1_out22), .in_24(demultiplexer_1_out23),
    .in_25(demultiplexer_1_out24), .in_26(demultiplexer_1_out25), .in_27(demultiplexer_1_out26),
    .in_28(demultiplexer_1_out27), .in_29(demultiplexer_1_out28), .in_30(demultiplexer_1_out29),
    .in_31(demultiplexer_1_out30), .in_32(demultiplexer_1_out31), .draw(Settings[0]), .erase(Settings[1]),
    .push(Settings[2]), .OUT(out_5), .out_39(led_32x_array_1_out_39), .out_40(led_32x_array_1_out_40),
    .out_41(led_32x_array_1_out_41), .out_42(led_32x_array_1_out_42), .out_43(led_32x_array_1_out_43),
    .out_44(led_32x_array_1_out_44), .out_45(led_32x_array_1_out_45), .out_46(led_32x_array_1_out_46),
    .out_47(led_32x_array_1_out_47), .out_48(led_32x_array_1_out_48), .out_49(led_32x_array_1_out_49),
    .out_50(led_32x_array_1_out_50), .out_51(led_32x_array_1_out_51), .out_52(led_32x_array_1_out_52),
    .out_53(led_32x_array_1_out_53), .out_54(led_32x_array_1_out_54), .out_55(led_32x_array_1_out_55),
    .out_56(led_32x_array_1_out_56), .out_57(led_32x_array_1_out_57), .out_58(led_32x_array_1_out_58),
    .out_59(led_32x_array_1_out_59), .out_60(led_32x_array_1_out_60), .out_61(led_32x_array_1_out_61),
    .out_62(led_32x_array_1_out_62), .out_63(led_32x_array_1_out_63), .out_64(led_32x_array_1_out_64),
    .out_65(led_32x_array_1_out_65), .out_66(led_32x_array_1_out_66), .out_67(led_32x_array_1_out_67),
    .out_68(led_32x_array_1_out_68), .out_69(led_32x_array_1_out_69), .out_70(led_32x_array_1_out_70),
    .Select(demultiplexer_2_out0), .Pixel_info(led_32x_array_1_pixel_info), .clear(Settings[3]));
  Pull_Resistor pull_resistor_1 (.node(pull_resistor_1_node));
  buf buffer_1 (pull_resistor_1_node, led_32x_array_1_pixel_info);
  Register #(.width(1)) register_1 (.D(pull_resistor_1_node), .Q(Pixel_Info), .clk(CLK));  // open: en, clr
  LED_32x_array led_32x_array_2 (
    .in_1(led_32x_array_1_out_39), .in_2(led_32x_array_1_out_40), .in_3(led_32x_array_1_out_41),
    .in_4(led_32x_array_1_out_42), .in_5(led_32x_array_1_out_43), .in_6(led_32x_array_1_out_44),
    .in_7(led_32x_array_1_out_45), .in_8(led_32x_array_1_out_46), .in_9(led_32x_array_1_out_47),
    .in_10(led_32x_array_1_out_48), .in_11(led_32x_array_1_out_49), .in_12(led_32x_array_1_out_50),
    .in_13(led_32x_array_1_out_51), .in_14(led_32x_array_1_out_52), .in_15(led_32x_array_1_out_53),
    .in_16(led_32x_array_1_out_54), .in_17(led_32x_array_1_out_55), .in_18(led_32x_array_1_out_56),
    .in_19(led_32x_array_1_out_57), .in_20(led_32x_array_1_out_58), .in_21(led_32x_array_1_out_59),
    .in_22(led_32x_array_1_out_60), .in_23(led_32x_array_1_out_61), .in_24(led_32x_array_1_out_62),
    .in_25(led_32x_array_1_out_63), .in_26(led_32x_array_1_out_64), .in_27(led_32x_array_1_out_65),
    .in_28(led_32x_array_1_out_66), .in_29(led_32x_array_1_out_67), .in_30(led_32x_array_1_out_68),
    .in_31(led_32x_array_1_out_69), .in_32(led_32x_array_1_out_70), .draw(Settings[0]), .erase(Settings[1]),
    .push(Settings[2]), .OUT(out_6), .out_39(led_32x_array_2_out_39), .out_40(led_32x_array_2_out_40),
    .out_41(led_32x_array_2_out_41), .out_42(led_32x_array_2_out_42), .out_43(led_32x_array_2_out_43),
    .out_44(led_32x_array_2_out_44), .out_45(led_32x_array_2_out_45), .out_46(led_32x_array_2_out_46),
    .out_47(led_32x_array_2_out_47), .out_48(led_32x_array_2_out_48), .out_49(led_32x_array_2_out_49),
    .out_50(led_32x_array_2_out_50), .out_51(led_32x_array_2_out_51), .out_52(led_32x_array_2_out_52),
    .out_53(led_32x_array_2_out_53), .out_54(led_32x_array_2_out_54), .out_55(led_32x_array_2_out_55),
    .out_56(led_32x_array_2_out_56), .out_57(led_32x_array_2_out_57), .out_58(led_32x_array_2_out_58),
    .out_59(led_32x_array_2_out_59), .out_60(led_32x_array_2_out_60), .out_61(led_32x_array_2_out_61),
    .out_62(led_32x_array_2_out_62), .out_63(led_32x_array_2_out_63), .out_64(led_32x_array_2_out_64),
    .out_65(led_32x_array_2_out_65), .out_66(led_32x_array_2_out_66), .out_67(led_32x_array_2_out_67),
    .out_68(led_32x_array_2_out_68), .out_69(led_32x_array_2_out_69), .out_70(led_32x_array_2_out_70),
    .Select(demultiplexer_2_out1), .Pixel_info(led_32x_array_2_pixel_info), .clear(Settings[3]));
  buf buffer_2 (pull_resistor_1_node, led_32x_array_2_pixel_info);
  LED_32x_array led_32x_array_3 (
    .in_1(led_32x_array_2_out_39), .in_2(led_32x_array_2_out_40), .in_3(led_32x_array_2_out_41),
    .in_4(led_32x_array_2_out_42), .in_5(led_32x_array_2_out_43), .in_6(led_32x_array_2_out_44),
    .in_7(led_32x_array_2_out_45), .in_8(led_32x_array_2_out_46), .in_9(led_32x_array_2_out_47),
    .in_10(led_32x_array_2_out_48), .in_11(led_32x_array_2_out_49), .in_12(led_32x_array_2_out_50),
    .in_13(led_32x_array_2_out_51), .in_14(led_32x_array_2_out_52), .in_15(led_32x_array_2_out_53),
    .in_16(led_32x_array_2_out_54), .in_17(led_32x_array_2_out_55), .in_18(led_32x_array_2_out_56),
    .in_19(led_32x_array_2_out_57), .in_20(led_32x_array_2_out_58), .in_21(led_32x_array_2_out_59),
    .in_22(led_32x_array_2_out_60), .in_23(led_32x_array_2_out_61), .in_24(led_32x_array_2_out_62),
    .in_25(led_32x_array_2_out_63), .in_26(led_32x_array_2_out_64), .in_27(led_32x_array_2_out_65),
    .in_28(led_32x_array_2_out_66), .in_29(led_32x_array_2_out_67), .in_30(led_32x_array_2_out_68),
    .in_31(led_32x_array_2_out_69), .in_32(led_32x_array_2_out_70), .draw(Settings[0]), .erase(Settings[1]),
    .push(Settings[2]), .OUT(out_7), .out_39(led_32x_array_3_out_39), .out_40(led_32x_array_3_out_40),
    .out_41(led_32x_array_3_out_41), .out_42(led_32x_array_3_out_42), .out_43(led_32x_array_3_out_43),
    .out_44(led_32x_array_3_out_44), .out_45(led_32x_array_3_out_45), .out_46(led_32x_array_3_out_46),
    .out_47(led_32x_array_3_out_47), .out_48(led_32x_array_3_out_48), .out_49(led_32x_array_3_out_49),
    .out_50(led_32x_array_3_out_50), .out_51(led_32x_array_3_out_51), .out_52(led_32x_array_3_out_52),
    .out_53(led_32x_array_3_out_53), .out_54(led_32x_array_3_out_54), .out_55(led_32x_array_3_out_55),
    .out_56(led_32x_array_3_out_56), .out_57(led_32x_array_3_out_57), .out_58(led_32x_array_3_out_58),
    .out_59(led_32x_array_3_out_59), .out_60(led_32x_array_3_out_60), .out_61(led_32x_array_3_out_61),
    .out_62(led_32x_array_3_out_62), .out_63(led_32x_array_3_out_63), .out_64(led_32x_array_3_out_64),
    .out_65(led_32x_array_3_out_65), .out_66(led_32x_array_3_out_66), .out_67(led_32x_array_3_out_67),
    .out_68(led_32x_array_3_out_68), .out_69(led_32x_array_3_out_69), .out_70(led_32x_array_3_out_70),
    .Select(demultiplexer_2_out2), .Pixel_info(led_32x_array_3_pixel_info), .clear(Settings[3]));
  buf buffer_3 (pull_resistor_1_node, led_32x_array_3_pixel_info);
  LED_32x_array led_32x_array_4 (
    .in_1(led_32x_array_3_out_39), .in_2(led_32x_array_3_out_40), .in_3(led_32x_array_3_out_41),
    .in_4(led_32x_array_3_out_42), .in_5(led_32x_array_3_out_43), .in_6(led_32x_array_3_out_44),
    .in_7(led_32x_array_3_out_45), .in_8(led_32x_array_3_out_46), .in_9(led_32x_array_3_out_47),
    .in_10(led_32x_array_3_out_48), .in_11(led_32x_array_3_out_49), .in_12(led_32x_array_3_out_50),
    .in_13(led_32x_array_3_out_51), .in_14(led_32x_array_3_out_52), .in_15(led_32x_array_3_out_53),
    .in_16(led_32x_array_3_out_54), .in_17(led_32x_array_3_out_55), .in_18(led_32x_array_3_out_56),
    .in_19(led_32x_array_3_out_57), .in_20(led_32x_array_3_out_58), .in_21(led_32x_array_3_out_59),
    .in_22(led_32x_array_3_out_60), .in_23(led_32x_array_3_out_61), .in_24(led_32x_array_3_out_62),
    .in_25(led_32x_array_3_out_63), .in_26(led_32x_array_3_out_64), .in_27(led_32x_array_3_out_65),
    .in_28(led_32x_array_3_out_66), .in_29(led_32x_array_3_out_67), .in_30(led_32x_array_3_out_68),
    .in_31(led_32x_array_3_out_69), .in_32(led_32x_array_3_out_70), .draw(Settings[0]), .erase(Settings[1]),
    .push(Settings[2]), .OUT(out_8), .out_39(led_32x_array_4_out_39), .out_40(led_32x_array_4_out_40),
    .out_41(led_32x_array_4_out_41), .out_42(led_32x_array_4_out_42), .out_43(led_32x_array_4_out_43),
    .out_44(led_32x_array_4_out_44), .out_45(led_32x_array_4_out_45), .out_46(led_32x_array_4_out_46),
    .out_47(led_32x_array_4_out_47), .out_48(led_32x_array_4_out_48), .out_49(led_32x_array_4_out_49),
    .out_50(led_32x_array_4_out_50), .out_51(led_32x_array_4_out_51), .out_52(led_32x_array_4_out_52),
    .out_53(led_32x_array_4_out_53), .out_54(led_32x_array_4_out_54), .out_55(led_32x_array_4_out_55),
    .out_56(led_32x_array_4_out_56), .out_57(led_32x_array_4_out_57), .out_58(led_32x_array_4_out_58),
    .out_59(led_32x_array_4_out_59), .out_60(led_32x_array_4_out_60), .out_61(led_32x_array_4_out_61),
    .out_62(led_32x_array_4_out_62), .out_63(led_32x_array_4_out_63), .out_64(led_32x_array_4_out_64),
    .out_65(led_32x_array_4_out_65), .out_66(led_32x_array_4_out_66), .out_67(led_32x_array_4_out_67),
    .out_68(led_32x_array_4_out_68), .out_69(led_32x_array_4_out_69), .out_70(led_32x_array_4_out_70),
    .Select(demultiplexer_2_out3), .Pixel_info(led_32x_array_4_pixel_info), .clear(Settings[3]));
  LED_32x_array led_32x_array_5 (
    .in_1(led_32x_array_4_out_39), .in_2(led_32x_array_4_out_40), .in_3(led_32x_array_4_out_41),
    .in_4(led_32x_array_4_out_42), .in_5(led_32x_array_4_out_43), .in_6(led_32x_array_4_out_44),
    .in_7(led_32x_array_4_out_45), .in_8(led_32x_array_4_out_46), .in_9(led_32x_array_4_out_47),
    .in_10(led_32x_array_4_out_48), .in_11(led_32x_array_4_out_49), .in_12(led_32x_array_4_out_50),
    .in_13(led_32x_array_4_out_51), .in_14(led_32x_array_4_out_52), .in_15(led_32x_array_4_out_53),
    .in_16(led_32x_array_4_out_54), .in_17(led_32x_array_4_out_55), .in_18(led_32x_array_4_out_56),
    .in_19(led_32x_array_4_out_57), .in_20(led_32x_array_4_out_58), .in_21(led_32x_array_4_out_59),
    .in_22(led_32x_array_4_out_60), .in_23(led_32x_array_4_out_61), .in_24(led_32x_array_4_out_62),
    .in_25(led_32x_array_4_out_63), .in_26(led_32x_array_4_out_64), .in_27(led_32x_array_4_out_65),
    .in_28(led_32x_array_4_out_66), .in_29(led_32x_array_4_out_67), .in_30(led_32x_array_4_out_68),
    .in_31(led_32x_array_4_out_69), .in_32(led_32x_array_4_out_70), .draw(Settings[0]), .erase(Settings[1]),
    .push(Settings[2]), .OUT(out_9), .out_39(led_32x_array_5_out_39), .out_40(led_32x_array_5_out_40),
    .out_41(led_32x_array_5_out_41), .out_42(led_32x_array_5_out_42), .out_43(led_32x_array_5_out_43),
    .out_44(led_32x_array_5_out_44), .out_45(led_32x_array_5_out_45), .out_46(led_32x_array_5_out_46),
    .out_47(led_32x_array_5_out_47), .out_48(led_32x_array_5_out_48), .out_49(led_32x_array_5_out_49),
    .out_50(led_32x_array_5_out_50), .out_51(led_32x_array_5_out_51), .out_52(led_32x_array_5_out_52),
    .out_53(led_32x_array_5_out_53), .out_54(led_32x_array_5_out_54), .out_55(led_32x_array_5_out_55),
    .out_56(led_32x_array_5_out_56), .out_57(led_32x_array_5_out_57), .out_58(led_32x_array_5_out_58),
    .out_59(led_32x_array_5_out_59), .out_60(led_32x_array_5_out_60), .out_61(led_32x_array_5_out_61),
    .out_62(led_32x_array_5_out_62), .out_63(led_32x_array_5_out_63), .out_64(led_32x_array_5_out_64),
    .out_65(led_32x_array_5_out_65), .out_66(led_32x_array_5_out_66), .out_67(led_32x_array_5_out_67),
    .out_68(led_32x_array_5_out_68), .out_69(led_32x_array_5_out_69), .out_70(led_32x_array_5_out_70),
    .Select(demultiplexer_2_out4), .Pixel_info(led_32x_array_5_pixel_info), .clear(Settings[3]));
  buf buffer_4 (pull_resistor_1_node, led_32x_array_4_pixel_info);
  buf buffer_5 (pull_resistor_1_node, led_32x_array_5_pixel_info);
  LED_32x_array led_32x_array_6 (
    .in_1(led_32x_array_5_out_39), .in_2(led_32x_array_5_out_40), .in_3(led_32x_array_5_out_41),
    .in_4(led_32x_array_5_out_42), .in_5(led_32x_array_5_out_43), .in_6(led_32x_array_5_out_44),
    .in_7(led_32x_array_5_out_45), .in_8(led_32x_array_5_out_46), .in_9(led_32x_array_5_out_47),
    .in_10(led_32x_array_5_out_48), .in_11(led_32x_array_5_out_49), .in_12(led_32x_array_5_out_50),
    .in_13(led_32x_array_5_out_51), .in_14(led_32x_array_5_out_52), .in_15(led_32x_array_5_out_53),
    .in_16(led_32x_array_5_out_54), .in_17(led_32x_array_5_out_55), .in_18(led_32x_array_5_out_56),
    .in_19(led_32x_array_5_out_57), .in_20(led_32x_array_5_out_58), .in_21(led_32x_array_5_out_59),
    .in_22(led_32x_array_5_out_60), .in_23(led_32x_array_5_out_61), .in_24(led_32x_array_5_out_62),
    .in_25(led_32x_array_5_out_63), .in_26(led_32x_array_5_out_64), .in_27(led_32x_array_5_out_65),
    .in_28(led_32x_array_5_out_66), .in_29(led_32x_array_5_out_67), .in_30(led_32x_array_5_out_68),
    .in_31(led_32x_array_5_out_69), .in_32(led_32x_array_5_out_70), .draw(Settings[0]), .erase(Settings[1]),
    .push(Settings[2]), .OUT(out_10), .out_39(led_32x_array_6_out_39), .out_40(led_32x_array_6_out_40),
    .out_41(led_32x_array_6_out_41), .out_42(led_32x_array_6_out_42), .out_43(led_32x_array_6_out_43),
    .out_44(led_32x_array_6_out_44), .out_45(led_32x_array_6_out_45), .out_46(led_32x_array_6_out_46),
    .out_47(led_32x_array_6_out_47), .out_48(led_32x_array_6_out_48), .out_49(led_32x_array_6_out_49),
    .out_50(led_32x_array_6_out_50), .out_51(led_32x_array_6_out_51), .out_52(led_32x_array_6_out_52),
    .out_53(led_32x_array_6_out_53), .out_54(led_32x_array_6_out_54), .out_55(led_32x_array_6_out_55),
    .out_56(led_32x_array_6_out_56), .out_57(led_32x_array_6_out_57), .out_58(led_32x_array_6_out_58),
    .out_59(led_32x_array_6_out_59), .out_60(led_32x_array_6_out_60), .out_61(led_32x_array_6_out_61),
    .out_62(led_32x_array_6_out_62), .out_63(led_32x_array_6_out_63), .out_64(led_32x_array_6_out_64),
    .out_65(led_32x_array_6_out_65), .out_66(led_32x_array_6_out_66), .out_67(led_32x_array_6_out_67),
    .out_68(led_32x_array_6_out_68), .out_69(led_32x_array_6_out_69), .out_70(led_32x_array_6_out_70),
    .Select(demultiplexer_2_out5), .Pixel_info(led_32x_array_6_pixel_info), .clear(Settings[3]));
  buf buffer_6 (pull_resistor_1_node, led_32x_array_6_pixel_info);
  LED_32x_array led_32x_array_7 (
    .in_1(led_32x_array_6_out_39), .in_2(led_32x_array_6_out_40), .in_3(led_32x_array_6_out_41),
    .in_4(led_32x_array_6_out_42), .in_5(led_32x_array_6_out_43), .in_6(led_32x_array_6_out_44),
    .in_7(led_32x_array_6_out_45), .in_8(led_32x_array_6_out_46), .in_9(led_32x_array_6_out_47),
    .in_10(led_32x_array_6_out_48), .in_11(led_32x_array_6_out_49), .in_12(led_32x_array_6_out_50),
    .in_13(led_32x_array_6_out_51), .in_14(led_32x_array_6_out_52), .in_15(led_32x_array_6_out_53),
    .in_16(led_32x_array_6_out_54), .in_17(led_32x_array_6_out_55), .in_18(led_32x_array_6_out_56),
    .in_19(led_32x_array_6_out_57), .in_20(led_32x_array_6_out_58), .in_21(led_32x_array_6_out_59),
    .in_22(led_32x_array_6_out_60), .in_23(led_32x_array_6_out_61), .in_24(led_32x_array_6_out_62),
    .in_25(led_32x_array_6_out_63), .in_26(led_32x_array_6_out_64), .in_27(led_32x_array_6_out_65),
    .in_28(led_32x_array_6_out_66), .in_29(led_32x_array_6_out_67), .in_30(led_32x_array_6_out_68),
    .in_31(led_32x_array_6_out_69), .in_32(led_32x_array_6_out_70), .draw(Settings[0]), .erase(Settings[1]),
    .push(Settings[2]), .OUT(out_11), .out_39(led_32x_array_7_out_39), .out_40(led_32x_array_7_out_40),
    .out_41(led_32x_array_7_out_41), .out_42(led_32x_array_7_out_42), .out_43(led_32x_array_7_out_43),
    .out_44(led_32x_array_7_out_44), .out_45(led_32x_array_7_out_45), .out_46(led_32x_array_7_out_46),
    .out_47(led_32x_array_7_out_47), .out_48(led_32x_array_7_out_48), .out_49(led_32x_array_7_out_49),
    .out_50(led_32x_array_7_out_50), .out_51(led_32x_array_7_out_51), .out_52(led_32x_array_7_out_52),
    .out_53(led_32x_array_7_out_53), .out_54(led_32x_array_7_out_54), .out_55(led_32x_array_7_out_55),
    .out_56(led_32x_array_7_out_56), .out_57(led_32x_array_7_out_57), .out_58(led_32x_array_7_out_58),
    .out_59(led_32x_array_7_out_59), .out_60(led_32x_array_7_out_60), .out_61(led_32x_array_7_out_61),
    .out_62(led_32x_array_7_out_62), .out_63(led_32x_array_7_out_63), .out_64(led_32x_array_7_out_64),
    .out_65(led_32x_array_7_out_65), .out_66(led_32x_array_7_out_66), .out_67(led_32x_array_7_out_67),
    .out_68(led_32x_array_7_out_68), .out_69(led_32x_array_7_out_69), .out_70(led_32x_array_7_out_70),
    .Select(demultiplexer_2_out6), .Pixel_info(led_32x_array_7_pixel_info), .clear(Settings[3]));
  buf buffer_7 (pull_resistor_1_node, led_32x_array_7_pixel_info);
  LED_32x_array led_32x_array_8 (
    .in_1(led_32x_array_7_out_39), .in_2(led_32x_array_7_out_40), .in_3(led_32x_array_7_out_41),
    .in_4(led_32x_array_7_out_42), .in_5(led_32x_array_7_out_43), .in_6(led_32x_array_7_out_44),
    .in_7(led_32x_array_7_out_45), .in_8(led_32x_array_7_out_46), .in_9(led_32x_array_7_out_47),
    .in_10(led_32x_array_7_out_48), .in_11(led_32x_array_7_out_49), .in_12(led_32x_array_7_out_50),
    .in_13(led_32x_array_7_out_51), .in_14(led_32x_array_7_out_52), .in_15(led_32x_array_7_out_53),
    .in_16(led_32x_array_7_out_54), .in_17(led_32x_array_7_out_55), .in_18(led_32x_array_7_out_56),
    .in_19(led_32x_array_7_out_57), .in_20(led_32x_array_7_out_58), .in_21(led_32x_array_7_out_59),
    .in_22(led_32x_array_7_out_60), .in_23(led_32x_array_7_out_61), .in_24(led_32x_array_7_out_62),
    .in_25(led_32x_array_7_out_63), .in_26(led_32x_array_7_out_64), .in_27(led_32x_array_7_out_65),
    .in_28(led_32x_array_7_out_66), .in_29(led_32x_array_7_out_67), .in_30(led_32x_array_7_out_68),
    .in_31(led_32x_array_7_out_69), .in_32(led_32x_array_7_out_70), .draw(Settings[0]), .erase(Settings[1]),
    .push(Settings[2]), .OUT(out_12), .out_39(led_32x_array_8_out_39), .out_40(led_32x_array_8_out_40),
    .out_41(led_32x_array_8_out_41), .out_42(led_32x_array_8_out_42), .out_43(led_32x_array_8_out_43),
    .out_44(led_32x_array_8_out_44), .out_45(led_32x_array_8_out_45), .out_46(led_32x_array_8_out_46),
    .out_47(led_32x_array_8_out_47), .out_48(led_32x_array_8_out_48), .out_49(led_32x_array_8_out_49),
    .out_50(led_32x_array_8_out_50), .out_51(led_32x_array_8_out_51), .out_52(led_32x_array_8_out_52),
    .out_53(led_32x_array_8_out_53), .out_54(led_32x_array_8_out_54), .out_55(led_32x_array_8_out_55),
    .out_56(led_32x_array_8_out_56), .out_57(led_32x_array_8_out_57), .out_58(led_32x_array_8_out_58),
    .out_59(led_32x_array_8_out_59), .out_60(led_32x_array_8_out_60), .out_61(led_32x_array_8_out_61),
    .out_62(led_32x_array_8_out_62), .out_63(led_32x_array_8_out_63), .out_64(led_32x_array_8_out_64),
    .out_65(led_32x_array_8_out_65), .out_66(led_32x_array_8_out_66), .out_67(led_32x_array_8_out_67),
    .out_68(led_32x_array_8_out_68), .out_69(led_32x_array_8_out_69), .out_70(led_32x_array_8_out_70),
    .Select(demultiplexer_2_out7), .Pixel_info(led_32x_array_8_pixel_info), .clear(Settings[3]));
  LED_32x_array led_32x_array_9 (
    .in_1(led_32x_array_8_out_39), .in_2(led_32x_array_8_out_40), .in_3(led_32x_array_8_out_41),
    .in_4(led_32x_array_8_out_42), .in_5(led_32x_array_8_out_43), .in_6(led_32x_array_8_out_44),
    .in_7(led_32x_array_8_out_45), .in_8(led_32x_array_8_out_46), .in_9(led_32x_array_8_out_47),
    .in_10(led_32x_array_8_out_48), .in_11(led_32x_array_8_out_49), .in_12(led_32x_array_8_out_50),
    .in_13(led_32x_array_8_out_51), .in_14(led_32x_array_8_out_52), .in_15(led_32x_array_8_out_53),
    .in_16(led_32x_array_8_out_54), .in_17(led_32x_array_8_out_55), .in_18(led_32x_array_8_out_56),
    .in_19(led_32x_array_8_out_57), .in_20(led_32x_array_8_out_58), .in_21(led_32x_array_8_out_59),
    .in_22(led_32x_array_8_out_60), .in_23(led_32x_array_8_out_61), .in_24(led_32x_array_8_out_62),
    .in_25(led_32x_array_8_out_63), .in_26(led_32x_array_8_out_64), .in_27(led_32x_array_8_out_65),
    .in_28(led_32x_array_8_out_66), .in_29(led_32x_array_8_out_67), .in_30(led_32x_array_8_out_68),
    .in_31(led_32x_array_8_out_69), .in_32(led_32x_array_8_out_70), .draw(Settings[0]), .erase(Settings[1]),
    .push(Settings[2]), .OUT(out_13), .out_39(led_32x_array_9_out_39), .out_40(led_32x_array_9_out_40),
    .out_41(led_32x_array_9_out_41), .out_42(led_32x_array_9_out_42), .out_43(led_32x_array_9_out_43),
    .out_44(led_32x_array_9_out_44), .out_45(led_32x_array_9_out_45), .out_46(led_32x_array_9_out_46),
    .out_47(led_32x_array_9_out_47), .out_48(led_32x_array_9_out_48), .out_49(led_32x_array_9_out_49),
    .out_50(led_32x_array_9_out_50), .out_51(led_32x_array_9_out_51), .out_52(led_32x_array_9_out_52),
    .out_53(led_32x_array_9_out_53), .out_54(led_32x_array_9_out_54), .out_55(led_32x_array_9_out_55),
    .out_56(led_32x_array_9_out_56), .out_57(led_32x_array_9_out_57), .out_58(led_32x_array_9_out_58),
    .out_59(led_32x_array_9_out_59), .out_60(led_32x_array_9_out_60), .out_61(led_32x_array_9_out_61),
    .out_62(led_32x_array_9_out_62), .out_63(led_32x_array_9_out_63), .out_64(led_32x_array_9_out_64),
    .out_65(led_32x_array_9_out_65), .out_66(led_32x_array_9_out_66), .out_67(led_32x_array_9_out_67),
    .out_68(led_32x_array_9_out_68), .out_69(led_32x_array_9_out_69), .out_70(led_32x_array_9_out_70),
    .Select(demultiplexer_2_out8), .Pixel_info(led_32x_array_9_pixel_info), .clear(Settings[3]));
  buf buffer_8 (pull_resistor_1_node, led_32x_array_8_pixel_info);
  buf buffer_9 (pull_resistor_1_node, led_32x_array_9_pixel_info);
  LED_32x_array led_32x_array_10 (
    .in_1(led_32x_array_9_out_39), .in_2(led_32x_array_9_out_40), .in_3(led_32x_array_9_out_41),
    .in_4(led_32x_array_9_out_42), .in_5(led_32x_array_9_out_43), .in_6(led_32x_array_9_out_44),
    .in_7(led_32x_array_9_out_45), .in_8(led_32x_array_9_out_46), .in_9(led_32x_array_9_out_47),
    .in_10(led_32x_array_9_out_48), .in_11(led_32x_array_9_out_49), .in_12(led_32x_array_9_out_50),
    .in_13(led_32x_array_9_out_51), .in_14(led_32x_array_9_out_52), .in_15(led_32x_array_9_out_53),
    .in_16(led_32x_array_9_out_54), .in_17(led_32x_array_9_out_55), .in_18(led_32x_array_9_out_56),
    .in_19(led_32x_array_9_out_57), .in_20(led_32x_array_9_out_58), .in_21(led_32x_array_9_out_59),
    .in_22(led_32x_array_9_out_60), .in_23(led_32x_array_9_out_61), .in_24(led_32x_array_9_out_62),
    .in_25(led_32x_array_9_out_63), .in_26(led_32x_array_9_out_64), .in_27(led_32x_array_9_out_65),
    .in_28(led_32x_array_9_out_66), .in_29(led_32x_array_9_out_67), .in_30(led_32x_array_9_out_68),
    .in_31(led_32x_array_9_out_69), .in_32(led_32x_array_9_out_70), .draw(Settings[0]), .erase(Settings[1]),
    .push(Settings[2]), .OUT(out_14), .out_39(led_32x_array_10_out_39), .out_40(led_32x_array_10_out_40),
    .out_41(led_32x_array_10_out_41), .out_42(led_32x_array_10_out_42), .out_43(led_32x_array_10_out_43),
    .out_44(led_32x_array_10_out_44), .out_45(led_32x_array_10_out_45), .out_46(led_32x_array_10_out_46),
    .out_47(led_32x_array_10_out_47), .out_48(led_32x_array_10_out_48), .out_49(led_32x_array_10_out_49),
    .out_50(led_32x_array_10_out_50), .out_51(led_32x_array_10_out_51), .out_52(led_32x_array_10_out_52),
    .out_53(led_32x_array_10_out_53), .out_54(led_32x_array_10_out_54), .out_55(led_32x_array_10_out_55),
    .out_56(led_32x_array_10_out_56), .out_57(led_32x_array_10_out_57), .out_58(led_32x_array_10_out_58),
    .out_59(led_32x_array_10_out_59), .out_60(led_32x_array_10_out_60), .out_61(led_32x_array_10_out_61),
    .out_62(led_32x_array_10_out_62), .out_63(led_32x_array_10_out_63), .out_64(led_32x_array_10_out_64),
    .out_65(led_32x_array_10_out_65), .out_66(led_32x_array_10_out_66), .out_67(led_32x_array_10_out_67),
    .out_68(led_32x_array_10_out_68), .out_69(led_32x_array_10_out_69), .out_70(led_32x_array_10_out_70),
    .Select(demultiplexer_2_out9), .Pixel_info(led_32x_array_10_pixel_info), .clear(Settings[3]));
  buf buffer_10 (pull_resistor_1_node, led_32x_array_10_pixel_info);
  LED_32x_array led_32x_array_11 (
    .in_1(led_32x_array_10_out_39), .in_2(led_32x_array_10_out_40), .in_3(led_32x_array_10_out_41),
    .in_4(led_32x_array_10_out_42), .in_5(led_32x_array_10_out_43), .in_6(led_32x_array_10_out_44),
    .in_7(led_32x_array_10_out_45), .in_8(led_32x_array_10_out_46), .in_9(led_32x_array_10_out_47),
    .in_10(led_32x_array_10_out_48), .in_11(led_32x_array_10_out_49), .in_12(led_32x_array_10_out_50),
    .in_13(led_32x_array_10_out_51), .in_14(led_32x_array_10_out_52), .in_15(led_32x_array_10_out_53),
    .in_16(led_32x_array_10_out_54), .in_17(led_32x_array_10_out_55), .in_18(led_32x_array_10_out_56),
    .in_19(led_32x_array_10_out_57), .in_20(led_32x_array_10_out_58), .in_21(led_32x_array_10_out_59),
    .in_22(led_32x_array_10_out_60), .in_23(led_32x_array_10_out_61), .in_24(led_32x_array_10_out_62),
    .in_25(led_32x_array_10_out_63), .in_26(led_32x_array_10_out_64), .in_27(led_32x_array_10_out_65),
    .in_28(led_32x_array_10_out_66), .in_29(led_32x_array_10_out_67), .in_30(led_32x_array_10_out_68),
    .in_31(led_32x_array_10_out_69), .in_32(led_32x_array_10_out_70), .draw(Settings[0]),
    .erase(Settings[1]), .push(Settings[2]), .OUT(out_15), .out_39(led_32x_array_11_out_39),
    .out_40(led_32x_array_11_out_40), .out_41(led_32x_array_11_out_41), .out_42(led_32x_array_11_out_42),
    .out_43(led_32x_array_11_out_43), .out_44(led_32x_array_11_out_44), .out_45(led_32x_array_11_out_45),
    .out_46(led_32x_array_11_out_46), .out_47(led_32x_array_11_out_47), .out_48(led_32x_array_11_out_48),
    .out_49(led_32x_array_11_out_49), .out_50(led_32x_array_11_out_50), .out_51(led_32x_array_11_out_51),
    .out_52(led_32x_array_11_out_52), .out_53(led_32x_array_11_out_53), .out_54(led_32x_array_11_out_54),
    .out_55(led_32x_array_11_out_55), .out_56(led_32x_array_11_out_56), .out_57(led_32x_array_11_out_57),
    .out_58(led_32x_array_11_out_58), .out_59(led_32x_array_11_out_59), .out_60(led_32x_array_11_out_60),
    .out_61(led_32x_array_11_out_61), .out_62(led_32x_array_11_out_62), .out_63(led_32x_array_11_out_63),
    .out_64(led_32x_array_11_out_64), .out_65(led_32x_array_11_out_65), .out_66(led_32x_array_11_out_66),
    .out_67(led_32x_array_11_out_67), .out_68(led_32x_array_11_out_68), .out_69(led_32x_array_11_out_69),
    .out_70(led_32x_array_11_out_70), .Select(demultiplexer_2_out10),
    .Pixel_info(led_32x_array_11_pixel_info), .clear(Settings[3]));
  buf buffer_11 (pull_resistor_1_node, led_32x_array_11_pixel_info);
  LED_32x_array led_32x_array_12 (
    .in_1(led_32x_array_11_out_39), .in_2(led_32x_array_11_out_40), .in_3(led_32x_array_11_out_41),
    .in_4(led_32x_array_11_out_42), .in_5(led_32x_array_11_out_43), .in_6(led_32x_array_11_out_44),
    .in_7(led_32x_array_11_out_45), .in_8(led_32x_array_11_out_46), .in_9(led_32x_array_11_out_47),
    .in_10(led_32x_array_11_out_48), .in_11(led_32x_array_11_out_49), .in_12(led_32x_array_11_out_50),
    .in_13(led_32x_array_11_out_51), .in_14(led_32x_array_11_out_52), .in_15(led_32x_array_11_out_53),
    .in_16(led_32x_array_11_out_54), .in_17(led_32x_array_11_out_55), .in_18(led_32x_array_11_out_56),
    .in_19(led_32x_array_11_out_57), .in_20(led_32x_array_11_out_58), .in_21(led_32x_array_11_out_59),
    .in_22(led_32x_array_11_out_60), .in_23(led_32x_array_11_out_61), .in_24(led_32x_array_11_out_62),
    .in_25(led_32x_array_11_out_63), .in_26(led_32x_array_11_out_64), .in_27(led_32x_array_11_out_65),
    .in_28(led_32x_array_11_out_66), .in_29(led_32x_array_11_out_67), .in_30(led_32x_array_11_out_68),
    .in_31(led_32x_array_11_out_69), .in_32(led_32x_array_11_out_70), .draw(Settings[0]),
    .erase(Settings[1]), .push(Settings[2]), .OUT(out_16), .out_39(led_32x_array_12_out_39),
    .out_40(led_32x_array_12_out_40), .out_41(led_32x_array_12_out_41), .out_42(led_32x_array_12_out_42),
    .out_43(led_32x_array_12_out_43), .out_44(led_32x_array_12_out_44), .out_45(led_32x_array_12_out_45),
    .out_46(led_32x_array_12_out_46), .out_47(led_32x_array_12_out_47), .out_48(led_32x_array_12_out_48),
    .out_49(led_32x_array_12_out_49), .out_50(led_32x_array_12_out_50), .out_51(led_32x_array_12_out_51),
    .out_52(led_32x_array_12_out_52), .out_53(led_32x_array_12_out_53), .out_54(led_32x_array_12_out_54),
    .out_55(led_32x_array_12_out_55), .out_56(led_32x_array_12_out_56), .out_57(led_32x_array_12_out_57),
    .out_58(led_32x_array_12_out_58), .out_59(led_32x_array_12_out_59), .out_60(led_32x_array_12_out_60),
    .out_61(led_32x_array_12_out_61), .out_62(led_32x_array_12_out_62), .out_63(led_32x_array_12_out_63),
    .out_64(led_32x_array_12_out_64), .out_65(led_32x_array_12_out_65), .out_66(led_32x_array_12_out_66),
    .out_67(led_32x_array_12_out_67), .out_68(led_32x_array_12_out_68), .out_69(led_32x_array_12_out_69),
    .out_70(led_32x_array_12_out_70), .Select(demultiplexer_2_out11),
    .Pixel_info(led_32x_array_12_pixel_info), .clear(Settings[3]));
  LED_32x_array led_32x_array_13 (
    .in_1(led_32x_array_12_out_39), .in_2(led_32x_array_12_out_40), .in_3(led_32x_array_12_out_41),
    .in_4(led_32x_array_12_out_42), .in_5(led_32x_array_12_out_43), .in_6(led_32x_array_12_out_44),
    .in_7(led_32x_array_12_out_45), .in_8(led_32x_array_12_out_46), .in_9(led_32x_array_12_out_47),
    .in_10(led_32x_array_12_out_48), .in_11(led_32x_array_12_out_49), .in_12(led_32x_array_12_out_50),
    .in_13(led_32x_array_12_out_51), .in_14(led_32x_array_12_out_52), .in_15(led_32x_array_12_out_53),
    .in_16(led_32x_array_12_out_54), .in_17(led_32x_array_12_out_55), .in_18(led_32x_array_12_out_56),
    .in_19(led_32x_array_12_out_57), .in_20(led_32x_array_12_out_58), .in_21(led_32x_array_12_out_59),
    .in_22(led_32x_array_12_out_60), .in_23(led_32x_array_12_out_61), .in_24(led_32x_array_12_out_62),
    .in_25(led_32x_array_12_out_63), .in_26(led_32x_array_12_out_64), .in_27(led_32x_array_12_out_65),
    .in_28(led_32x_array_12_out_66), .in_29(led_32x_array_12_out_67), .in_30(led_32x_array_12_out_68),
    .in_31(led_32x_array_12_out_69), .in_32(led_32x_array_12_out_70), .draw(Settings[0]),
    .erase(Settings[1]), .push(Settings[2]), .OUT(out_17), .out_39(led_32x_array_13_out_39),
    .out_40(led_32x_array_13_out_40), .out_41(led_32x_array_13_out_41), .out_42(led_32x_array_13_out_42),
    .out_43(led_32x_array_13_out_43), .out_44(led_32x_array_13_out_44), .out_45(led_32x_array_13_out_45),
    .out_46(led_32x_array_13_out_46), .out_47(led_32x_array_13_out_47), .out_48(led_32x_array_13_out_48),
    .out_49(led_32x_array_13_out_49), .out_50(led_32x_array_13_out_50), .out_51(led_32x_array_13_out_51),
    .out_52(led_32x_array_13_out_52), .out_53(led_32x_array_13_out_53), .out_54(led_32x_array_13_out_54),
    .out_55(led_32x_array_13_out_55), .out_56(led_32x_array_13_out_56), .out_57(led_32x_array_13_out_57),
    .out_58(led_32x_array_13_out_58), .out_59(led_32x_array_13_out_59), .out_60(led_32x_array_13_out_60),
    .out_61(led_32x_array_13_out_61), .out_62(led_32x_array_13_out_62), .out_63(led_32x_array_13_out_63),
    .out_64(led_32x_array_13_out_64), .out_65(led_32x_array_13_out_65), .out_66(led_32x_array_13_out_66),
    .out_67(led_32x_array_13_out_67), .out_68(led_32x_array_13_out_68), .out_69(led_32x_array_13_out_69),
    .out_70(led_32x_array_13_out_70), .Select(demultiplexer_2_out12),
    .Pixel_info(led_32x_array_13_pixel_info), .clear(Settings[3]));
  buf buffer_12 (pull_resistor_1_node, led_32x_array_12_pixel_info);
  buf buffer_13 (pull_resistor_1_node, led_32x_array_13_pixel_info);
  LED_32x_array led_32x_array_14 (
    .in_1(led_32x_array_13_out_39), .in_2(led_32x_array_13_out_40), .in_3(led_32x_array_13_out_41),
    .in_4(led_32x_array_13_out_42), .in_5(led_32x_array_13_out_43), .in_6(led_32x_array_13_out_44),
    .in_7(led_32x_array_13_out_45), .in_8(led_32x_array_13_out_46), .in_9(led_32x_array_13_out_47),
    .in_10(led_32x_array_13_out_48), .in_11(led_32x_array_13_out_49), .in_12(led_32x_array_13_out_50),
    .in_13(led_32x_array_13_out_51), .in_14(led_32x_array_13_out_52), .in_15(led_32x_array_13_out_53),
    .in_16(led_32x_array_13_out_54), .in_17(led_32x_array_13_out_55), .in_18(led_32x_array_13_out_56),
    .in_19(led_32x_array_13_out_57), .in_20(led_32x_array_13_out_58), .in_21(led_32x_array_13_out_59),
    .in_22(led_32x_array_13_out_60), .in_23(led_32x_array_13_out_61), .in_24(led_32x_array_13_out_62),
    .in_25(led_32x_array_13_out_63), .in_26(led_32x_array_13_out_64), .in_27(led_32x_array_13_out_65),
    .in_28(led_32x_array_13_out_66), .in_29(led_32x_array_13_out_67), .in_30(led_32x_array_13_out_68),
    .in_31(led_32x_array_13_out_69), .in_32(led_32x_array_13_out_70), .draw(Settings[0]),
    .erase(Settings[1]), .push(Settings[2]), .OUT(out_18), .out_39(led_32x_array_14_out_39),
    .out_40(led_32x_array_14_out_40), .out_41(led_32x_array_14_out_41), .out_42(led_32x_array_14_out_42),
    .out_43(led_32x_array_14_out_43), .out_44(led_32x_array_14_out_44), .out_45(led_32x_array_14_out_45),
    .out_46(led_32x_array_14_out_46), .out_47(led_32x_array_14_out_47), .out_48(led_32x_array_14_out_48),
    .out_49(led_32x_array_14_out_49), .out_50(led_32x_array_14_out_50), .out_51(led_32x_array_14_out_51),
    .out_52(led_32x_array_14_out_52), .out_53(led_32x_array_14_out_53), .out_54(led_32x_array_14_out_54),
    .out_55(led_32x_array_14_out_55), .out_56(led_32x_array_14_out_56), .out_57(led_32x_array_14_out_57),
    .out_58(led_32x_array_14_out_58), .out_59(led_32x_array_14_out_59), .out_60(led_32x_array_14_out_60),
    .out_61(led_32x_array_14_out_61), .out_62(led_32x_array_14_out_62), .out_63(led_32x_array_14_out_63),
    .out_64(led_32x_array_14_out_64), .out_65(led_32x_array_14_out_65), .out_66(led_32x_array_14_out_66),
    .out_67(led_32x_array_14_out_67), .out_68(led_32x_array_14_out_68), .out_69(led_32x_array_14_out_69),
    .out_70(led_32x_array_14_out_70), .Select(demultiplexer_2_out13),
    .Pixel_info(led_32x_array_14_pixel_info), .clear(Settings[3]));
  buf buffer_14 (pull_resistor_1_node, led_32x_array_14_pixel_info);
  LED_32x_array led_32x_array_15 (
    .in_1(led_32x_array_14_out_39), .in_2(led_32x_array_14_out_40), .in_3(led_32x_array_14_out_41),
    .in_4(led_32x_array_14_out_42), .in_5(led_32x_array_14_out_43), .in_6(led_32x_array_14_out_44),
    .in_7(led_32x_array_14_out_45), .in_8(led_32x_array_14_out_46), .in_9(led_32x_array_14_out_47),
    .in_10(led_32x_array_14_out_48), .in_11(led_32x_array_14_out_49), .in_12(led_32x_array_14_out_50),
    .in_13(led_32x_array_14_out_51), .in_14(led_32x_array_14_out_52), .in_15(led_32x_array_14_out_53),
    .in_16(led_32x_array_14_out_54), .in_17(led_32x_array_14_out_55), .in_18(led_32x_array_14_out_56),
    .in_19(led_32x_array_14_out_57), .in_20(led_32x_array_14_out_58), .in_21(led_32x_array_14_out_59),
    .in_22(led_32x_array_14_out_60), .in_23(led_32x_array_14_out_61), .in_24(led_32x_array_14_out_62),
    .in_25(led_32x_array_14_out_63), .in_26(led_32x_array_14_out_64), .in_27(led_32x_array_14_out_65),
    .in_28(led_32x_array_14_out_66), .in_29(led_32x_array_14_out_67), .in_30(led_32x_array_14_out_68),
    .in_31(led_32x_array_14_out_69), .in_32(led_32x_array_14_out_70), .draw(Settings[0]),
    .erase(Settings[1]), .push(Settings[2]), .OUT(out_19), .out_39(led_32x_array_15_out_39),
    .out_40(led_32x_array_15_out_40), .out_41(led_32x_array_15_out_41), .out_42(led_32x_array_15_out_42),
    .out_43(led_32x_array_15_out_43), .out_44(led_32x_array_15_out_44), .out_45(led_32x_array_15_out_45),
    .out_46(led_32x_array_15_out_46), .out_47(led_32x_array_15_out_47), .out_48(led_32x_array_15_out_48),
    .out_49(led_32x_array_15_out_49), .out_50(led_32x_array_15_out_50), .out_51(led_32x_array_15_out_51),
    .out_52(led_32x_array_15_out_52), .out_53(led_32x_array_15_out_53), .out_54(led_32x_array_15_out_54),
    .out_55(led_32x_array_15_out_55), .out_56(led_32x_array_15_out_56), .out_57(led_32x_array_15_out_57),
    .out_58(led_32x_array_15_out_58), .out_59(led_32x_array_15_out_59), .out_60(led_32x_array_15_out_60),
    .out_61(led_32x_array_15_out_61), .out_62(led_32x_array_15_out_62), .out_63(led_32x_array_15_out_63),
    .out_64(led_32x_array_15_out_64), .out_65(led_32x_array_15_out_65), .out_66(led_32x_array_15_out_66),
    .out_67(led_32x_array_15_out_67), .out_68(led_32x_array_15_out_68), .out_69(led_32x_array_15_out_69),
    .out_70(led_32x_array_15_out_70), .Select(demultiplexer_2_out14),
    .Pixel_info(led_32x_array_15_pixel_info), .clear(Settings[3]));
  buf buffer_15 (pull_resistor_1_node, led_32x_array_15_pixel_info);
  LED_32x_array led_32x_array_16 (
    .in_1(led_32x_array_15_out_39), .in_2(led_32x_array_15_out_40), .in_3(led_32x_array_15_out_41),
    .in_4(led_32x_array_15_out_42), .in_5(led_32x_array_15_out_43), .in_6(led_32x_array_15_out_44),
    .in_7(led_32x_array_15_out_45), .in_8(led_32x_array_15_out_46), .in_9(led_32x_array_15_out_47),
    .in_10(led_32x_array_15_out_48), .in_11(led_32x_array_15_out_49), .in_12(led_32x_array_15_out_50),
    .in_13(led_32x_array_15_out_51), .in_14(led_32x_array_15_out_52), .in_15(led_32x_array_15_out_53),
    .in_16(led_32x_array_15_out_54), .in_17(led_32x_array_15_out_55), .in_18(led_32x_array_15_out_56),
    .in_19(led_32x_array_15_out_57), .in_20(led_32x_array_15_out_58), .in_21(led_32x_array_15_out_59),
    .in_22(led_32x_array_15_out_60), .in_23(led_32x_array_15_out_61), .in_24(led_32x_array_15_out_62),
    .in_25(led_32x_array_15_out_63), .in_26(led_32x_array_15_out_64), .in_27(led_32x_array_15_out_65),
    .in_28(led_32x_array_15_out_66), .in_29(led_32x_array_15_out_67), .in_30(led_32x_array_15_out_68),
    .in_31(led_32x_array_15_out_69), .in_32(led_32x_array_15_out_70), .draw(Settings[0]),
    .erase(Settings[1]), .push(Settings[2]), .OUT(out_20), .out_39(led_32x_array_16_out_39),
    .out_40(led_32x_array_16_out_40), .out_41(led_32x_array_16_out_41), .out_42(led_32x_array_16_out_42),
    .out_43(led_32x_array_16_out_43), .out_44(led_32x_array_16_out_44), .out_45(led_32x_array_16_out_45),
    .out_46(led_32x_array_16_out_46), .out_47(led_32x_array_16_out_47), .out_48(led_32x_array_16_out_48),
    .out_49(led_32x_array_16_out_49), .out_50(led_32x_array_16_out_50), .out_51(led_32x_array_16_out_51),
    .out_52(led_32x_array_16_out_52), .out_53(led_32x_array_16_out_53), .out_54(led_32x_array_16_out_54),
    .out_55(led_32x_array_16_out_55), .out_56(led_32x_array_16_out_56), .out_57(led_32x_array_16_out_57),
    .out_58(led_32x_array_16_out_58), .out_59(led_32x_array_16_out_59), .out_60(led_32x_array_16_out_60),
    .out_61(led_32x_array_16_out_61), .out_62(led_32x_array_16_out_62), .out_63(led_32x_array_16_out_63),
    .out_64(led_32x_array_16_out_64), .out_65(led_32x_array_16_out_65), .out_66(led_32x_array_16_out_66),
    .out_67(led_32x_array_16_out_67), .out_68(led_32x_array_16_out_68), .out_69(led_32x_array_16_out_69),
    .out_70(led_32x_array_16_out_70), .Select(demultiplexer_2_out15),
    .Pixel_info(led_32x_array_16_pixel_info), .clear(Settings[3]));
  LED_32x_array led_32x_array_17 (
    .in_1(led_32x_array_16_out_39), .in_2(led_32x_array_16_out_40), .in_3(led_32x_array_16_out_41),
    .in_4(led_32x_array_16_out_42), .in_5(led_32x_array_16_out_43), .in_6(led_32x_array_16_out_44),
    .in_7(led_32x_array_16_out_45), .in_8(led_32x_array_16_out_46), .in_9(led_32x_array_16_out_47),
    .in_10(led_32x_array_16_out_48), .in_11(led_32x_array_16_out_49), .in_12(led_32x_array_16_out_50),
    .in_13(led_32x_array_16_out_51), .in_14(led_32x_array_16_out_52), .in_15(led_32x_array_16_out_53),
    .in_16(led_32x_array_16_out_54), .in_17(led_32x_array_16_out_55), .in_18(led_32x_array_16_out_56),
    .in_19(led_32x_array_16_out_57), .in_20(led_32x_array_16_out_58), .in_21(led_32x_array_16_out_59),
    .in_22(led_32x_array_16_out_60), .in_23(led_32x_array_16_out_61), .in_24(led_32x_array_16_out_62),
    .in_25(led_32x_array_16_out_63), .in_26(led_32x_array_16_out_64), .in_27(led_32x_array_16_out_65),
    .in_28(led_32x_array_16_out_66), .in_29(led_32x_array_16_out_67), .in_30(led_32x_array_16_out_68),
    .in_31(led_32x_array_16_out_69), .in_32(led_32x_array_16_out_70), .draw(Settings[0]),
    .erase(Settings[1]), .push(Settings[2]), .OUT(out_21), .out_39(led_32x_array_17_out_39),
    .out_40(led_32x_array_17_out_40), .out_41(led_32x_array_17_out_41), .out_42(led_32x_array_17_out_42),
    .out_43(led_32x_array_17_out_43), .out_44(led_32x_array_17_out_44), .out_45(led_32x_array_17_out_45),
    .out_46(led_32x_array_17_out_46), .out_47(led_32x_array_17_out_47), .out_48(led_32x_array_17_out_48),
    .out_49(led_32x_array_17_out_49), .out_50(led_32x_array_17_out_50), .out_51(led_32x_array_17_out_51),
    .out_52(led_32x_array_17_out_52), .out_53(led_32x_array_17_out_53), .out_54(led_32x_array_17_out_54),
    .out_55(led_32x_array_17_out_55), .out_56(led_32x_array_17_out_56), .out_57(led_32x_array_17_out_57),
    .out_58(led_32x_array_17_out_58), .out_59(led_32x_array_17_out_59), .out_60(led_32x_array_17_out_60),
    .out_61(led_32x_array_17_out_61), .out_62(led_32x_array_17_out_62), .out_63(led_32x_array_17_out_63),
    .out_64(led_32x_array_17_out_64), .out_65(led_32x_array_17_out_65), .out_66(led_32x_array_17_out_66),
    .out_67(led_32x_array_17_out_67), .out_68(led_32x_array_17_out_68), .out_69(led_32x_array_17_out_69),
    .out_70(led_32x_array_17_out_70), .Select(demultiplexer_2_out16),
    .Pixel_info(led_32x_array_17_pixel_info), .clear(Settings[3]));
  buf buffer_16 (pull_resistor_1_node, led_32x_array_16_pixel_info);
  buf buffer_17 (pull_resistor_1_node, led_32x_array_17_pixel_info);
  LED_32x_array led_32x_array_18 (
    .in_1(led_32x_array_17_out_39), .in_2(led_32x_array_17_out_40), .in_3(led_32x_array_17_out_41),
    .in_4(led_32x_array_17_out_42), .in_5(led_32x_array_17_out_43), .in_6(led_32x_array_17_out_44),
    .in_7(led_32x_array_17_out_45), .in_8(led_32x_array_17_out_46), .in_9(led_32x_array_17_out_47),
    .in_10(led_32x_array_17_out_48), .in_11(led_32x_array_17_out_49), .in_12(led_32x_array_17_out_50),
    .in_13(led_32x_array_17_out_51), .in_14(led_32x_array_17_out_52), .in_15(led_32x_array_17_out_53),
    .in_16(led_32x_array_17_out_54), .in_17(led_32x_array_17_out_55), .in_18(led_32x_array_17_out_56),
    .in_19(led_32x_array_17_out_57), .in_20(led_32x_array_17_out_58), .in_21(led_32x_array_17_out_59),
    .in_22(led_32x_array_17_out_60), .in_23(led_32x_array_17_out_61), .in_24(led_32x_array_17_out_62),
    .in_25(led_32x_array_17_out_63), .in_26(led_32x_array_17_out_64), .in_27(led_32x_array_17_out_65),
    .in_28(led_32x_array_17_out_66), .in_29(led_32x_array_17_out_67), .in_30(led_32x_array_17_out_68),
    .in_31(led_32x_array_17_out_69), .in_32(led_32x_array_17_out_70), .draw(Settings[0]),
    .erase(Settings[1]), .push(Settings[2]), .OUT(out_22), .out_39(led_32x_array_18_out_39),
    .out_40(led_32x_array_18_out_40), .out_41(led_32x_array_18_out_41), .out_42(led_32x_array_18_out_42),
    .out_43(led_32x_array_18_out_43), .out_44(led_32x_array_18_out_44), .out_45(led_32x_array_18_out_45),
    .out_46(led_32x_array_18_out_46), .out_47(led_32x_array_18_out_47), .out_48(led_32x_array_18_out_48),
    .out_49(led_32x_array_18_out_49), .out_50(led_32x_array_18_out_50), .out_51(led_32x_array_18_out_51),
    .out_52(led_32x_array_18_out_52), .out_53(led_32x_array_18_out_53), .out_54(led_32x_array_18_out_54),
    .out_55(led_32x_array_18_out_55), .out_56(led_32x_array_18_out_56), .out_57(led_32x_array_18_out_57),
    .out_58(led_32x_array_18_out_58), .out_59(led_32x_array_18_out_59), .out_60(led_32x_array_18_out_60),
    .out_61(led_32x_array_18_out_61), .out_62(led_32x_array_18_out_62), .out_63(led_32x_array_18_out_63),
    .out_64(led_32x_array_18_out_64), .out_65(led_32x_array_18_out_65), .out_66(led_32x_array_18_out_66),
    .out_67(led_32x_array_18_out_67), .out_68(led_32x_array_18_out_68), .out_69(led_32x_array_18_out_69),
    .out_70(led_32x_array_18_out_70), .Select(demultiplexer_2_out17),
    .Pixel_info(led_32x_array_18_pixel_info), .clear(Settings[3]));
  buf buffer_18 (pull_resistor_1_node, led_32x_array_18_pixel_info);
  LED_32x_array led_32x_array_19 (
    .in_1(led_32x_array_18_out_39), .in_2(led_32x_array_18_out_40), .in_3(led_32x_array_18_out_41),
    .in_4(led_32x_array_18_out_42), .in_5(led_32x_array_18_out_43), .in_6(led_32x_array_18_out_44),
    .in_7(led_32x_array_18_out_45), .in_8(led_32x_array_18_out_46), .in_9(led_32x_array_18_out_47),
    .in_10(led_32x_array_18_out_48), .in_11(led_32x_array_18_out_49), .in_12(led_32x_array_18_out_50),
    .in_13(led_32x_array_18_out_51), .in_14(led_32x_array_18_out_52), .in_15(led_32x_array_18_out_53),
    .in_16(led_32x_array_18_out_54), .in_17(led_32x_array_18_out_55), .in_18(led_32x_array_18_out_56),
    .in_19(led_32x_array_18_out_57), .in_20(led_32x_array_18_out_58), .in_21(led_32x_array_18_out_59),
    .in_22(led_32x_array_18_out_60), .in_23(led_32x_array_18_out_61), .in_24(led_32x_array_18_out_62),
    .in_25(led_32x_array_18_out_63), .in_26(led_32x_array_18_out_64), .in_27(led_32x_array_18_out_65),
    .in_28(led_32x_array_18_out_66), .in_29(led_32x_array_18_out_67), .in_30(led_32x_array_18_out_68),
    .in_31(led_32x_array_18_out_69), .in_32(led_32x_array_18_out_70), .draw(Settings[0]),
    .erase(Settings[1]), .push(Settings[2]), .OUT(out_23), .out_39(led_32x_array_19_out_39),
    .out_40(led_32x_array_19_out_40), .out_41(led_32x_array_19_out_41), .out_42(led_32x_array_19_out_42),
    .out_43(led_32x_array_19_out_43), .out_44(led_32x_array_19_out_44), .out_45(led_32x_array_19_out_45),
    .out_46(led_32x_array_19_out_46), .out_47(led_32x_array_19_out_47), .out_48(led_32x_array_19_out_48),
    .out_49(led_32x_array_19_out_49), .out_50(led_32x_array_19_out_50), .out_51(led_32x_array_19_out_51),
    .out_52(led_32x_array_19_out_52), .out_53(led_32x_array_19_out_53), .out_54(led_32x_array_19_out_54),
    .out_55(led_32x_array_19_out_55), .out_56(led_32x_array_19_out_56), .out_57(led_32x_array_19_out_57),
    .out_58(led_32x_array_19_out_58), .out_59(led_32x_array_19_out_59), .out_60(led_32x_array_19_out_60),
    .out_61(led_32x_array_19_out_61), .out_62(led_32x_array_19_out_62), .out_63(led_32x_array_19_out_63),
    .out_64(led_32x_array_19_out_64), .out_65(led_32x_array_19_out_65), .out_66(led_32x_array_19_out_66),
    .out_67(led_32x_array_19_out_67), .out_68(led_32x_array_19_out_68), .out_69(led_32x_array_19_out_69),
    .out_70(led_32x_array_19_out_70), .Select(demultiplexer_2_out18),
    .Pixel_info(led_32x_array_19_pixel_info), .clear(Settings[3]));
  buf buffer_19 (pull_resistor_1_node, led_32x_array_19_pixel_info);
  LED_32x_array led_32x_array_20 (
    .in_1(led_32x_array_19_out_39), .in_2(led_32x_array_19_out_40), .in_3(led_32x_array_19_out_41),
    .in_4(led_32x_array_19_out_42), .in_5(led_32x_array_19_out_43), .in_6(led_32x_array_19_out_44),
    .in_7(led_32x_array_19_out_45), .in_8(led_32x_array_19_out_46), .in_9(led_32x_array_19_out_47),
    .in_10(led_32x_array_19_out_48), .in_11(led_32x_array_19_out_49), .in_12(led_32x_array_19_out_50),
    .in_13(led_32x_array_19_out_51), .in_14(led_32x_array_19_out_52), .in_15(led_32x_array_19_out_53),
    .in_16(led_32x_array_19_out_54), .in_17(led_32x_array_19_out_55), .in_18(led_32x_array_19_out_56),
    .in_19(led_32x_array_19_out_57), .in_20(led_32x_array_19_out_58), .in_21(led_32x_array_19_out_59),
    .in_22(led_32x_array_19_out_60), .in_23(led_32x_array_19_out_61), .in_24(led_32x_array_19_out_62),
    .in_25(led_32x_array_19_out_63), .in_26(led_32x_array_19_out_64), .in_27(led_32x_array_19_out_65),
    .in_28(led_32x_array_19_out_66), .in_29(led_32x_array_19_out_67), .in_30(led_32x_array_19_out_68),
    .in_31(led_32x_array_19_out_69), .in_32(led_32x_array_19_out_70), .draw(Settings[0]),
    .erase(Settings[1]), .push(Settings[2]), .OUT(out_24), .out_39(led_32x_array_20_out_39),
    .out_40(led_32x_array_20_out_40), .out_41(led_32x_array_20_out_41), .out_42(led_32x_array_20_out_42),
    .out_43(led_32x_array_20_out_43), .out_44(led_32x_array_20_out_44), .out_45(led_32x_array_20_out_45),
    .out_46(led_32x_array_20_out_46), .out_47(led_32x_array_20_out_47), .out_48(led_32x_array_20_out_48),
    .out_49(led_32x_array_20_out_49), .out_50(led_32x_array_20_out_50), .out_51(led_32x_array_20_out_51),
    .out_52(led_32x_array_20_out_52), .out_53(led_32x_array_20_out_53), .out_54(led_32x_array_20_out_54),
    .out_55(led_32x_array_20_out_55), .out_56(led_32x_array_20_out_56), .out_57(led_32x_array_20_out_57),
    .out_58(led_32x_array_20_out_58), .out_59(led_32x_array_20_out_59), .out_60(led_32x_array_20_out_60),
    .out_61(led_32x_array_20_out_61), .out_62(led_32x_array_20_out_62), .out_63(led_32x_array_20_out_63),
    .out_64(led_32x_array_20_out_64), .out_65(led_32x_array_20_out_65), .out_66(led_32x_array_20_out_66),
    .out_67(led_32x_array_20_out_67), .out_68(led_32x_array_20_out_68), .out_69(led_32x_array_20_out_69),
    .out_70(led_32x_array_20_out_70), .Select(demultiplexer_2_out19),
    .Pixel_info(led_32x_array_20_pixel_info), .clear(Settings[3]));
  LED_32x_array led_32x_array_21 (
    .in_1(led_32x_array_20_out_39), .in_2(led_32x_array_20_out_40), .in_3(led_32x_array_20_out_41),
    .in_4(led_32x_array_20_out_42), .in_5(led_32x_array_20_out_43), .in_6(led_32x_array_20_out_44),
    .in_7(led_32x_array_20_out_45), .in_8(led_32x_array_20_out_46), .in_9(led_32x_array_20_out_47),
    .in_10(led_32x_array_20_out_48), .in_11(led_32x_array_20_out_49), .in_12(led_32x_array_20_out_50),
    .in_13(led_32x_array_20_out_51), .in_14(led_32x_array_20_out_52), .in_15(led_32x_array_20_out_53),
    .in_16(led_32x_array_20_out_54), .in_17(led_32x_array_20_out_55), .in_18(led_32x_array_20_out_56),
    .in_19(led_32x_array_20_out_57), .in_20(led_32x_array_20_out_58), .in_21(led_32x_array_20_out_59),
    .in_22(led_32x_array_20_out_60), .in_23(led_32x_array_20_out_61), .in_24(led_32x_array_20_out_62),
    .in_25(led_32x_array_20_out_63), .in_26(led_32x_array_20_out_64), .in_27(led_32x_array_20_out_65),
    .in_28(led_32x_array_20_out_66), .in_29(led_32x_array_20_out_67), .in_30(led_32x_array_20_out_68),
    .in_31(led_32x_array_20_out_69), .in_32(led_32x_array_20_out_70), .draw(Settings[0]),
    .erase(Settings[1]), .push(Settings[2]), .OUT(out_25), .out_39(led_32x_array_21_out_39),
    .out_40(led_32x_array_21_out_40), .out_41(led_32x_array_21_out_41), .out_42(led_32x_array_21_out_42),
    .out_43(led_32x_array_21_out_43), .out_44(led_32x_array_21_out_44), .out_45(led_32x_array_21_out_45),
    .out_46(led_32x_array_21_out_46), .out_47(led_32x_array_21_out_47), .out_48(led_32x_array_21_out_48),
    .out_49(led_32x_array_21_out_49), .out_50(led_32x_array_21_out_50), .out_51(led_32x_array_21_out_51),
    .out_52(led_32x_array_21_out_52), .out_53(led_32x_array_21_out_53), .out_54(led_32x_array_21_out_54),
    .out_55(led_32x_array_21_out_55), .out_56(led_32x_array_21_out_56), .out_57(led_32x_array_21_out_57),
    .out_58(led_32x_array_21_out_58), .out_59(led_32x_array_21_out_59), .out_60(led_32x_array_21_out_60),
    .out_61(led_32x_array_21_out_61), .out_62(led_32x_array_21_out_62), .out_63(led_32x_array_21_out_63),
    .out_64(led_32x_array_21_out_64), .out_65(led_32x_array_21_out_65), .out_66(led_32x_array_21_out_66),
    .out_67(led_32x_array_21_out_67), .out_68(led_32x_array_21_out_68), .out_69(led_32x_array_21_out_69),
    .out_70(led_32x_array_21_out_70), .Select(demultiplexer_2_out20),
    .Pixel_info(led_32x_array_21_pixel_info), .clear(Settings[3]));
  buf buffer_20 (pull_resistor_1_node, led_32x_array_20_pixel_info);
  buf buffer_21 (pull_resistor_1_node, led_32x_array_21_pixel_info);
  LED_32x_array led_32x_array_22 (
    .in_1(led_32x_array_21_out_39), .in_2(led_32x_array_21_out_40), .in_3(led_32x_array_21_out_41),
    .in_4(led_32x_array_21_out_42), .in_5(led_32x_array_21_out_43), .in_6(led_32x_array_21_out_44),
    .in_7(led_32x_array_21_out_45), .in_8(led_32x_array_21_out_46), .in_9(led_32x_array_21_out_47),
    .in_10(led_32x_array_21_out_48), .in_11(led_32x_array_21_out_49), .in_12(led_32x_array_21_out_50),
    .in_13(led_32x_array_21_out_51), .in_14(led_32x_array_21_out_52), .in_15(led_32x_array_21_out_53),
    .in_16(led_32x_array_21_out_54), .in_17(led_32x_array_21_out_55), .in_18(led_32x_array_21_out_56),
    .in_19(led_32x_array_21_out_57), .in_20(led_32x_array_21_out_58), .in_21(led_32x_array_21_out_59),
    .in_22(led_32x_array_21_out_60), .in_23(led_32x_array_21_out_61), .in_24(led_32x_array_21_out_62),
    .in_25(led_32x_array_21_out_63), .in_26(led_32x_array_21_out_64), .in_27(led_32x_array_21_out_65),
    .in_28(led_32x_array_21_out_66), .in_29(led_32x_array_21_out_67), .in_30(led_32x_array_21_out_68),
    .in_31(led_32x_array_21_out_69), .in_32(led_32x_array_21_out_70), .draw(Settings[0]),
    .erase(Settings[1]), .push(Settings[2]), .OUT(out_26), .out_39(led_32x_array_22_out_39),
    .out_40(led_32x_array_22_out_40), .out_41(led_32x_array_22_out_41), .out_42(led_32x_array_22_out_42),
    .out_43(led_32x_array_22_out_43), .out_44(led_32x_array_22_out_44), .out_45(led_32x_array_22_out_45),
    .out_46(led_32x_array_22_out_46), .out_47(led_32x_array_22_out_47), .out_48(led_32x_array_22_out_48),
    .out_49(led_32x_array_22_out_49), .out_50(led_32x_array_22_out_50), .out_51(led_32x_array_22_out_51),
    .out_52(led_32x_array_22_out_52), .out_53(led_32x_array_22_out_53), .out_54(led_32x_array_22_out_54),
    .out_55(led_32x_array_22_out_55), .out_56(led_32x_array_22_out_56), .out_57(led_32x_array_22_out_57),
    .out_58(led_32x_array_22_out_58), .out_59(led_32x_array_22_out_59), .out_60(led_32x_array_22_out_60),
    .out_61(led_32x_array_22_out_61), .out_62(led_32x_array_22_out_62), .out_63(led_32x_array_22_out_63),
    .out_64(led_32x_array_22_out_64), .out_65(led_32x_array_22_out_65), .out_66(led_32x_array_22_out_66),
    .out_67(led_32x_array_22_out_67), .out_68(led_32x_array_22_out_68), .out_69(led_32x_array_22_out_69),
    .out_70(led_32x_array_22_out_70), .Select(demultiplexer_2_out21),
    .Pixel_info(led_32x_array_22_pixel_info), .clear(Settings[3]));
  buf buffer_22 (pull_resistor_1_node, led_32x_array_22_pixel_info);
  LED_32x_array led_32x_array_23 (
    .in_1(led_32x_array_22_out_39), .in_2(led_32x_array_22_out_40), .in_3(led_32x_array_22_out_41),
    .in_4(led_32x_array_22_out_42), .in_5(led_32x_array_22_out_43), .in_6(led_32x_array_22_out_44),
    .in_7(led_32x_array_22_out_45), .in_8(led_32x_array_22_out_46), .in_9(led_32x_array_22_out_47),
    .in_10(led_32x_array_22_out_48), .in_11(led_32x_array_22_out_49), .in_12(led_32x_array_22_out_50),
    .in_13(led_32x_array_22_out_51), .in_14(led_32x_array_22_out_52), .in_15(led_32x_array_22_out_53),
    .in_16(led_32x_array_22_out_54), .in_17(led_32x_array_22_out_55), .in_18(led_32x_array_22_out_56),
    .in_19(led_32x_array_22_out_57), .in_20(led_32x_array_22_out_58), .in_21(led_32x_array_22_out_59),
    .in_22(led_32x_array_22_out_60), .in_23(led_32x_array_22_out_61), .in_24(led_32x_array_22_out_62),
    .in_25(led_32x_array_22_out_63), .in_26(led_32x_array_22_out_64), .in_27(led_32x_array_22_out_65),
    .in_28(led_32x_array_22_out_66), .in_29(led_32x_array_22_out_67), .in_30(led_32x_array_22_out_68),
    .in_31(led_32x_array_22_out_69), .in_32(led_32x_array_22_out_70), .draw(Settings[0]),
    .erase(Settings[1]), .push(Settings[2]), .OUT(out_27), .out_39(led_32x_array_23_out_39),
    .out_40(led_32x_array_23_out_40), .out_41(led_32x_array_23_out_41), .out_42(led_32x_array_23_out_42),
    .out_43(led_32x_array_23_out_43), .out_44(led_32x_array_23_out_44), .out_45(led_32x_array_23_out_45),
    .out_46(led_32x_array_23_out_46), .out_47(led_32x_array_23_out_47), .out_48(led_32x_array_23_out_48),
    .out_49(led_32x_array_23_out_49), .out_50(led_32x_array_23_out_50), .out_51(led_32x_array_23_out_51),
    .out_52(led_32x_array_23_out_52), .out_53(led_32x_array_23_out_53), .out_54(led_32x_array_23_out_54),
    .out_55(led_32x_array_23_out_55), .out_56(led_32x_array_23_out_56), .out_57(led_32x_array_23_out_57),
    .out_58(led_32x_array_23_out_58), .out_59(led_32x_array_23_out_59), .out_60(led_32x_array_23_out_60),
    .out_61(led_32x_array_23_out_61), .out_62(led_32x_array_23_out_62), .out_63(led_32x_array_23_out_63),
    .out_64(led_32x_array_23_out_64), .out_65(led_32x_array_23_out_65), .out_66(led_32x_array_23_out_66),
    .out_67(led_32x_array_23_out_67), .out_68(led_32x_array_23_out_68), .out_69(led_32x_array_23_out_69),
    .out_70(led_32x_array_23_out_70), .Select(demultiplexer_2_out22),
    .Pixel_info(led_32x_array_23_pixel_info), .clear(Settings[3]));
  buf buffer_23 (pull_resistor_1_node, led_32x_array_23_pixel_info);
  LED_32x_array led_32x_array_24 (
    .in_1(led_32x_array_23_out_39), .in_2(led_32x_array_23_out_40), .in_3(led_32x_array_23_out_41),
    .in_4(led_32x_array_23_out_42), .in_5(led_32x_array_23_out_43), .in_6(led_32x_array_23_out_44),
    .in_7(led_32x_array_23_out_45), .in_8(led_32x_array_23_out_46), .in_9(led_32x_array_23_out_47),
    .in_10(led_32x_array_23_out_48), .in_11(led_32x_array_23_out_49), .in_12(led_32x_array_23_out_50),
    .in_13(led_32x_array_23_out_51), .in_14(led_32x_array_23_out_52), .in_15(led_32x_array_23_out_53),
    .in_16(led_32x_array_23_out_54), .in_17(led_32x_array_23_out_55), .in_18(led_32x_array_23_out_56),
    .in_19(led_32x_array_23_out_57), .in_20(led_32x_array_23_out_58), .in_21(led_32x_array_23_out_59),
    .in_22(led_32x_array_23_out_60), .in_23(led_32x_array_23_out_61), .in_24(led_32x_array_23_out_62),
    .in_25(led_32x_array_23_out_63), .in_26(led_32x_array_23_out_64), .in_27(led_32x_array_23_out_65),
    .in_28(led_32x_array_23_out_66), .in_29(led_32x_array_23_out_67), .in_30(led_32x_array_23_out_68),
    .in_31(led_32x_array_23_out_69), .in_32(led_32x_array_23_out_70), .draw(Settings[0]),
    .erase(Settings[1]), .push(Settings[2]), .OUT(out_28), .out_39(led_32x_array_24_out_39),
    .out_40(led_32x_array_24_out_40), .out_41(led_32x_array_24_out_41), .out_42(led_32x_array_24_out_42),
    .out_43(led_32x_array_24_out_43), .out_44(led_32x_array_24_out_44), .out_45(led_32x_array_24_out_45),
    .out_46(led_32x_array_24_out_46), .out_47(led_32x_array_24_out_47), .out_48(led_32x_array_24_out_48),
    .out_49(led_32x_array_24_out_49), .out_50(led_32x_array_24_out_50), .out_51(led_32x_array_24_out_51),
    .out_52(led_32x_array_24_out_52), .out_53(led_32x_array_24_out_53), .out_54(led_32x_array_24_out_54),
    .out_55(led_32x_array_24_out_55), .out_56(led_32x_array_24_out_56), .out_57(led_32x_array_24_out_57),
    .out_58(led_32x_array_24_out_58), .out_59(led_32x_array_24_out_59), .out_60(led_32x_array_24_out_60),
    .out_61(led_32x_array_24_out_61), .out_62(led_32x_array_24_out_62), .out_63(led_32x_array_24_out_63),
    .out_64(led_32x_array_24_out_64), .out_65(led_32x_array_24_out_65), .out_66(led_32x_array_24_out_66),
    .out_67(led_32x_array_24_out_67), .out_68(led_32x_array_24_out_68), .out_69(led_32x_array_24_out_69),
    .out_70(led_32x_array_24_out_70), .Select(demultiplexer_2_out23),
    .Pixel_info(led_32x_array_24_pixel_info), .clear(Settings[3]));
  LED_32x_array led_32x_array_25 (
    .in_1(led_32x_array_24_out_39), .in_2(led_32x_array_24_out_40), .in_3(led_32x_array_24_out_41),
    .in_4(led_32x_array_24_out_42), .in_5(led_32x_array_24_out_43), .in_6(led_32x_array_24_out_44),
    .in_7(led_32x_array_24_out_45), .in_8(led_32x_array_24_out_46), .in_9(led_32x_array_24_out_47),
    .in_10(led_32x_array_24_out_48), .in_11(led_32x_array_24_out_49), .in_12(led_32x_array_24_out_50),
    .in_13(led_32x_array_24_out_51), .in_14(led_32x_array_24_out_52), .in_15(led_32x_array_24_out_53),
    .in_16(led_32x_array_24_out_54), .in_17(led_32x_array_24_out_55), .in_18(led_32x_array_24_out_56),
    .in_19(led_32x_array_24_out_57), .in_20(led_32x_array_24_out_58), .in_21(led_32x_array_24_out_59),
    .in_22(led_32x_array_24_out_60), .in_23(led_32x_array_24_out_61), .in_24(led_32x_array_24_out_62),
    .in_25(led_32x_array_24_out_63), .in_26(led_32x_array_24_out_64), .in_27(led_32x_array_24_out_65),
    .in_28(led_32x_array_24_out_66), .in_29(led_32x_array_24_out_67), .in_30(led_32x_array_24_out_68),
    .in_31(led_32x_array_24_out_69), .in_32(led_32x_array_24_out_70), .draw(Settings[0]),
    .erase(Settings[1]), .push(Settings[2]), .OUT(out_29), .out_39(led_32x_array_25_out_39),
    .out_40(led_32x_array_25_out_40), .out_41(led_32x_array_25_out_41), .out_42(led_32x_array_25_out_42),
    .out_43(led_32x_array_25_out_43), .out_44(led_32x_array_25_out_44), .out_45(led_32x_array_25_out_45),
    .out_46(led_32x_array_25_out_46), .out_47(led_32x_array_25_out_47), .out_48(led_32x_array_25_out_48),
    .out_49(led_32x_array_25_out_49), .out_50(led_32x_array_25_out_50), .out_51(led_32x_array_25_out_51),
    .out_52(led_32x_array_25_out_52), .out_53(led_32x_array_25_out_53), .out_54(led_32x_array_25_out_54),
    .out_55(led_32x_array_25_out_55), .out_56(led_32x_array_25_out_56), .out_57(led_32x_array_25_out_57),
    .out_58(led_32x_array_25_out_58), .out_59(led_32x_array_25_out_59), .out_60(led_32x_array_25_out_60),
    .out_61(led_32x_array_25_out_61), .out_62(led_32x_array_25_out_62), .out_63(led_32x_array_25_out_63),
    .out_64(led_32x_array_25_out_64), .out_65(led_32x_array_25_out_65), .out_66(led_32x_array_25_out_66),
    .out_67(led_32x_array_25_out_67), .out_68(led_32x_array_25_out_68), .out_69(led_32x_array_25_out_69),
    .out_70(led_32x_array_25_out_70), .Select(demultiplexer_2_out24),
    .Pixel_info(led_32x_array_25_pixel_info), .clear(Settings[3]));
  buf buffer_24 (pull_resistor_1_node, led_32x_array_24_pixel_info);
  buf buffer_25 (pull_resistor_1_node, led_32x_array_25_pixel_info);
  LED_32x_array led_32x_array_26 (
    .in_1(led_32x_array_25_out_39), .in_2(led_32x_array_25_out_40), .in_3(led_32x_array_25_out_41),
    .in_4(led_32x_array_25_out_42), .in_5(led_32x_array_25_out_43), .in_6(led_32x_array_25_out_44),
    .in_7(led_32x_array_25_out_45), .in_8(led_32x_array_25_out_46), .in_9(led_32x_array_25_out_47),
    .in_10(led_32x_array_25_out_48), .in_11(led_32x_array_25_out_49), .in_12(led_32x_array_25_out_50),
    .in_13(led_32x_array_25_out_51), .in_14(led_32x_array_25_out_52), .in_15(led_32x_array_25_out_53),
    .in_16(led_32x_array_25_out_54), .in_17(led_32x_array_25_out_55), .in_18(led_32x_array_25_out_56),
    .in_19(led_32x_array_25_out_57), .in_20(led_32x_array_25_out_58), .in_21(led_32x_array_25_out_59),
    .in_22(led_32x_array_25_out_60), .in_23(led_32x_array_25_out_61), .in_24(led_32x_array_25_out_62),
    .in_25(led_32x_array_25_out_63), .in_26(led_32x_array_25_out_64), .in_27(led_32x_array_25_out_65),
    .in_28(led_32x_array_25_out_66), .in_29(led_32x_array_25_out_67), .in_30(led_32x_array_25_out_68),
    .in_31(led_32x_array_25_out_69), .in_32(led_32x_array_25_out_70), .draw(Settings[0]),
    .erase(Settings[1]), .push(Settings[2]), .OUT(out_30), .out_39(led_32x_array_26_out_39),
    .out_40(led_32x_array_26_out_40), .out_41(led_32x_array_26_out_41), .out_42(led_32x_array_26_out_42),
    .out_43(led_32x_array_26_out_43), .out_44(led_32x_array_26_out_44), .out_45(led_32x_array_26_out_45),
    .out_46(led_32x_array_26_out_46), .out_47(led_32x_array_26_out_47), .out_48(led_32x_array_26_out_48),
    .out_49(led_32x_array_26_out_49), .out_50(led_32x_array_26_out_50), .out_51(led_32x_array_26_out_51),
    .out_52(led_32x_array_26_out_52), .out_53(led_32x_array_26_out_53), .out_54(led_32x_array_26_out_54),
    .out_55(led_32x_array_26_out_55), .out_56(led_32x_array_26_out_56), .out_57(led_32x_array_26_out_57),
    .out_58(led_32x_array_26_out_58), .out_59(led_32x_array_26_out_59), .out_60(led_32x_array_26_out_60),
    .out_61(led_32x_array_26_out_61), .out_62(led_32x_array_26_out_62), .out_63(led_32x_array_26_out_63),
    .out_64(led_32x_array_26_out_64), .out_65(led_32x_array_26_out_65), .out_66(led_32x_array_26_out_66),
    .out_67(led_32x_array_26_out_67), .out_68(led_32x_array_26_out_68), .out_69(led_32x_array_26_out_69),
    .out_70(led_32x_array_26_out_70), .Select(demultiplexer_2_out25),
    .Pixel_info(led_32x_array_26_pixel_info), .clear(Settings[3]));
  buf buffer_26 (pull_resistor_1_node, led_32x_array_26_pixel_info);
  LED_32x_array led_32x_array_27 (
    .in_1(led_32x_array_26_out_39), .in_2(led_32x_array_26_out_40), .in_3(led_32x_array_26_out_41),
    .in_4(led_32x_array_26_out_42), .in_5(led_32x_array_26_out_43), .in_6(led_32x_array_26_out_44),
    .in_7(led_32x_array_26_out_45), .in_8(led_32x_array_26_out_46), .in_9(led_32x_array_26_out_47),
    .in_10(led_32x_array_26_out_48), .in_11(led_32x_array_26_out_49), .in_12(led_32x_array_26_out_50),
    .in_13(led_32x_array_26_out_51), .in_14(led_32x_array_26_out_52), .in_15(led_32x_array_26_out_53),
    .in_16(led_32x_array_26_out_54), .in_17(led_32x_array_26_out_55), .in_18(led_32x_array_26_out_56),
    .in_19(led_32x_array_26_out_57), .in_20(led_32x_array_26_out_58), .in_21(led_32x_array_26_out_59),
    .in_22(led_32x_array_26_out_60), .in_23(led_32x_array_26_out_61), .in_24(led_32x_array_26_out_62),
    .in_25(led_32x_array_26_out_63), .in_26(led_32x_array_26_out_64), .in_27(led_32x_array_26_out_65),
    .in_28(led_32x_array_26_out_66), .in_29(led_32x_array_26_out_67), .in_30(led_32x_array_26_out_68),
    .in_31(led_32x_array_26_out_69), .in_32(led_32x_array_26_out_70), .draw(Settings[0]),
    .erase(Settings[1]), .push(Settings[2]), .OUT(out_31), .out_39(led_32x_array_27_out_39),
    .out_40(led_32x_array_27_out_40), .out_41(led_32x_array_27_out_41), .out_42(led_32x_array_27_out_42),
    .out_43(led_32x_array_27_out_43), .out_44(led_32x_array_27_out_44), .out_45(led_32x_array_27_out_45),
    .out_46(led_32x_array_27_out_46), .out_47(led_32x_array_27_out_47), .out_48(led_32x_array_27_out_48),
    .out_49(led_32x_array_27_out_49), .out_50(led_32x_array_27_out_50), .out_51(led_32x_array_27_out_51),
    .out_52(led_32x_array_27_out_52), .out_53(led_32x_array_27_out_53), .out_54(led_32x_array_27_out_54),
    .out_55(led_32x_array_27_out_55), .out_56(led_32x_array_27_out_56), .out_57(led_32x_array_27_out_57),
    .out_58(led_32x_array_27_out_58), .out_59(led_32x_array_27_out_59), .out_60(led_32x_array_27_out_60),
    .out_61(led_32x_array_27_out_61), .out_62(led_32x_array_27_out_62), .out_63(led_32x_array_27_out_63),
    .out_64(led_32x_array_27_out_64), .out_65(led_32x_array_27_out_65), .out_66(led_32x_array_27_out_66),
    .out_67(led_32x_array_27_out_67), .out_68(led_32x_array_27_out_68), .out_69(led_32x_array_27_out_69),
    .out_70(led_32x_array_27_out_70), .Select(demultiplexer_2_out26),
    .Pixel_info(led_32x_array_27_pixel_info), .clear(Settings[3]));
  buf buffer_27 (pull_resistor_1_node, led_32x_array_27_pixel_info);
  LED_32x_array led_32x_array_28 (
    .in_1(led_32x_array_27_out_39), .in_2(led_32x_array_27_out_40), .in_3(led_32x_array_27_out_41),
    .in_4(led_32x_array_27_out_42), .in_5(led_32x_array_27_out_43), .in_6(led_32x_array_27_out_44),
    .in_7(led_32x_array_27_out_45), .in_8(led_32x_array_27_out_46), .in_9(led_32x_array_27_out_47),
    .in_10(led_32x_array_27_out_48), .in_11(led_32x_array_27_out_49), .in_12(led_32x_array_27_out_50),
    .in_13(led_32x_array_27_out_51), .in_14(led_32x_array_27_out_52), .in_15(led_32x_array_27_out_53),
    .in_16(led_32x_array_27_out_54), .in_17(led_32x_array_27_out_55), .in_18(led_32x_array_27_out_56),
    .in_19(led_32x_array_27_out_57), .in_20(led_32x_array_27_out_58), .in_21(led_32x_array_27_out_59),
    .in_22(led_32x_array_27_out_60), .in_23(led_32x_array_27_out_61), .in_24(led_32x_array_27_out_62),
    .in_25(led_32x_array_27_out_63), .in_26(led_32x_array_27_out_64), .in_27(led_32x_array_27_out_65),
    .in_28(led_32x_array_27_out_66), .in_29(led_32x_array_27_out_67), .in_30(led_32x_array_27_out_68),
    .in_31(led_32x_array_27_out_69), .in_32(led_32x_array_27_out_70), .draw(Settings[0]),
    .erase(Settings[1]), .push(Settings[2]), .OUT(out_32), .out_39(led_32x_array_28_out_39),
    .out_40(led_32x_array_28_out_40), .out_41(led_32x_array_28_out_41), .out_42(led_32x_array_28_out_42),
    .out_43(led_32x_array_28_out_43), .out_44(led_32x_array_28_out_44), .out_45(led_32x_array_28_out_45),
    .out_46(led_32x_array_28_out_46), .out_47(led_32x_array_28_out_47), .out_48(led_32x_array_28_out_48),
    .out_49(led_32x_array_28_out_49), .out_50(led_32x_array_28_out_50), .out_51(led_32x_array_28_out_51),
    .out_52(led_32x_array_28_out_52), .out_53(led_32x_array_28_out_53), .out_54(led_32x_array_28_out_54),
    .out_55(led_32x_array_28_out_55), .out_56(led_32x_array_28_out_56), .out_57(led_32x_array_28_out_57),
    .out_58(led_32x_array_28_out_58), .out_59(led_32x_array_28_out_59), .out_60(led_32x_array_28_out_60),
    .out_61(led_32x_array_28_out_61), .out_62(led_32x_array_28_out_62), .out_63(led_32x_array_28_out_63),
    .out_64(led_32x_array_28_out_64), .out_65(led_32x_array_28_out_65), .out_66(led_32x_array_28_out_66),
    .out_67(led_32x_array_28_out_67), .out_68(led_32x_array_28_out_68), .out_69(led_32x_array_28_out_69),
    .out_70(led_32x_array_28_out_70), .Select(demultiplexer_2_out27),
    .Pixel_info(led_32x_array_28_pixel_info), .clear(Settings[3]));
  LED_32x_array led_32x_array_29 (
    .in_1(led_32x_array_28_out_39), .in_2(led_32x_array_28_out_40), .in_3(led_32x_array_28_out_41),
    .in_4(led_32x_array_28_out_42), .in_5(led_32x_array_28_out_43), .in_6(led_32x_array_28_out_44),
    .in_7(led_32x_array_28_out_45), .in_8(led_32x_array_28_out_46), .in_9(led_32x_array_28_out_47),
    .in_10(led_32x_array_28_out_48), .in_11(led_32x_array_28_out_49), .in_12(led_32x_array_28_out_50),
    .in_13(led_32x_array_28_out_51), .in_14(led_32x_array_28_out_52), .in_15(led_32x_array_28_out_53),
    .in_16(led_32x_array_28_out_54), .in_17(led_32x_array_28_out_55), .in_18(led_32x_array_28_out_56),
    .in_19(led_32x_array_28_out_57), .in_20(led_32x_array_28_out_58), .in_21(led_32x_array_28_out_59),
    .in_22(led_32x_array_28_out_60), .in_23(led_32x_array_28_out_61), .in_24(led_32x_array_28_out_62),
    .in_25(led_32x_array_28_out_63), .in_26(led_32x_array_28_out_64), .in_27(led_32x_array_28_out_65),
    .in_28(led_32x_array_28_out_66), .in_29(led_32x_array_28_out_67), .in_30(led_32x_array_28_out_68),
    .in_31(led_32x_array_28_out_69), .in_32(led_32x_array_28_out_70), .draw(Settings[0]),
    .erase(Settings[1]), .push(Settings[2]), .OUT(out_33), .out_39(led_32x_array_29_out_39),
    .out_40(led_32x_array_29_out_40), .out_41(led_32x_array_29_out_41), .out_42(led_32x_array_29_out_42),
    .out_43(led_32x_array_29_out_43), .out_44(led_32x_array_29_out_44), .out_45(led_32x_array_29_out_45),
    .out_46(led_32x_array_29_out_46), .out_47(led_32x_array_29_out_47), .out_48(led_32x_array_29_out_48),
    .out_49(led_32x_array_29_out_49), .out_50(led_32x_array_29_out_50), .out_51(led_32x_array_29_out_51),
    .out_52(led_32x_array_29_out_52), .out_53(led_32x_array_29_out_53), .out_54(led_32x_array_29_out_54),
    .out_55(led_32x_array_29_out_55), .out_56(led_32x_array_29_out_56), .out_57(led_32x_array_29_out_57),
    .out_58(led_32x_array_29_out_58), .out_59(led_32x_array_29_out_59), .out_60(led_32x_array_29_out_60),
    .out_61(led_32x_array_29_out_61), .out_62(led_32x_array_29_out_62), .out_63(led_32x_array_29_out_63),
    .out_64(led_32x_array_29_out_64), .out_65(led_32x_array_29_out_65), .out_66(led_32x_array_29_out_66),
    .out_67(led_32x_array_29_out_67), .out_68(led_32x_array_29_out_68), .out_69(led_32x_array_29_out_69),
    .out_70(led_32x_array_29_out_70), .Select(demultiplexer_2_out28),
    .Pixel_info(led_32x_array_29_pixel_info), .clear(Settings[3]));
  buf buffer_28 (pull_resistor_1_node, led_32x_array_28_pixel_info);
  buf buffer_29 (pull_resistor_1_node, led_32x_array_29_pixel_info);
  LED_32x_array led_32x_array_30 (
    .in_1(led_32x_array_29_out_39), .in_2(led_32x_array_29_out_40), .in_3(led_32x_array_29_out_41),
    .in_4(led_32x_array_29_out_42), .in_5(led_32x_array_29_out_43), .in_6(led_32x_array_29_out_44),
    .in_7(led_32x_array_29_out_45), .in_8(led_32x_array_29_out_46), .in_9(led_32x_array_29_out_47),
    .in_10(led_32x_array_29_out_48), .in_11(led_32x_array_29_out_49), .in_12(led_32x_array_29_out_50),
    .in_13(led_32x_array_29_out_51), .in_14(led_32x_array_29_out_52), .in_15(led_32x_array_29_out_53),
    .in_16(led_32x_array_29_out_54), .in_17(led_32x_array_29_out_55), .in_18(led_32x_array_29_out_56),
    .in_19(led_32x_array_29_out_57), .in_20(led_32x_array_29_out_58), .in_21(led_32x_array_29_out_59),
    .in_22(led_32x_array_29_out_60), .in_23(led_32x_array_29_out_61), .in_24(led_32x_array_29_out_62),
    .in_25(led_32x_array_29_out_63), .in_26(led_32x_array_29_out_64), .in_27(led_32x_array_29_out_65),
    .in_28(led_32x_array_29_out_66), .in_29(led_32x_array_29_out_67), .in_30(led_32x_array_29_out_68),
    .in_31(led_32x_array_29_out_69), .in_32(led_32x_array_29_out_70), .draw(Settings[0]),
    .erase(Settings[1]), .push(Settings[2]), .OUT(out_34), .out_39(led_32x_array_30_out_39),
    .out_40(led_32x_array_30_out_40), .out_41(led_32x_array_30_out_41), .out_42(led_32x_array_30_out_42),
    .out_43(led_32x_array_30_out_43), .out_44(led_32x_array_30_out_44), .out_45(led_32x_array_30_out_45),
    .out_46(led_32x_array_30_out_46), .out_47(led_32x_array_30_out_47), .out_48(led_32x_array_30_out_48),
    .out_49(led_32x_array_30_out_49), .out_50(led_32x_array_30_out_50), .out_51(led_32x_array_30_out_51),
    .out_52(led_32x_array_30_out_52), .out_53(led_32x_array_30_out_53), .out_54(led_32x_array_30_out_54),
    .out_55(led_32x_array_30_out_55), .out_56(led_32x_array_30_out_56), .out_57(led_32x_array_30_out_57),
    .out_58(led_32x_array_30_out_58), .out_59(led_32x_array_30_out_59), .out_60(led_32x_array_30_out_60),
    .out_61(led_32x_array_30_out_61), .out_62(led_32x_array_30_out_62), .out_63(led_32x_array_30_out_63),
    .out_64(led_32x_array_30_out_64), .out_65(led_32x_array_30_out_65), .out_66(led_32x_array_30_out_66),
    .out_67(led_32x_array_30_out_67), .out_68(led_32x_array_30_out_68), .out_69(led_32x_array_30_out_69),
    .out_70(led_32x_array_30_out_70), .Select(demultiplexer_2_out29),
    .Pixel_info(led_32x_array_30_pixel_info), .clear(Settings[3]));
  buf buffer_30 (pull_resistor_1_node, led_32x_array_30_pixel_info);
  LED_32x_array led_32x_array_31 (
    .in_1(led_32x_array_30_out_39), .in_2(led_32x_array_30_out_40), .in_3(led_32x_array_30_out_41),
    .in_4(led_32x_array_30_out_42), .in_5(led_32x_array_30_out_43), .in_6(led_32x_array_30_out_44),
    .in_7(led_32x_array_30_out_45), .in_8(led_32x_array_30_out_46), .in_9(led_32x_array_30_out_47),
    .in_10(led_32x_array_30_out_48), .in_11(led_32x_array_30_out_49), .in_12(led_32x_array_30_out_50),
    .in_13(led_32x_array_30_out_51), .in_14(led_32x_array_30_out_52), .in_15(led_32x_array_30_out_53),
    .in_16(led_32x_array_30_out_54), .in_17(led_32x_array_30_out_55), .in_18(led_32x_array_30_out_56),
    .in_19(led_32x_array_30_out_57), .in_20(led_32x_array_30_out_58), .in_21(led_32x_array_30_out_59),
    .in_22(led_32x_array_30_out_60), .in_23(led_32x_array_30_out_61), .in_24(led_32x_array_30_out_62),
    .in_25(led_32x_array_30_out_63), .in_26(led_32x_array_30_out_64), .in_27(led_32x_array_30_out_65),
    .in_28(led_32x_array_30_out_66), .in_29(led_32x_array_30_out_67), .in_30(led_32x_array_30_out_68),
    .in_31(led_32x_array_30_out_69), .in_32(led_32x_array_30_out_70), .draw(Settings[0]),
    .erase(Settings[1]), .push(Settings[2]), .OUT(out_35), .out_39(led_32x_array_31_out_39),
    .out_40(led_32x_array_31_out_40), .out_41(led_32x_array_31_out_41), .out_42(led_32x_array_31_out_42),
    .out_43(led_32x_array_31_out_43), .out_44(led_32x_array_31_out_44), .out_45(led_32x_array_31_out_45),
    .out_46(led_32x_array_31_out_46), .out_47(led_32x_array_31_out_47), .out_48(led_32x_array_31_out_48),
    .out_49(led_32x_array_31_out_49), .out_50(led_32x_array_31_out_50), .out_51(led_32x_array_31_out_51),
    .out_52(led_32x_array_31_out_52), .out_53(led_32x_array_31_out_53), .out_54(led_32x_array_31_out_54),
    .out_55(led_32x_array_31_out_55), .out_56(led_32x_array_31_out_56), .out_57(led_32x_array_31_out_57),
    .out_58(led_32x_array_31_out_58), .out_59(led_32x_array_31_out_59), .out_60(led_32x_array_31_out_60),
    .out_61(led_32x_array_31_out_61), .out_62(led_32x_array_31_out_62), .out_63(led_32x_array_31_out_63),
    .out_64(led_32x_array_31_out_64), .out_65(led_32x_array_31_out_65), .out_66(led_32x_array_31_out_66),
    .out_67(led_32x_array_31_out_67), .out_68(led_32x_array_31_out_68), .out_69(led_32x_array_31_out_69),
    .out_70(led_32x_array_31_out_70), .Select(demultiplexer_2_out30),
    .Pixel_info(led_32x_array_31_pixel_info), .clear(Settings[3]));
  buf buffer_31 (pull_resistor_1_node, led_32x_array_31_pixel_info);
  LED_32x_array led_32x_array_32 (
    .in_1(led_32x_array_31_out_39), .in_2(led_32x_array_31_out_40), .in_3(led_32x_array_31_out_41),
    .in_4(led_32x_array_31_out_42), .in_5(led_32x_array_31_out_43), .in_6(led_32x_array_31_out_44),
    .in_7(led_32x_array_31_out_45), .in_8(led_32x_array_31_out_46), .in_9(led_32x_array_31_out_47),
    .in_10(led_32x_array_31_out_48), .in_11(led_32x_array_31_out_49), .in_12(led_32x_array_31_out_50),
    .in_13(led_32x_array_31_out_51), .in_14(led_32x_array_31_out_52), .in_15(led_32x_array_31_out_53),
    .in_16(led_32x_array_31_out_54), .in_17(led_32x_array_31_out_55), .in_18(led_32x_array_31_out_56),
    .in_19(led_32x_array_31_out_57), .in_20(led_32x_array_31_out_58), .in_21(led_32x_array_31_out_59),
    .in_22(led_32x_array_31_out_60), .in_23(led_32x_array_31_out_61), .in_24(led_32x_array_31_out_62),
    .in_25(led_32x_array_31_out_63), .in_26(led_32x_array_31_out_64), .in_27(led_32x_array_31_out_65),
    .in_28(led_32x_array_31_out_66), .in_29(led_32x_array_31_out_67), .in_30(led_32x_array_31_out_68),
    .in_31(led_32x_array_31_out_69), .in_32(led_32x_array_31_out_70), .draw(Settings[0]),
    .erase(Settings[1]), .push(Settings[2]), .OUT(out_36), .out_39(led_32x_array_32_out_39),
    .out_40(led_32x_array_32_out_40), .out_41(led_32x_array_32_out_41), .out_42(led_32x_array_32_out_42),
    .out_43(led_32x_array_32_out_43), .out_44(led_32x_array_32_out_44), .out_45(led_32x_array_32_out_45),
    .out_46(led_32x_array_32_out_46), .out_47(led_32x_array_32_out_47), .out_48(led_32x_array_32_out_48),
    .out_49(led_32x_array_32_out_49), .out_50(led_32x_array_32_out_50), .out_51(led_32x_array_32_out_51),
    .out_52(led_32x_array_32_out_52), .out_53(led_32x_array_32_out_53), .out_54(led_32x_array_32_out_54),
    .out_55(led_32x_array_32_out_55), .out_56(led_32x_array_32_out_56), .out_57(led_32x_array_32_out_57),
    .out_58(led_32x_array_32_out_58), .out_59(led_32x_array_32_out_59), .out_60(led_32x_array_32_out_60),
    .out_61(led_32x_array_32_out_61), .out_62(led_32x_array_32_out_62), .out_63(led_32x_array_32_out_63),
    .out_64(led_32x_array_32_out_64), .out_65(led_32x_array_32_out_65), .out_66(led_32x_array_32_out_66),
    .out_67(led_32x_array_32_out_67), .out_68(led_32x_array_32_out_68), .out_69(led_32x_array_32_out_69),
    .out_70(led_32x_array_32_out_70), .Select(demultiplexer_2_out31),
    .Pixel_info(led_32x_array_32_pixel_info), .clear(Settings[3]));
  buf buffer_32 (pull_resistor_1_node, led_32x_array_32_pixel_info);

  // Notes on the sheet:
  //   buffer_1 drives only 1 and floats otherwise
  //   buffer_2 drives only 1 and floats otherwise
  //   buffer_3 drives only 1 and floats otherwise
  //   buffer_4 drives only 1 and floats otherwise
  //   buffer_5 drives only 1 and floats otherwise
  //   buffer_6 drives only 1 and floats otherwise
  //   buffer_7 drives only 1 and floats otherwise
  //   buffer_8 drives only 1 and floats otherwise
  //   buffer_9 drives only 1 and floats otherwise
  //   buffer_10 drives only 1 and floats otherwise
  //   buffer_11 drives only 1 and floats otherwise
  //   buffer_12 drives only 1 and floats otherwise
  //   buffer_13 drives only 1 and floats otherwise
  //   buffer_14 drives only 1 and floats otherwise
  //   buffer_15 drives only 1 and floats otherwise
  //   buffer_16 drives only 1 and floats otherwise
  //   buffer_17 drives only 1 and floats otherwise
  //   buffer_18 drives only 1 and floats otherwise
  //   buffer_19 drives only 1 and floats otherwise
  //   buffer_20 drives only 1 and floats otherwise
  //   buffer_21 drives only 1 and floats otherwise
  //   buffer_22 drives only 1 and floats otherwise
  //   buffer_23 drives only 1 and floats otherwise
  //   buffer_24 drives only 1 and floats otherwise
  //   buffer_25 drives only 1 and floats otherwise
  //   buffer_26 drives only 1 and floats otherwise
  //   buffer_27 drives only 1 and floats otherwise
  //   buffer_28 drives only 1 and floats otherwise
  //   buffer_29 drives only 1 and floats otherwise
  //   buffer_30 drives only 1 and floats otherwise
  //   buffer_31 drives only 1 and floats otherwise
  //   buffer_32 drives only 1 and floats otherwise
endmodule

module LED_32x_array (
  input  in_1,
  input  in_2,
  input  in_3,
  input  in_4,
  input  in_5,
  input  in_6,
  input  in_7,
  input  in_8,
  input  in_9,
  input  in_10,
  input  in_11,
  input  in_12,
  input  in_13,
  input  in_14,
  input  in_15,
  input  in_16,
  input  in_17,
  input  in_18,
  input  in_19,
  input  in_20,
  input  in_21,
  input  in_22,
  input  in_23,
  input  in_24,
  input  in_25,
  input  in_26,
  input  in_27,
  input  in_28,
  input  in_29,
  input  in_30,
  input  in_31,
  input  in_32,
  input  Select,
  input  draw,
  input  erase,
  input  push,
  input  clear,
  output [31:0] OUT,
  output out_39,
  output out_40,
  output out_41,
  output out_42,
  output out_43,
  output out_44,
  output out_45,
  output out_46,
  output out_47,
  output out_48,
  output out_49,
  output out_50,
  output out_51,
  output out_52,
  output out_53,
  output out_54,
  output out_55,
  output out_56,
  output out_57,
  output out_58,
  output out_59,
  output out_60,
  output out_61,
  output out_62,
  output out_63,
  output out_64,
  output out_65,
  output out_66,
  output out_67,
  output out_68,
  output out_69,
  output out_70,
  output Pixel_info
);

  wire and_1_out, and_2_out, and_3_out, and_4_out, and_5_out, and_6_out, and_7_out, and_8_out, and_9_out,
       and_10_out, and_11_out, and_12_out, and_13_out, and_14_out, and_15_out, and_16_out, and_17_out,
       and_18_out, and_19_out, and_20_out, and_21_out, and_22_out, and_23_out, and_24_out, and_25_out,
       and_26_out, and_27_out, and_28_out, and_29_out, and_30_out, and_31_out, and_32_out, and_33_out,
       and_34_out, and_35_out, and_36_out, and_37_out, and_38_out, and_39_out, and_40_out, and_41_out,
       and_42_out, and_43_out, and_44_out, and_45_out, and_46_out, and_47_out, and_48_out, and_49_out,
       and_50_out, and_51_out, and_52_out, and_53_out, and_54_out, and_55_out, and_56_out, and_57_out,
       and_58_out, and_59_out, and_60_out, and_61_out, and_62_out, and_63_out, and_64_out, buffer_1_out,
       s_r_ff_1_q, s_r_ff_2_q, s_r_ff_3_q, s_r_ff_4_q, s_r_ff_5_q, s_r_ff_6_q, s_r_ff_7_q, s_r_ff_8_q,
       s_r_ff_9_q, s_r_ff_10_q, s_r_ff_11_q, s_r_ff_12_q, s_r_ff_13_q, s_r_ff_14_q, s_r_ff_15_q, s_r_ff_16_q,
       s_r_ff_17_q, s_r_ff_18_q, s_r_ff_19_q, s_r_ff_20_q, s_r_ff_21_q, s_r_ff_22_q, s_r_ff_23_q,
       s_r_ff_24_q, s_r_ff_25_q, s_r_ff_26_q, s_r_ff_27_q, s_r_ff_28_q, s_r_ff_29_q, s_r_ff_30_q,
       s_r_ff_31_q, s_r_ff_32_q;

  and and_1 (and_1_out, Select, in_1);
  and and_2 (and_2_out, Select, in_2);
  and and_3 (and_3_out, Select, in_3);
  and and_4 (and_4_out, Select, in_4);
  and and_5 (and_5_out, Select, in_5);
  and and_6 (and_6_out, Select, in_6);
  and and_7 (and_7_out, Select, in_7);
  and and_8 (and_8_out, Select, in_8);
  and and_9 (and_9_out, Select, in_9);
  and and_10 (and_10_out, Select, in_10);
  and and_11 (and_11_out, Select, in_11);
  and and_12 (and_12_out, Select, in_12);
  and and_13 (and_13_out, Select, in_13);
  and and_14 (and_14_out, Select, in_14);
  and and_15 (and_15_out, Select, in_15);
  and and_16 (and_16_out, Select, in_16);
  and and_17 (and_17_out, Select, in_17);
  and and_18 (and_18_out, Select, in_18);
  and and_19 (and_19_out, Select, in_19);
  and and_20 (and_20_out, Select, in_20);
  and and_21 (and_21_out, Select, in_21);
  and and_22 (and_22_out, Select, in_22);
  and and_23 (and_23_out, Select, in_23);
  and and_24 (and_24_out, Select, in_24);
  and and_25 (and_25_out, Select, in_25);
  and and_26 (and_26_out, Select, in_26);
  and and_27 (and_27_out, Select, in_27);
  and and_28 (and_28_out, Select, in_28);
  and and_29 (and_29_out, Select, in_29);
  and and_30 (and_30_out, Select, in_30);
  and and_31 (and_31_out, Select, in_31);
  and and_32 (and_32_out, Select, in_32);
  S_R_Flip_Flop s_r_ff_1 (.S(draw), .clk(and_1_out), .R(erase), .Q(s_r_ff_1_q), .reset(clear));  // open: Qn, preset, en
  Register #(.width(1)) register_1 (.D(s_r_ff_1_q), .Q(OUT[0]), .clk(push));  // open: en, clr
  S_R_Flip_Flop s_r_ff_2 (.S(draw), .clk(and_2_out), .R(erase), .Q(s_r_ff_2_q), .reset(clear));  // open: Qn, preset, en
  Register #(.width(1)) register_2 (.D(s_r_ff_2_q), .Q(OUT[1]), .clk(push));  // open: en, clr
  S_R_Flip_Flop s_r_ff_3 (.S(draw), .clk(and_3_out), .R(erase), .Q(s_r_ff_3_q), .reset(clear));  // open: Qn, preset, en
  Register #(.width(1)) register_3 (.D(s_r_ff_3_q), .Q(OUT[2]), .clk(push));  // open: en, clr
  S_R_Flip_Flop s_r_ff_4 (.S(draw), .clk(and_4_out), .R(erase), .Q(s_r_ff_4_q), .reset(clear));  // open: Qn, preset, en
  Register #(.width(1)) register_4 (.D(s_r_ff_4_q), .Q(OUT[3]), .clk(push));  // open: en, clr
  S_R_Flip_Flop s_r_ff_5 (.S(draw), .clk(and_5_out), .R(erase), .Q(s_r_ff_5_q), .reset(clear));  // open: Qn, preset, en
  Register #(.width(1)) register_5 (.D(s_r_ff_5_q), .Q(OUT[4]), .clk(push));  // open: en, clr
  S_R_Flip_Flop s_r_ff_6 (.S(draw), .clk(and_6_out), .R(erase), .Q(s_r_ff_6_q), .reset(clear));  // open: Qn, preset, en
  Register #(.width(1)) register_6 (.D(s_r_ff_6_q), .Q(OUT[5]), .clk(push));  // open: en, clr
  S_R_Flip_Flop s_r_ff_7 (.S(draw), .clk(and_7_out), .R(erase), .Q(s_r_ff_7_q), .reset(clear));  // open: Qn, preset, en
  Register #(.width(1)) register_7 (.D(s_r_ff_7_q), .Q(OUT[6]), .clk(push));  // open: en, clr
  S_R_Flip_Flop s_r_ff_8 (.S(draw), .clk(and_8_out), .R(erase), .Q(s_r_ff_8_q), .reset(clear));  // open: Qn, preset, en
  Register #(.width(1)) register_8 (.D(s_r_ff_8_q), .Q(OUT[7]), .clk(push));  // open: en, clr
  S_R_Flip_Flop s_r_ff_9 (.S(draw), .clk(and_9_out), .R(erase), .Q(s_r_ff_9_q), .reset(clear));  // open: Qn, preset, en
  Register #(.width(1)) register_9 (.D(s_r_ff_9_q), .Q(OUT[8]), .clk(push));  // open: en, clr
  S_R_Flip_Flop s_r_ff_10 (
    .S(draw), .clk(and_10_out), .R(erase), .Q(s_r_ff_10_q), .reset(clear));  // open: Qn, preset, en
  Register #(.width(1)) register_10 (.D(s_r_ff_10_q), .Q(OUT[9]), .clk(push));  // open: en, clr
  S_R_Flip_Flop s_r_ff_11 (
    .S(draw), .clk(and_11_out), .R(erase), .Q(s_r_ff_11_q), .reset(clear));  // open: Qn, preset, en
  Register #(.width(1)) register_11 (.D(s_r_ff_11_q), .Q(OUT[10]), .clk(push));  // open: en, clr
  S_R_Flip_Flop s_r_ff_12 (
    .S(draw), .clk(and_12_out), .R(erase), .Q(s_r_ff_12_q), .reset(clear));  // open: Qn, preset, en
  Register #(.width(1)) register_12 (.D(s_r_ff_12_q), .Q(OUT[11]), .clk(push));  // open: en, clr
  S_R_Flip_Flop s_r_ff_13 (
    .S(draw), .clk(and_13_out), .R(erase), .Q(s_r_ff_13_q), .reset(clear));  // open: Qn, preset, en
  Register #(.width(1)) register_13 (.D(s_r_ff_13_q), .Q(OUT[12]), .clk(push));  // open: en, clr
  S_R_Flip_Flop s_r_ff_14 (
    .S(draw), .clk(and_14_out), .R(erase), .Q(s_r_ff_14_q), .reset(clear));  // open: Qn, preset, en
  Register #(.width(1)) register_14 (.D(s_r_ff_14_q), .Q(OUT[13]), .clk(push));  // open: en, clr
  S_R_Flip_Flop s_r_ff_15 (
    .S(draw), .clk(and_15_out), .R(erase), .Q(s_r_ff_15_q), .reset(clear));  // open: Qn, preset, en
  Register #(.width(1)) register_15 (.D(s_r_ff_15_q), .Q(OUT[14]), .clk(push));  // open: en, clr
  S_R_Flip_Flop s_r_ff_16 (
    .S(draw), .clk(and_16_out), .R(erase), .Q(s_r_ff_16_q), .reset(clear));  // open: Qn, preset, en
  Register #(.width(1)) register_16 (.D(s_r_ff_16_q), .Q(OUT[15]), .clk(push));  // open: en, clr
  S_R_Flip_Flop s_r_ff_17 (
    .S(draw), .clk(and_17_out), .R(erase), .Q(s_r_ff_17_q), .reset(clear));  // open: Qn, preset, en
  Register #(.width(1)) register_17 (.D(s_r_ff_17_q), .Q(OUT[16]), .clk(push));  // open: en, clr
  S_R_Flip_Flop s_r_ff_18 (
    .S(draw), .clk(and_18_out), .R(erase), .Q(s_r_ff_18_q), .reset(clear));  // open: Qn, preset, en
  Register #(.width(1)) register_18 (.D(s_r_ff_18_q), .Q(OUT[17]), .clk(push));  // open: en, clr
  S_R_Flip_Flop s_r_ff_19 (
    .S(draw), .clk(and_19_out), .R(erase), .Q(s_r_ff_19_q), .reset(clear));  // open: Qn, preset, en
  Register #(.width(1)) register_19 (.D(s_r_ff_19_q), .Q(OUT[18]), .clk(push));  // open: en, clr
  S_R_Flip_Flop s_r_ff_20 (
    .S(draw), .clk(and_20_out), .R(erase), .Q(s_r_ff_20_q), .reset(clear));  // open: Qn, preset, en
  Register #(.width(1)) register_20 (.D(s_r_ff_20_q), .Q(OUT[19]), .clk(push));  // open: en, clr
  S_R_Flip_Flop s_r_ff_21 (
    .S(draw), .clk(and_21_out), .R(erase), .Q(s_r_ff_21_q), .reset(clear));  // open: Qn, preset, en
  Register #(.width(1)) register_21 (.D(s_r_ff_21_q), .Q(OUT[20]), .clk(push));  // open: en, clr
  S_R_Flip_Flop s_r_ff_22 (
    .S(draw), .clk(and_22_out), .R(erase), .Q(s_r_ff_22_q), .reset(clear));  // open: Qn, preset, en
  Register #(.width(1)) register_22 (.D(s_r_ff_22_q), .Q(OUT[21]), .clk(push));  // open: en, clr
  S_R_Flip_Flop s_r_ff_23 (
    .S(draw), .clk(and_23_out), .R(erase), .Q(s_r_ff_23_q), .reset(clear));  // open: Qn, preset, en
  Register #(.width(1)) register_23 (.D(s_r_ff_23_q), .Q(OUT[22]), .clk(push));  // open: en, clr
  S_R_Flip_Flop s_r_ff_24 (
    .S(draw), .clk(and_24_out), .R(erase), .Q(s_r_ff_24_q), .reset(clear));  // open: Qn, preset, en
  Register #(.width(1)) register_24 (.D(s_r_ff_24_q), .Q(OUT[23]), .clk(push));  // open: en, clr
  S_R_Flip_Flop s_r_ff_25 (
    .S(draw), .clk(and_25_out), .R(erase), .Q(s_r_ff_25_q), .reset(clear));  // open: Qn, preset, en
  Register #(.width(1)) register_25 (.D(s_r_ff_25_q), .Q(OUT[24]), .clk(push));  // open: en, clr
  S_R_Flip_Flop s_r_ff_26 (
    .S(draw), .clk(and_26_out), .R(erase), .Q(s_r_ff_26_q), .reset(clear));  // open: Qn, preset, en
  Register #(.width(1)) register_26 (.D(s_r_ff_26_q), .Q(OUT[25]), .clk(push));  // open: en, clr
  S_R_Flip_Flop s_r_ff_27 (
    .S(draw), .clk(and_27_out), .R(erase), .Q(s_r_ff_27_q), .reset(clear));  // open: Qn, preset, en
  Register #(.width(1)) register_27 (.D(s_r_ff_27_q), .Q(OUT[26]), .clk(push));  // open: en, clr
  S_R_Flip_Flop s_r_ff_28 (
    .S(draw), .clk(and_28_out), .R(erase), .Q(s_r_ff_28_q), .reset(clear));  // open: Qn, preset, en
  Register #(.width(1)) register_28 (.D(s_r_ff_28_q), .Q(OUT[27]), .clk(push));  // open: en, clr
  S_R_Flip_Flop s_r_ff_29 (
    .S(draw), .clk(and_29_out), .R(erase), .Q(s_r_ff_29_q), .reset(clear));  // open: Qn, preset, en
  Register #(.width(1)) register_29 (.D(s_r_ff_29_q), .Q(OUT[28]), .clk(push));  // open: en, clr
  S_R_Flip_Flop s_r_ff_30 (
    .S(draw), .clk(and_30_out), .R(erase), .Q(s_r_ff_30_q), .reset(clear));  // open: Qn, preset, en
  Register #(.width(1)) register_30 (.D(s_r_ff_30_q), .Q(OUT[29]), .clk(push));  // open: en, clr
  S_R_Flip_Flop s_r_ff_31 (
    .S(draw), .clk(and_31_out), .R(erase), .Q(s_r_ff_31_q), .reset(clear));  // open: Qn, preset, en
  Register #(.width(1)) register_31 (.D(s_r_ff_31_q), .Q(OUT[30]), .clk(push));  // open: en, clr
  S_R_Flip_Flop s_r_ff_32 (
    .S(draw), .clk(and_32_out), .R(erase), .Q(s_r_ff_32_q), .reset(clear));  // open: Qn, preset, en
  Register #(.width(1)) register_32 (.D(s_r_ff_32_q), .Q(OUT[31]), .clk(push));  // open: en, clr
  and and_33 (and_33_out, s_r_ff_1_q, in_1);
  buf buffer_1 (buffer_1_out, and_33_out);
  buf buffer_2 (buffer_1_out, and_34_out);
  and and_34 (and_34_out, s_r_ff_2_q, in_2);
  and and_35 (and_35_out, s_r_ff_3_q, in_3);
  buf buffer_3 (buffer_1_out, and_35_out);
  and and_36 (and_36_out, s_r_ff_4_q, in_4);
  buf buffer_4 (buffer_1_out, and_36_out);
  buf buffer_5 (buffer_1_out, and_37_out);
  and and_37 (and_37_out, s_r_ff_5_q, in_5);
  and and_38 (and_38_out, s_r_ff_6_q, in_6);
  buf buffer_6 (buffer_1_out, and_38_out);
  buf buffer_7 (buffer_1_out, and_39_out);
  and and_39 (and_39_out, s_r_ff_7_q, in_7);
  and and_40 (and_40_out, s_r_ff_8_q, in_8);
  buf buffer_8 (buffer_1_out, and_40_out);
  and and_41 (and_41_out, s_r_ff_9_q, in_9);
  buf buffer_9 (buffer_1_out, and_41_out);
  and and_42 (and_42_out, s_r_ff_10_q, in_10);
  buf buffer_10 (buffer_1_out, and_42_out);
  buf buffer_11 (buffer_1_out, and_43_out);
  and and_43 (and_43_out, s_r_ff_11_q, in_11);
  buf buffer_12 (buffer_1_out, and_44_out);
  and and_44 (and_44_out, s_r_ff_12_q, in_12);
  buf buffer_13 (buffer_1_out, and_45_out);
  and and_45 (and_45_out, s_r_ff_13_q, in_13);
  and and_46 (and_46_out, s_r_ff_14_q, in_14);
  buf buffer_14 (buffer_1_out, and_46_out);
  buf buffer_15 (buffer_1_out, and_47_out);
  and and_47 (and_47_out, s_r_ff_15_q, in_15);
  and and_48 (and_48_out, s_r_ff_16_q, in_16);
  buf buffer_16 (buffer_1_out, and_48_out);
  buf buffer_17 (buffer_1_out, and_49_out);
  and and_49 (and_49_out, s_r_ff_17_q, in_17);
  and and_50 (and_50_out, s_r_ff_18_q, in_18);
  buf buffer_18 (buffer_1_out, and_50_out);
  and and_51 (and_51_out, s_r_ff_19_q, in_19);
  buf buffer_19 (buffer_1_out, and_51_out);
  and and_52 (and_52_out, s_r_ff_20_q, in_20);
  buf buffer_20 (buffer_1_out, and_52_out);
  and and_53 (and_53_out, s_r_ff_21_q, in_21);
  buf buffer_21 (buffer_1_out, and_53_out);
  buf buffer_22 (buffer_1_out, and_54_out);
  and and_54 (and_54_out, s_r_ff_22_q, in_22);
  buf buffer_23 (buffer_1_out, and_55_out);
  and and_55 (and_55_out, s_r_ff_23_q, in_23);
  and and_56 (and_56_out, s_r_ff_24_q, in_24);
  buf buffer_24 (buffer_1_out, and_56_out);
  buf buffer_25 (buffer_1_out, and_57_out);
  and and_57 (and_57_out, s_r_ff_25_q, in_25);
  and and_58 (and_58_out, s_r_ff_26_q, in_26);
  buf buffer_26 (buffer_1_out, and_58_out);
  buf buffer_27 (buffer_1_out, and_59_out);
  and and_59 (and_59_out, s_r_ff_27_q, in_27);
  and and_60 (and_60_out, s_r_ff_28_q, in_28);
  buf buffer_28 (buffer_1_out, and_60_out);
  and and_61 (and_61_out, s_r_ff_29_q, in_29);
  buf buffer_29 (buffer_1_out, and_61_out);
  and and_62 (and_62_out, s_r_ff_30_q, in_30);
  buf buffer_30 (buffer_1_out, and_62_out);
  and and_63 (and_63_out, s_r_ff_31_q, in_31);
  buf buffer_31 (buffer_1_out, and_63_out);
  and and_64 (and_64_out, s_r_ff_32_q, in_32);
  buf buffer_32 (buffer_1_out, and_64_out);
  Pull_Resistor pull_resistor_1 (.node(buffer_1_out));
  and and_65 (Pixel_info, buffer_1_out, Select);

  assign out_39 = in_1;
  assign out_40 = in_2;
  assign out_41 = in_3;
  assign out_42 = in_4;
  assign out_43 = in_5;
  assign out_44 = in_6;
  assign out_45 = in_7;
  assign out_46 = in_8;
  assign out_47 = in_9;
  assign out_48 = in_10;
  assign out_49 = in_11;
  assign out_50 = in_12;
  assign out_51 = in_13;
  assign out_52 = in_14;
  assign out_53 = in_15;
  assign out_54 = in_16;
  assign out_55 = in_17;
  assign out_56 = in_18;
  assign out_57 = in_19;
  assign out_58 = in_20;
  assign out_59 = in_21;
  assign out_60 = in_22;
  assign out_61 = in_23;
  assign out_62 = in_24;
  assign out_63 = in_25;
  assign out_64 = in_26;
  assign out_65 = in_27;
  assign out_66 = in_28;
  assign out_67 = in_29;
  assign out_68 = in_30;
  assign out_69 = in_31;
  assign out_70 = in_32;

  // Notes on the sheet:
  //   buffer_1 drives only 1 and floats otherwise
  //   buffer_2 drives only 1 and floats otherwise
  //   buffer_3 drives only 1 and floats otherwise
  //   buffer_4 drives only 1 and floats otherwise
  //   buffer_5 drives only 1 and floats otherwise
  //   buffer_6 drives only 1 and floats otherwise
  //   buffer_7 drives only 1 and floats otherwise
  //   buffer_8 drives only 1 and floats otherwise
  //   buffer_9 drives only 1 and floats otherwise
  //   buffer_10 drives only 1 and floats otherwise
  //   buffer_11 drives only 1 and floats otherwise
  //   buffer_12 drives only 1 and floats otherwise
  //   buffer_13 drives only 1 and floats otherwise
  //   buffer_14 drives only 1 and floats otherwise
  //   buffer_15 drives only 1 and floats otherwise
  //   buffer_16 drives only 1 and floats otherwise
  //   buffer_17 drives only 1 and floats otherwise
  //   buffer_18 drives only 1 and floats otherwise
  //   buffer_19 drives only 1 and floats otherwise
  //   buffer_20 drives only 1 and floats otherwise
  //   buffer_21 drives only 1 and floats otherwise
  //   buffer_22 drives only 1 and floats otherwise
  //   buffer_23 drives only 1 and floats otherwise
  //   buffer_24 drives only 1 and floats otherwise
  //   buffer_25 drives only 1 and floats otherwise
  //   buffer_26 drives only 1 and floats otherwise
  //   buffer_27 drives only 1 and floats otherwise
  //   buffer_28 drives only 1 and floats otherwise
  //   buffer_29 drives only 1 and floats otherwise
  //   buffer_30 drives only 1 and floats otherwise
  //   buffer_31 drives only 1 and floats otherwise
  //   buffer_32 drives only 1 and floats otherwise
endmodule

module Character_display_module (
  input  [2:0] Settings,
  input  [7:0] Code,
  output [6:0] out_3,
  output [6:0] out_4,
  output [6:0] out_5,
  output [6:0] out_6,
  output [6:0] out_7,
  output [6:0] out_8,
  output [6:0] out_9,
  output [6:0] out_10,
  output [6:0] out_11,
  output [6:0] out_12,
  output [6:0] out_13,
  output [6:0] out_14,
  output [6:0] out_15,
  output [6:0] out_16,
  output [6:0] out_17,
  output [6:0] out_18,
  output [6:0] out_19,
  output [6:0] out_20,
  output [6:0] out_21,
  output [6:0] out_22,
  output [6:0] out_23,
  output [6:0] out_24,
  output [6:0] out_25,
  output [6:0] out_26,
  output [6:0] out_27,
  output [6:0] out_28,
  output [6:0] out_29,
  output [6:0] out_30,
  output [6:0] out_31,
  output [6:0] out_32,
  output [6:0] out_33,
  output [6:0] out_34,
  output [6:0] out_35,
  output [6:0] out_36,
  output [6:0] out_37,
  output [6:0] out_38,
  output [6:0] out_39,
  output [6:0] out_40,
  output [6:0] out_41,
  output [6:0] out_42,
  output [6:0] out_43,
  output [6:0] out_44,
  output [6:0] out_45,
  output [6:0] out_46,
  output [6:0] out_47,
  output [6:0] out_48,
  output [6:0] out_49,
  output [6:0] out_50,
  output [6:0] out_51,
  output [6:0] out_52
);

  wire not_1_out;
  wire [6:0] char_code_1_c0, char_code_1_c1, char_code_1_c2, char_code_1_c3, char_code_1_c4, register_1_q,
       register_2_q, register_3_q, register_4_q, register_5_q, register_7_q, register_9_q, register_11_q,
       register_13_q, register_15_q, register_17_q, register_19_q, register_21_q, register_23_q,
       register_25_q, register_28_q, register_29_q, register_32_q, register_33_q, register_36_q,
       register_37_q, register_40_q, register_41_q, register_44_q, register_45_q, register_47_q,
       register_49_q, register_51_q, register_53_q, register_55_q, register_57_q, register_59_q,
       register_61_q, register_63_q, register_65_q, register_68_q, register_69_q, register_72_q,
       register_73_q, register_76_q, register_77_q, register_80_q, register_81_q, register_84_q,
       register_85_q, register_87_q, register_89_q, register_91_q, register_93_q, register_95_q;

  not not_1 (not_1_out, Settings[2]);
  Char_Code char_code_1 (
    .code(Code[4:0]), .c4(char_code_1_c4), .c3(char_code_1_c3), .c2(char_code_1_c2), .c1(char_code_1_c1),
    .c0(char_code_1_c0));
  Register #(.width(7)) register_1 (
    .D(char_code_1_c4), .Q(register_1_q), .clk(not_1_out), .clr(Settings[0]));  // open: en
  Register #(.width(7)) register_2 (
    .D(char_code_1_c3), .Q(register_2_q), .clk(not_1_out), .clr(Settings[0]));  // open: en
  Register #(.width(7)) register_3 (
    .D(char_code_1_c2), .Q(register_3_q), .clk(not_1_out), .clr(Settings[0]));  // open: en
  Register #(.width(7)) register_4 (
    .D(char_code_1_c1), .Q(register_4_q), .clk(not_1_out), .clr(Settings[0]));  // open: en
  Register #(.width(7)) register_5 (
    .D(char_code_1_c0), .Q(register_5_q), .clk(not_1_out), .clr(Settings[0]));  // open: en
  Register #(.width(7)) register_6 (.D(register_1_q), .Q(out_3), .clk(Settings[1]));  // open: en, clr
  Register #(.width(7)) register_7 (
    .D(register_1_q), .Q(register_7_q), .clk(not_1_out), .clr(Settings[0]));  // open: en
  Register #(.width(7)) register_8 (.D(register_2_q), .Q(out_4), .clk(Settings[1]));  // open: en, clr
  Register #(.width(7)) register_9 (
    .D(register_2_q), .Q(register_9_q), .clk(not_1_out), .clr(Settings[0]));  // open: en
  Register #(.width(7)) register_10 (.D(register_3_q), .Q(out_5), .clk(Settings[1]));  // open: en, clr
  Register #(.width(7)) register_11 (
    .D(register_3_q), .Q(register_11_q), .clk(not_1_out), .clr(Settings[0]));  // open: en
  Register #(.width(7)) register_12 (.D(register_4_q), .Q(out_6), .clk(Settings[1]));  // open: en, clr
  Register #(.width(7)) register_13 (
    .D(register_4_q), .Q(register_13_q), .clk(not_1_out), .clr(Settings[0]));  // open: en
  Register #(.width(7)) register_14 (.D(register_5_q), .Q(out_7), .clk(Settings[1]));  // open: en, clr
  Register #(.width(7)) register_15 (
    .D(register_5_q), .Q(register_15_q), .clk(not_1_out), .clr(Settings[0]));  // open: en
  Register #(.width(7)) register_16 (.D(register_7_q), .Q(out_8), .clk(Settings[1]));  // open: en, clr
  Register #(.width(7)) register_17 (
    .D(register_7_q), .Q(register_17_q), .clk(not_1_out), .clr(Settings[0]));  // open: en
  Register #(.width(7)) register_18 (.D(register_9_q), .Q(out_9), .clk(Settings[1]));  // open: en, clr
  Register #(.width(7)) register_19 (
    .D(register_9_q), .Q(register_19_q), .clk(not_1_out), .clr(Settings[0]));  // open: en
  Register #(.width(7)) register_20 (.D(register_11_q), .Q(out_10), .clk(Settings[1]));  // open: en, clr
  Register #(.width(7)) register_21 (
    .D(register_11_q), .Q(register_21_q), .clk(not_1_out), .clr(Settings[0]));  // open: en
  Register #(.width(7)) register_22 (.D(register_13_q), .Q(out_11), .clk(Settings[1]));  // open: en, clr
  Register #(.width(7)) register_23 (
    .D(register_13_q), .Q(register_23_q), .clk(not_1_out), .clr(Settings[0]));  // open: en
  Register #(.width(7)) register_24 (.D(register_15_q), .Q(out_12), .clk(Settings[1]));  // open: en, clr
  Register #(.width(7)) register_25 (
    .D(register_15_q), .Q(register_25_q), .clk(not_1_out), .clr(Settings[0]));  // open: en
  Register #(.width(7)) register_26 (.D(register_29_q), .Q(out_18), .clk(Settings[1]));  // open: en, clr
  Register #(.width(7)) register_27 (.D(register_17_q), .Q(out_13), .clk(Settings[1]));  // open: en, clr
  Register #(.width(7)) register_28 (
    .D(register_29_q), .Q(register_28_q), .clk(not_1_out), .clr(Settings[0]));  // open: en
  Register #(.width(7)) register_29 (
    .D(register_17_q), .Q(register_29_q), .clk(not_1_out), .clr(Settings[0]));  // open: en
  Register #(.width(7)) register_30 (.D(register_32_q), .Q(out_19), .clk(Settings[1]));  // open: en, clr
  Register #(.width(7)) register_31 (.D(register_19_q), .Q(out_14), .clk(Settings[1]));  // open: en, clr
  Register #(.width(7)) register_32 (
    .D(register_19_q), .Q(register_32_q), .clk(not_1_out), .clr(Settings[0]));  // open: en
  Register #(.width(7)) register_33 (
    .D(register_32_q), .Q(register_33_q), .clk(not_1_out), .clr(Settings[0]));  // open: en
  Register #(.width(7)) register_34 (.D(register_36_q), .Q(out_20), .clk(Settings[1]));  // open: en, clr
  Register #(.width(7)) register_35 (.D(register_21_q), .Q(out_15), .clk(Settings[1]));  // open: en, clr
  Register #(.width(7)) register_36 (
    .D(register_21_q), .Q(register_36_q), .clk(not_1_out), .clr(Settings[0]));  // open: en
  Register #(.width(7)) register_37 (
    .D(register_36_q), .Q(register_37_q), .clk(not_1_out), .clr(Settings[0]));  // open: en
  Register #(.width(7)) register_38 (.D(register_40_q), .Q(out_21), .clk(Settings[1]));  // open: en, clr
  Register #(.width(7)) register_39 (.D(register_23_q), .Q(out_16), .clk(Settings[1]));  // open: en, clr
  Register #(.width(7)) register_40 (
    .D(register_23_q), .Q(register_40_q), .clk(not_1_out), .clr(Settings[0]));  // open: en
  Register #(.width(7)) register_41 (
    .D(register_40_q), .Q(register_41_q), .clk(not_1_out), .clr(Settings[0]));  // open: en
  Register #(.width(7)) register_42 (.D(register_25_q), .Q(out_17), .clk(Settings[1]));  // open: en, clr
  Register #(.width(7)) register_43 (.D(register_44_q), .Q(out_22), .clk(Settings[1]));  // open: en, clr
  Register #(.width(7)) register_44 (
    .D(register_25_q), .Q(register_44_q), .clk(not_1_out), .clr(Settings[0]));  // open: en
  Register #(.width(7)) register_45 (
    .D(register_44_q), .Q(register_45_q), .clk(not_1_out), .clr(Settings[0]));  // open: en
  Register #(.width(7)) register_46 (.D(register_28_q), .Q(out_23), .clk(Settings[1]));  // open: en, clr
  Register #(.width(7)) register_47 (
    .D(register_28_q), .Q(register_47_q), .clk(not_1_out), .clr(Settings[0]));  // open: en
  Register #(.width(7)) register_48 (.D(register_33_q), .Q(out_24), .clk(Settings[1]));  // open: en, clr
  Register #(.width(7)) register_49 (
    .D(register_33_q), .Q(register_49_q), .clk(not_1_out), .clr(Settings[0]));  // open: en
  Register #(.width(7)) register_50 (.D(register_37_q), .Q(out_25), .clk(Settings[1]));  // open: en, clr
  Register #(.width(7)) register_51 (
    .D(register_37_q), .Q(register_51_q), .clk(not_1_out), .clr(Settings[0]));  // open: en
  Register #(.width(7)) register_52 (.D(register_41_q), .Q(out_26), .clk(Settings[1]));  // open: en, clr
  Register #(.width(7)) register_53 (
    .D(register_41_q), .Q(register_53_q), .clk(not_1_out), .clr(Settings[0]));  // open: en
  Register #(.width(7)) register_54 (.D(register_45_q), .Q(out_27), .clk(Settings[1]));  // open: en, clr
  Register #(.width(7)) register_55 (
    .D(register_45_q), .Q(register_55_q), .clk(not_1_out), .clr(Settings[0]));  // open: en
  Register #(.width(7)) register_56 (.D(register_47_q), .Q(out_28), .clk(Settings[1]));  // open: en, clr
  Register #(.width(7)) register_57 (
    .D(register_47_q), .Q(register_57_q), .clk(not_1_out), .clr(Settings[0]));  // open: en
  Register #(.width(7)) register_58 (.D(register_49_q), .Q(out_29), .clk(Settings[1]));  // open: en, clr
  Register #(.width(7)) register_59 (
    .D(register_49_q), .Q(register_59_q), .clk(not_1_out), .clr(Settings[0]));  // open: en
  Register #(.width(7)) register_60 (.D(register_51_q), .Q(out_30), .clk(Settings[1]));  // open: en, clr
  Register #(.width(7)) register_61 (
    .D(register_51_q), .Q(register_61_q), .clk(not_1_out), .clr(Settings[0]));  // open: en
  Register #(.width(7)) register_62 (.D(register_53_q), .Q(out_31), .clk(Settings[1]));  // open: en, clr
  Register #(.width(7)) register_63 (
    .D(register_53_q), .Q(register_63_q), .clk(not_1_out), .clr(Settings[0]));  // open: en
  Register #(.width(7)) register_64 (.D(register_55_q), .Q(out_32), .clk(Settings[1]));  // open: en, clr
  Register #(.width(7)) register_65 (
    .D(register_55_q), .Q(register_65_q), .clk(not_1_out), .clr(Settings[0]));  // open: en
  Register #(.width(7)) register_66 (.D(register_57_q), .Q(out_33), .clk(Settings[1]));  // open: en, clr
  Register #(.width(7)) register_67 (.D(register_68_q), .Q(out_38), .clk(Settings[1]));  // open: en, clr
  Register #(.width(7)) register_68 (
    .D(register_57_q), .Q(register_68_q), .clk(not_1_out), .clr(Settings[0]));  // open: en
  Register #(.width(7)) register_69 (
    .D(register_68_q), .Q(register_69_q), .clk(not_1_out), .clr(Settings[0]));  // open: en
  Register #(.width(7)) register_70 (.D(register_59_q), .Q(out_34), .clk(Settings[1]));  // open: en, clr
  Register #(.width(7)) register_71 (.D(register_73_q), .Q(out_39), .clk(Settings[1]));  // open: en, clr
  Register #(.width(7)) register_72 (
    .D(register_73_q), .Q(register_72_q), .clk(not_1_out), .clr(Settings[0]));  // open: en
  Register #(.width(7)) register_73 (
    .D(register_59_q), .Q(register_73_q), .clk(not_1_out), .clr(Settings[0]));  // open: en
  Register #(.width(7)) register_74 (.D(register_61_q), .Q(out_35), .clk(Settings[1]));  // open: en, clr
  Register #(.width(7)) register_75 (.D(register_77_q), .Q(out_40), .clk(Settings[1]));  // open: en, clr
  Register #(.width(7)) register_76 (
    .D(register_77_q), .Q(register_76_q), .clk(not_1_out), .clr(Settings[0]));  // open: en
  Register #(.width(7)) register_77 (
    .D(register_61_q), .Q(register_77_q), .clk(not_1_out), .clr(Settings[0]));  // open: en
  Register #(.width(7)) register_78 (.D(register_81_q), .Q(out_41), .clk(Settings[1]));  // open: en, clr
  Register #(.width(7)) register_79 (.D(register_63_q), .Q(out_36), .clk(Settings[1]));  // open: en, clr
  Register #(.width(7)) register_80 (
    .D(register_81_q), .Q(register_80_q), .clk(not_1_out), .clr(Settings[0]));  // open: en
  Register #(.width(7)) register_81 (
    .D(register_63_q), .Q(register_81_q), .clk(not_1_out), .clr(Settings[0]));  // open: en
  Register #(.width(7)) register_82 (.D(register_65_q), .Q(out_37), .clk(Settings[1]));  // open: en, clr
  Register #(.width(7)) register_83 (.D(register_84_q), .Q(out_42), .clk(Settings[1]));  // open: en, clr
  Register #(.width(7)) register_84 (
    .D(register_65_q), .Q(register_84_q), .clk(not_1_out), .clr(Settings[0]));  // open: en
  Register #(.width(7)) register_85 (
    .D(register_84_q), .Q(register_85_q), .clk(not_1_out), .clr(Settings[0]));  // open: en
  Register #(.width(7)) register_86 (.D(register_69_q), .Q(out_43), .clk(Settings[1]));  // open: en, clr
  Register #(.width(7)) register_87 (
    .D(register_69_q), .Q(register_87_q), .clk(not_1_out), .clr(Settings[0]));  // open: en
  Register #(.width(7)) register_88 (.D(register_72_q), .Q(out_44), .clk(Settings[1]));  // open: en, clr
  Register #(.width(7)) register_89 (
    .D(register_72_q), .Q(register_89_q), .clk(not_1_out), .clr(Settings[0]));  // open: en
  Register #(.width(7)) register_90 (.D(register_76_q), .Q(out_45), .clk(Settings[1]));  // open: en, clr
  Register #(.width(7)) register_91 (
    .D(register_76_q), .Q(register_91_q), .clk(not_1_out), .clr(Settings[0]));  // open: en
  Register #(.width(7)) register_92 (.D(register_80_q), .Q(out_46), .clk(Settings[1]));  // open: en, clr
  Register #(.width(7)) register_93 (
    .D(register_80_q), .Q(register_93_q), .clk(not_1_out), .clr(Settings[0]));  // open: en
  Register #(.width(7)) register_94 (.D(register_85_q), .Q(out_47), .clk(Settings[1]));  // open: en, clr
  Register #(.width(7)) register_95 (
    .D(register_85_q), .Q(register_95_q), .clk(not_1_out), .clr(Settings[0]));  // open: en
  Register #(.width(7)) register_96 (.D(register_87_q), .Q(out_48), .clk(Settings[1]));  // open: en, clr
  Register #(.width(7)) register_97 (.D(register_89_q), .Q(out_49), .clk(Settings[1]));  // open: en, clr
  Register #(.width(7)) register_98 (.D(register_91_q), .Q(out_50), .clk(Settings[1]));  // open: en, clr
  Register #(.width(7)) register_99 (.D(register_93_q), .Q(out_51), .clk(Settings[1]));  // open: en, clr
  Register #(.width(7)) register_100 (.D(register_95_q), .Q(out_52), .clk(Settings[1]));  // open: en, clr
endmodule

module Char_Code (
  input  [4:0] code,
  output [6:0] c1,
  output [6:0] c0,
  output [6:0] c4,
  output [6:0] c3,
  output [6:0] c2
);

  wire decoder_1_out0, decoder_1_out1, decoder_1_out2, decoder_1_out3, decoder_1_out4, decoder_1_out5,
       decoder_1_out6, decoder_1_out7, decoder_1_out8, decoder_1_out9, decoder_1_out10, decoder_1_out11,
       decoder_1_out12, decoder_1_out13, decoder_1_out14, decoder_1_out15, decoder_1_out16, decoder_1_out17,
       decoder_1_out18, decoder_1_out19, decoder_1_out20, decoder_1_out21, decoder_1_out22, decoder_1_out23,
       decoder_1_out24, decoder_1_out25, decoder_1_out26, decoder_1_out27, decoder_1_out28, decoder_1_out29,
       decoder_1_out30, decoder_1_out31;
  wire [0:0] undriven_46, undriven_54, undriven_99;
  wire [1:0] undriven_65, undriven_73;
  wire [1:1] undriven_114;
  wire [3:0] undriven_55, undriven_63;
  wire [4:0] undriven_83, undriven_90;
  wire [4:1] undriven_100;
  wire [5:0] undriven_3, undriven_5, undriven_7, undriven_12, undriven_14, undriven_16, undriven_17,
       undriven_21, undriven_23, undriven_25, undriven_38, undriven_40, undriven_43, undriven_45,
       undriven_56, undriven_58, undriven_60, undriven_62, undriven_91, undriven_120, undriven_121,
       undriven_124, undriven_125, undriven_128;
  wire [5:1] undriven_13, undriven_15, undriven_20, undriven_22, undriven_24, undriven_30, undriven_31,
       undriven_32, undriven_33, undriven_34, undriven_35, undriven_39, undriven_41, undriven_42,
       undriven_47, undriven_49, undriven_51, undriven_53, undriven_66, undriven_68, undriven_70,
       undriven_74, undriven_81, undriven_82, undriven_84, undriven_87, undriven_89, undriven_93,
       undriven_94, undriven_95, undriven_96, undriven_97, undriven_98, undriven_108, undriven_123,
       undriven_137, undriven_139, undriven_141;
  wire [5:3] undriven_92;
  wire [6:0] undriven, undriven_2, undriven_4, undriven_6, undriven_8, undriven_9, undriven_11, undriven_26,
       undriven_28, undriven_36, undriven_37, undriven_44, undriven_57, undriven_61, undriven_64,
       undriven_69, undriven_72, undriven_75, undriven_76, undriven_77, undriven_78, undriven_79,
       undriven_80, undriven_85, undriven_88, undriven_101, undriven_102, undriven_104, undriven_105,
       undriven_106, undriven_107, undriven_109, undriven_110, undriven_112, undriven_116, undriven_118,
       undriven_119, undriven_122, undriven_126, undriven_127, undriven_130, undriven_134, undriven_135,
       undriven_136, undriven_138, undriven_140, undriven_142, undriven_143, undriven_144;
  wire [6:1] undriven_19, undriven_29, undriven_48, undriven_50, undriven_52, undriven_59, undriven_103,
       undriven_111, undriven_113, undriven_115, undriven_117, undriven_129, undriven_131, undriven_132,
       undriven_133;
  wire [6:2] undriven_67, undriven_71;
  wire [6:4] undriven_27, undriven_86;
  wire [6:6] undriven_10, undriven_18;

  Decoder #(.select(5)) decoder_1 (
    .out0(decoder_1_out0), .out1(decoder_1_out1), .out2(decoder_1_out2), .out3(decoder_1_out3),
    .out4(decoder_1_out4), .out5(decoder_1_out5), .out6(decoder_1_out6), .out7(decoder_1_out7),
    .out8(decoder_1_out8), .out9(decoder_1_out9), .out10(decoder_1_out10), .out11(decoder_1_out11),
    .out12(decoder_1_out12), .out13(decoder_1_out13), .out14(decoder_1_out14), .out15(decoder_1_out15),
    .out16(decoder_1_out16), .out17(decoder_1_out17), .out18(decoder_1_out18), .out19(decoder_1_out19),
    .out20(decoder_1_out20), .out21(decoder_1_out21), .out22(decoder_1_out22), .out23(decoder_1_out23),
    .out24(decoder_1_out24), .out25(decoder_1_out25), .out26(decoder_1_out26), .out27(decoder_1_out27),
    .out28(decoder_1_out28), .out29(decoder_1_out29), .out30(decoder_1_out30), .out31(decoder_1_out31),
    .sel(code));  // open: en
  assign c3 = decoder_1_out0 ? undriven_2 : 7'bz;  // Controlled_Buffer controlled_buffer_1
  assign c1 = decoder_1_out0 ? undriven_6 : 7'bz;  // Controlled_Buffer controlled_buffer_2
  assign c4 = decoder_1_out0 ? undriven : 7'bz;  // Controlled_Buffer controlled_buffer_3
  assign c2 = decoder_1_out0 ? undriven_4 : 7'bz;  // Controlled_Buffer controlled_buffer_4
  assign c0 = decoder_1_out0 ? undriven_8 : 7'bz;  // Controlled_Buffer controlled_buffer_5
  assign c2 = decoder_1_out16 ? {1'b1, undriven_5[5], 1'b1, undriven_5[3:0]} : 7'bz;  // Controlled_Buffer controlled_buffer_6
  assign c1 = decoder_1_out16 ? {1'b1, undriven_7[5], 1'b1, undriven_7[3:0]} : 7'bz;  // Controlled_Buffer controlled_buffer_7
  assign c4 = decoder_1_out16 ? {7{1'b1}} : 7'bz;  // Controlled_Buffer controlled_buffer_8
  assign c0 = decoder_1_out16 ? {undriven_9[6], 1'b1, undriven_9[4:0]} : 7'bz;  // Controlled_Buffer controlled_buffer_9
  assign c3 = decoder_1_out16 ? {1'b1, undriven_3[5], 1'b1, undriven_3[3:0]} : 7'bz;  // Controlled_Buffer controlled_buffer_10
  assign c3 = decoder_1_out1 ? {1'b1, undriven_12[5], 1'b1, undriven_12[3:0]} : 7'bz;  // Controlled_Buffer controlled_buffer_11
  assign c4 = decoder_1_out1 ? {undriven_10[6], {6{1'b1}}} : 7'bz;  // Controlled_Buffer controlled_buffer_12
  assign c2 = decoder_1_out1 ? {1'b1, undriven_14[5], 1'b1, undriven_14[3:0]} : 7'bz;  // Controlled_Buffer controlled_buffer_13
  assign c3 = decoder_1_out17 ? {1'b1, undriven_13, 1'b1} : 7'bz;  // Controlled_Buffer controlled_buffer_14
  assign c2 = decoder_1_out17 ? {1'b1, undriven_15, 1'b1} : 7'bz;  // Controlled_Buffer controlled_buffer_15
  assign c4 = decoder_1_out17 ? {undriven_11[6], {5{1'b1}}, undriven_11[0]} : 7'bz;  // Controlled_Buffer controlled_buffer_16
  assign c4 = decoder_1_out2 ? {7{1'b1}} : 7'bz;  // Controlled_Buffer controlled_buffer_17
  assign c0 = decoder_1_out1 ? {undriven_18[6], {6{1'b1}}} : 7'bz;  // Controlled_Buffer controlled_buffer_18
  assign c1 = decoder_1_out1 ? {1'b1, undriven_16[5], 1'b1, undriven_16[3:0]} : 7'bz;  // Controlled_Buffer controlled_buffer_19
  assign c1 = decoder_1_out17 ? {1'b1, undriven_17[5:2], 1'b1, undriven_17[0]} : 7'bz;  // Controlled_Buffer controlled_buffer_20
  assign c0 = decoder_1_out17 ? {undriven_19[6], 4'b1111, undriven_19[1], 1'b1} : 7'bz;  // Controlled_Buffer controlled_buffer_21
  assign c4 = decoder_1_out18 ? {7{1'b1}} : 7'bz;  // Controlled_Buffer controlled_buffer_22
  assign c2 = decoder_1_out2 ? {1'b1, undriven_22[5], 1'b1, undriven_22[3:1], 1'b1} : 7'bz;  // Controlled_Buffer controlled_buffer_23
  assign c3 = decoder_1_out2 ? {1'b1, undriven_20[5], 1'b1, undriven_20[3:1], 1'b1} : 7'bz;  // Controlled_Buffer controlled_buffer_24
  assign c0 = decoder_1_out2 ? {undriven_26[6], 1'b1, undriven_26[4], 3'b111, undriven_26[0]} : 7'bz;  // Controlled_Buffer controlled_buffer_25
  assign c1 = decoder_1_out2 ? {1'b1, undriven_24[5], 1'b1, undriven_24[3:1], 1'b1} : 7'bz;  // Controlled_Buffer controlled_buffer_26
  assign c1 = decoder_1_out18 ? {1'b1, undriven_25[5], 1'b1, undriven_25[3:0]} : 7'bz;  // Controlled_Buffer controlled_buffer_27
  assign c2 = decoder_1_out18 ? {1'b1, undriven_23[5], 1'b1, undriven_23[3:0]} : 7'bz;  // Controlled_Buffer controlled_buffer_28
  assign c0 = decoder_1_out18 ? {undriven_27[6], 1'b1, undriven_27[4], 4'b1111} : 7'bz;  // Controlled_Buffer controlled_buffer_29
  assign c3 = decoder_1_out18 ? {1'b1, undriven_21[5], 1'b1, undriven_21[3:0]} : 7'bz;  // Controlled_Buffer controlled_buffer_30
  assign c1 = decoder_1_out3 ? {1'b1, undriven_34, 1'b1} : 7'bz;  // Controlled_Buffer controlled_buffer_31
  assign c2 = decoder_1_out3 ? {1'b1, undriven_32, 1'b1} : 7'bz;  // Controlled_Buffer controlled_buffer_32
  assign c3 = decoder_1_out3 ? {1'b1, undriven_30, 1'b1} : 7'bz;  // Controlled_Buffer controlled_buffer_33
  assign c4 = decoder_1_out3 ? {undriven_28[6], {5{1'b1}}, undriven_28[0]} : 7'bz;  // Controlled_Buffer controlled_buffer_34
  assign c0 = decoder_1_out3 ? {undriven_36[6], 1'b1, undriven_36[4:2], 1'b1, undriven_36[0]} : 7'bz;  // Controlled_Buffer controlled_buffer_35
  assign c0 = decoder_1_out19 ? {undriven_37[6:4], 3'b111, undriven_37[0]} : 7'bz;  // Controlled_Buffer controlled_buffer_36
  assign c2 = decoder_1_out19 ? {1'b1, undriven_33[5], 1'b1, undriven_33[3:1], 1'b1} : 7'bz;  // Controlled_Buffer controlled_buffer_37
  assign c4 = decoder_1_out19 ? {undriven_29[6], 1'b1, undriven_29[4:1], 1'b1} : 7'bz;  // Controlled_Buffer controlled_buffer_38
  assign c3 = decoder_1_out19 ? {1'b1, undriven_31[5], 1'b1, undriven_31[3:1], 1'b1} : 7'bz;  // Controlled_Buffer controlled_buffer_39
  assign c1 = decoder_1_out19 ? {1'b1, undriven_35[5], 1'b1, undriven_35[3:1], 1'b1} : 7'bz;  // Controlled_Buffer controlled_buffer_40
  assign c4 = decoder_1_out4 ? {7{1'b1}} : 7'bz;  // Controlled_Buffer controlled_buffer_41
  assign c0 = decoder_1_out4 ? {undriven_44[6], {5{1'b1}}, undriven_44[0]} : 7'bz;  // Controlled_Buffer controlled_buffer_42
  assign c3 = decoder_1_out4 ? {1'b1, undriven_39, 1'b1} : 7'bz;  // Controlled_Buffer controlled_buffer_43
  assign c1 = decoder_1_out4 ? {1'b1, undriven_42, 1'b1} : 7'bz;  // Controlled_Buffer controlled_buffer_44
  assign c2 = decoder_1_out4 ? {1'b1, undriven_41, 1'b1} : 7'bz;  // Controlled_Buffer controlled_buffer_45
  assign c2 = decoder_1_out20 ? {7{1'b1}} : 7'bz;  // Controlled_Buffer controlled_buffer_46
  assign c4 = decoder_1_out20 ? {1'b1, undriven_38} : 7'bz;  // Controlled_Buffer controlled_buffer_47
  assign c0 = decoder_1_out20 ? {1'b1, undriven_45} : 7'bz;  // Controlled_Buffer controlled_buffer_48
  assign c3 = decoder_1_out20 ? {1'b1, undriven_40} : 7'bz;  // Controlled_Buffer controlled_buffer_49
  assign c1 = decoder_1_out20 ? {1'b1, undriven_43} : 7'bz;  // Controlled_Buffer controlled_buffer_50
  assign c3 = decoder_1_out5 ? {1'b1, undriven_47[5], 1'b1, undriven_47[3:1], 1'b1} : 7'bz;  // Controlled_Buffer controlled_buffer_51
  assign c4 = decoder_1_out5 ? {7{1'b1}} : 7'bz;  // Controlled_Buffer controlled_buffer_52
  assign c2 = decoder_1_out5 ? {1'b1, undriven_49[5], 1'b1, undriven_49[3:1], 1'b1} : 7'bz;  // Controlled_Buffer controlled_buffer_53
  assign c2 = decoder_1_out21 ? {undriven_50, 1'b1} : 7'bz;  // Controlled_Buffer controlled_buffer_54
  assign c4 = decoder_1_out21 ? {{6{1'b1}}, undriven_46[0]} : 7'bz;  // Controlled_Buffer controlled_buffer_55
  assign c3 = decoder_1_out21 ? {undriven_48, 1'b1} : 7'bz;  // Controlled_Buffer controlled_buffer_56
  assign c1 = decoder_1_out5 ? {1'b1, undriven_51, 1'b1} : 7'bz;  // Controlled_Buffer controlled_buffer_57
  assign c0 = decoder_1_out5 ? {1'b1, undriven_53, 1'b1} : 7'bz;  // Controlled_Buffer controlled_buffer_58
  assign c4 = decoder_1_out6 ? {7{1'b1}} : 7'bz;  // Controlled_Buffer controlled_buffer_59
  assign c1 = decoder_1_out21 ? {undriven_52, 1'b1} : 7'bz;  // Controlled_Buffer controlled_buffer_60
  assign c4 = decoder_1_out22 ? {3'b111, undriven_55} : 7'bz;  // Controlled_Buffer controlled_buffer_61
  assign c0 = decoder_1_out21 ? {{6{1'b1}}, undriven_54[0]} : 7'bz;  // Controlled_Buffer controlled_buffer_62
  assign c0 = decoder_1_out6 ? {1'b1, undriven_62} : 7'bz;  // Controlled_Buffer controlled_buffer_63
  assign c1 = decoder_1_out6 ? {1'b1, undriven_60} : 7'bz;  // Controlled_Buffer controlled_buffer_64
  assign c2 = decoder_1_out6 ? {1'b1, undriven_58[5:4], 1'b1, undriven_58[2:0]} : 7'bz;  // Controlled_Buffer controlled_buffer_65
  assign c3 = decoder_1_out6 ? {1'b1, undriven_56[5:4], 1'b1, undriven_56[2:0]} : 7'bz;  // Controlled_Buffer controlled_buffer_66
  assign c0 = decoder_1_out22 ? {3'b111, undriven_63} : 7'bz;  // Controlled_Buffer controlled_buffer_67
  assign c1 = decoder_1_out22 ? {undriven_61[6:4], 3'b111, undriven_61[0]} : 7'bz;  // Controlled_Buffer controlled_buffer_68
  assign c3 = decoder_1_out22 ? {undriven_57[6:4], 3'b111, undriven_57[0]} : 7'bz;  // Controlled_Buffer controlled_buffer_69
  assign c2 = decoder_1_out22 ? {undriven_59, 1'b1} : 7'bz;  // Controlled_Buffer controlled_buffer_70
  assign c2 = decoder_1_out7 ? {1'b1, undriven_68, 1'b1} : 7'bz;  // Controlled_Buffer controlled_buffer_71
  assign c0 = decoder_1_out7 ? {undriven_72[6], 1'b1, undriven_72[4], 3'b111, undriven_72[0]} : 7'bz;  // Controlled_Buffer controlled_buffer_72
  assign c3 = decoder_1_out7 ? {1'b1, undriven_66, 1'b1} : 7'bz;  // Controlled_Buffer controlled_buffer_73
  assign c1 = decoder_1_out7 ? {1'b1, undriven_70[5:4], 1'b1, undriven_70[2:1], 1'b1} : 7'bz;  // Controlled_Buffer controlled_buffer_74
  assign c4 = decoder_1_out7 ? {undriven_64[6], {5{1'b1}}, undriven_64[0]} : 7'bz;  // Controlled_Buffer controlled_buffer_75
  assign c3 = decoder_1_out23 ? {undriven_67, 2'b11} : 7'bz;  // Controlled_Buffer controlled_buffer_76
  assign c4 = decoder_1_out23 ? {{5{1'b1}}, undriven_65} : 7'bz;  // Controlled_Buffer controlled_buffer_77
  assign c1 = decoder_1_out23 ? {undriven_71, 2'b11} : 7'bz;  // Controlled_Buffer controlled_buffer_78
  assign c2 = decoder_1_out23 ? {undriven_69[6:3], 1'b1, undriven_69[1:0]} : 7'bz;  // Controlled_Buffer controlled_buffer_79
  assign c0 = decoder_1_out23 ? {{5{1'b1}}, undriven_73} : 7'bz;  // Controlled_Buffer controlled_buffer_80
  assign c2 = decoder_1_out8 ? {undriven_77[6:5], 1'b1, undriven_77[3:0]} : 7'bz;  // Controlled_Buffer controlled_buffer_81
  assign c0 = decoder_1_out8 ? {7{1'b1}} : 7'bz;  // Controlled_Buffer controlled_buffer_82
  assign c3 = decoder_1_out8 ? {undriven_75[6:5], 1'b1, undriven_75[3:0]} : 7'bz;  // Controlled_Buffer controlled_buffer_83
  assign c1 = decoder_1_out8 ? {undriven_79[6:5], 1'b1, undriven_79[3:0]} : 7'bz;  // Controlled_Buffer controlled_buffer_84
  assign c4 = decoder_1_out8 ? {7{1'b1}} : 7'bz;  // Controlled_Buffer controlled_buffer_85
  assign c0 = decoder_1_out24 ? {1'b1, undriven_81, 1'b1} : 7'bz;  // Controlled_Buffer controlled_buffer_86
  assign c1 = decoder_1_out24 ? {undriven_80[6], 2'b11, undriven_80[3], 2'b11, undriven_80[0]} : 7'bz;  // Controlled_Buffer controlled_buffer_87
  assign c4 = decoder_1_out24 ? {1'b1, undriven_74, 1'b1} : 7'bz;  // Controlled_Buffer controlled_buffer_88
  assign c3 = decoder_1_out24 ? {undriven_76[6], 2'b11, undriven_76[3], 2'b11, undriven_76[0]} : 7'bz;  // Controlled_Buffer controlled_buffer_89
  assign c2 = decoder_1_out24 ? {undriven_78[6:4], 1'b1, undriven_78[2:0]} : 7'bz;  // Controlled_Buffer controlled_buffer_90
  assign c3 = decoder_1_out9 ? {1'b1, undriven_84, 1'b1} : 7'bz;  // Controlled_Buffer controlled_buffer_91
  assign c2 = decoder_1_out9 ? {7{1'b1}} : 7'bz;  // Controlled_Buffer controlled_buffer_92
  assign c4 = decoder_1_out9 ? {1'b1, undriven_82, 1'b1} : 7'bz;  // Controlled_Buffer controlled_buffer_93
  assign c4 = decoder_1_out25 ? {2'b11, undriven_83} : 7'bz;  // Controlled_Buffer controlled_buffer_94
  assign c2 = decoder_1_out25 ? {undriven_86, 4'b1111} : 7'bz;  // Controlled_Buffer controlled_buffer_95
  assign c3 = decoder_1_out25 ? {undriven_85[6:5], 1'b1, undriven_85[3:0]} : 7'bz;  // Controlled_Buffer controlled_buffer_96
  assign c4 = decoder_1_out10 ? {1'b1, undriven_91[5:3], 2'b11, undriven_91[0]} : 7'bz;  // Controlled_Buffer controlled_buffer_97
  assign c1 = decoder_1_out9 ? {1'b1, undriven_87, 1'b1} : 7'bz;  // Controlled_Buffer controlled_buffer_98
  assign c0 = decoder_1_out9 ? {1'b1, undriven_89, 1'b1} : 7'bz;  // Controlled_Buffer controlled_buffer_99
  assign c1 = decoder_1_out25 ? {undriven_88[6:5], 1'b1, undriven_88[3:0]} : 7'bz;  // Controlled_Buffer controlled_buffer_100
  assign c0 = decoder_1_out25 ? {2'b11, undriven_90} : 7'bz;  // Controlled_Buffer controlled_buffer_101
  assign c4 = decoder_1_out26 ? {1'b1, undriven_92, 3'b111} : 7'bz;  // Controlled_Buffer controlled_buffer_102
  assign c3 = decoder_1_out10 ? {1'b1, undriven_93, 1'b1} : 7'bz;  // Controlled_Buffer controlled_buffer_103
  assign c1 = decoder_1_out10 ? {1'b1, undriven_97, 1'b1} : 7'bz;  // Controlled_Buffer controlled_buffer_104
  assign c2 = decoder_1_out10 ? {1'b1, undriven_95, 1'b1} : 7'bz;  // Controlled_Buffer controlled_buffer_105
  assign c0 = decoder_1_out10 ? {{6{1'b1}}, undriven_99[0]} : 7'bz;  // Controlled_Buffer controlled_buffer_106
  assign c2 = decoder_1_out26 ? {1'b1, undriven_96[5], 1'b1, undriven_96[3:1], 1'b1} : 7'bz;  // Controlled_Buffer controlled_buffer_107
  assign c3 = decoder_1_out26 ? {1'b1, undriven_94[5:4], 1'b1, undriven_94[2:1], 1'b1} : 7'bz;  // Controlled_Buffer controlled_buffer_108
  assign c0 = decoder_1_out26 ? {2'b11, undriven_100, 1'b1} : 7'bz;  // Controlled_Buffer controlled_buffer_109
  assign c1 = decoder_1_out26 ? {1'b1, undriven_98[5], 1'b1, undriven_98[3:1], 1'b1} : 7'bz;  // Controlled_Buffer controlled_buffer_110
  assign c1 = decoder_1_out11 ? {undriven_106[6], 1'b1, undriven_106[4:2], 1'b1, undriven_106[0]} : 7'bz;  // Controlled_Buffer controlled_buffer_111
  assign c2 = decoder_1_out11 ? {undriven_104[6:5], 1'b1, undriven_104[3], 1'b1, undriven_104[1:0]} : 7'bz;  // Controlled_Buffer controlled_buffer_112
  assign c0 = decoder_1_out11 ? {1'b1, undriven_108, 1'b1} : 7'bz;  // Controlled_Buffer controlled_buffer_113
  assign c3 = decoder_1_out11 ? {undriven_102[6:4], 1'b1, undriven_102[2:0]} : 7'bz;  // Controlled_Buffer controlled_buffer_114
  assign c4 = decoder_1_out11 ? {7{1'b1}} : 7'bz;  // Controlled_Buffer controlled_buffer_115
  assign c2 = decoder_1_out27 ? undriven_105 : 7'bz;  // Controlled_Buffer controlled_buffer_116
  assign c0 = decoder_1_out27 ? undriven_109 : 7'bz;  // Controlled_Buffer controlled_buffer_117
  assign c4 = decoder_1_out27 ? undriven_101 : 7'bz;  // Controlled_Buffer controlled_buffer_118
  assign c3 = decoder_1_out27 ? {undriven_103, 1'b1} : 7'bz;  // Controlled_Buffer controlled_buffer_119
  assign c1 = decoder_1_out27 ? undriven_107 : 7'bz;  // Controlled_Buffer controlled_buffer_120
  assign c2 = decoder_1_out12 ? {undriven_113, 1'b1} : 7'bz;  // Controlled_Buffer controlled_buffer_121
  assign c0 = decoder_1_out12 ? {undriven_117, 1'b1} : 7'bz;  // Controlled_Buffer controlled_buffer_122
  assign c1 = decoder_1_out12 ? {undriven_115, 1'b1} : 7'bz;  // Controlled_Buffer controlled_buffer_123
  assign c4 = decoder_1_out12 ? {7{1'b1}} : 7'bz;  // Controlled_Buffer controlled_buffer_124
  assign c3 = decoder_1_out12 ? {undriven_111, 1'b1} : 7'bz;  // Controlled_Buffer controlled_buffer_125
  assign c0 = decoder_1_out28 ? undriven_118 : 7'bz;  // Controlled_Buffer controlled_buffer_126
  assign c4 = decoder_1_out28 ? undriven_110 : 7'bz;  // Controlled_Buffer controlled_buffer_127
  assign c2 = decoder_1_out28 ? {{5{1'b1}}, undriven_114[1], 1'b1} : 7'bz;  // Controlled_Buffer controlled_buffer_128
  assign c1 = decoder_1_out28 ? undriven_116 : 7'bz;  // Controlled_Buffer controlled_buffer_129
  assign c3 = decoder_1_out28 ? undriven_112 : 7'bz;  // Controlled_Buffer controlled_buffer_130
  assign c4 = decoder_1_out13 ? {7{1'b1}} : 7'bz;  // Controlled_Buffer controlled_buffer_131
  assign c3 = decoder_1_out13 ? {1'b1, undriven_120} : 7'bz;  // Controlled_Buffer controlled_buffer_132
  assign c2 = decoder_1_out13 ? {undriven_122[6], 3'b111, undriven_122[2:0]} : 7'bz;  // Controlled_Buffer controlled_buffer_133
  assign c2 = decoder_1_out29 ? {1'b1, undriven_123[5:3], 1'b1, undriven_123[1], 1'b1} : 7'bz;  // Controlled_Buffer controlled_buffer_134
  assign c4 = decoder_1_out29 ? {undriven_119[6], 1'b1, undriven_119[4:0]} : 7'bz;  // Controlled_Buffer controlled_buffer_135
  assign c3 = decoder_1_out29 ? {1'b1, undriven_121} : 7'bz;  // Controlled_Buffer controlled_buffer_136
  assign c0 = decoder_1_out13 ? {7{1'b1}} : 7'bz;  // Controlled_Buffer controlled_buffer_137
  assign c1 = decoder_1_out13 ? {1'b1, undriven_124} : 7'bz;  // Controlled_Buffer controlled_buffer_138
  assign c4 = decoder_1_out14 ? {7{1'b1}} : 7'bz;  // Controlled_Buffer controlled_buffer_139
  assign c1 = decoder_1_out29 ? {1'b1, undriven_125[5:4], 1'b1, undriven_125[2:0]} : 7'bz;  // Controlled_Buffer controlled_buffer_140
  assign c4 = decoder_1_out30 ? {undriven_127[6:2], 1'b1, undriven_127[0]} : 7'bz;  // Controlled_Buffer controlled_buffer_141
  assign c0 = decoder_1_out29 ? {undriven_126[6], 2'b11, undriven_126[3:0]} : 7'bz;  // Controlled_Buffer controlled_buffer_142
  assign c0 = decoder_1_out14 ? {7{1'b1}} : 7'bz;  // Controlled_Buffer controlled_buffer_143
  assign c2 = decoder_1_out14 ? {undriven_130[6], {5{1'b1}}, undriven_130[0]} : 7'bz;  // Controlled_Buffer controlled_buffer_144
  assign c1 = decoder_1_out14 ? {undriven_132, 1'b1} : 7'bz;  // Controlled_Buffer controlled_buffer_145
  assign c3 = decoder_1_out14 ? {1'b1, undriven_128} : 7'bz;  // Controlled_Buffer controlled_buffer_146
  assign c2 = decoder_1_out30 ? {undriven_131, 1'b1} : 7'bz;  // Controlled_Buffer controlled_buffer_147
  assign c3 = decoder_1_out30 ? {undriven_129[6], 1'b1, undriven_129[4:1], 1'b1} : 7'bz;  // Controlled_Buffer controlled_buffer_148
  assign c1 = decoder_1_out30 ? {undriven_133[6], 1'b1, undriven_133[4:1], 1'b1} : 7'bz;  // Controlled_Buffer controlled_buffer_149
  assign c0 = decoder_1_out30 ? {undriven_134[6:2], 1'b1, undriven_134[0]} : 7'bz;  // Controlled_Buffer controlled_buffer_150
  assign c0 = decoder_1_out15 ? {undriven_143[6], {5{1'b1}}, undriven_143[0]} : 7'bz;  // Controlled_Buffer controlled_buffer_151
  assign c3 = decoder_1_out15 ? {1'b1, undriven_137, 1'b1} : 7'bz;  // Controlled_Buffer controlled_buffer_152
  assign c4 = decoder_1_out15 ? {undriven_135[6], {5{1'b1}}, undriven_135[0]} : 7'bz;  // Controlled_Buffer controlled_buffer_153
  assign c2 = decoder_1_out15 ? {1'b1, undriven_139, 1'b1} : 7'bz;  // Controlled_Buffer controlled_buffer_154
  assign c1 = decoder_1_out15 ? {1'b1, undriven_141, 1'b1} : 7'bz;  // Controlled_Buffer controlled_buffer_155
  assign c1 = decoder_1_out31 ? {undriven_142[6], 1'b1, undriven_142[4:3], 1'b1, undriven_142[1:0]} : 7'bz;  // Controlled_Buffer controlled_buffer_156
  assign c0 = decoder_1_out31 ? {undriven_144[6:2], 1'b1, undriven_144[0]} : 7'bz;  // Controlled_Buffer controlled_buffer_157
  assign c4 = decoder_1_out31 ? {undriven_136[6:2], 1'b1, undriven_136[0]} : 7'bz;  // Controlled_Buffer controlled_buffer_158
  assign c3 = decoder_1_out31 ? {undriven_138[6], 1'b1, undriven_138[4:3], 1'b1, undriven_138[1:0]} : 7'bz;  // Controlled_Buffer controlled_buffer_159
  assign c2 = decoder_1_out31 ? {undriven_140[6:3], 1'b1, undriven_140[1:0]} : 7'bz;  // Controlled_Buffer controlled_buffer_160
  Pull_Resistor pull_resistor_1 (.node(c4[6]));
  Pull_Resistor pull_resistor_2 (.node(c4[5]));
  Pull_Resistor pull_resistor_3 (.node(c4[1]));
  Pull_Resistor pull_resistor_4 (.node(c4[3]));
  Pull_Resistor pull_resistor_5 (.node(c4[2]));
  Pull_Resistor pull_resistor_6 (.node(c4[4]));
  Pull_Resistor pull_resistor_7 (.node(c4[0]));
  Pull_Resistor pull_resistor_8 (.node(c3[6]));
  Pull_Resistor pull_resistor_9 (.node(c3[5]));
  Pull_Resistor pull_resistor_10 (.node(c3[2]));
  Pull_Resistor pull_resistor_11 (.node(c3[4]));
  Pull_Resistor pull_resistor_12 (.node(c3[3]));
  Pull_Resistor pull_resistor_13 (.node(c3[0]));
  Pull_Resistor pull_resistor_14 (.node(c3[1]));
  Pull_Resistor pull_resistor_15 (.node(c2[4]));
  Pull_Resistor pull_resistor_16 (.node(c2[5]));
  Pull_Resistor pull_resistor_17 (.node(c2[6]));
  Pull_Resistor pull_resistor_18 (.node(c2[3]));
  Pull_Resistor pull_resistor_19 (.node(c2[1]));
  Pull_Resistor pull_resistor_20 (.node(c2[2]));
  Pull_Resistor pull_resistor_21 (.node(c2[0]));
  Pull_Resistor pull_resistor_22 (.node(c1[6]));
  Pull_Resistor pull_resistor_23 (.node(c1[5]));
  Pull_Resistor pull_resistor_24 (.node(c1[1]));
  Pull_Resistor pull_resistor_25 (.node(c1[4]));
  Pull_Resistor pull_resistor_26 (.node(c1[3]));
  Pull_Resistor pull_resistor_27 (.node(c1[2]));
  Pull_Resistor pull_resistor_28 (.node(c1[0]));
  Pull_Resistor pull_resistor_29 (.node(c0[3]));
  Pull_Resistor pull_resistor_30 (.node(c0[5]));
  Pull_Resistor pull_resistor_31 (.node(c0[6]));
  Pull_Resistor pull_resistor_32 (.node(c0[4]));
  Pull_Resistor pull_resistor_33 (.node(c0[1]));
  Pull_Resistor pull_resistor_34 (.node(c0[2]));
  Pull_Resistor pull_resistor_35 (.node(c0[0]));
endmodule

module Control_Unit (
  input  [3:0] in_1,
  output [1:0] PCmux,
  output [1:0] Wmux,
  output [1:0] Dmux,
  output ImmMux,
  output ALUMux,
  output Flag,
  output [2:0] ALUcode,
  output Push_Pop,
  output StackEn,
  output RegEn,
  output DataR_W,
  output DataEn,
  output Halt
);

  wire and_1_out, and_2_out, and_11_out, and_15_out, and_16_out, not_1_out, or_1_out, or_2_out, xnor_1_out;
  wire [1:0] xor_1_out;
  wire [1:1] and_7_out, and_8_out, or_5_out;
  wire [2:0] adder_1_out;
  wire [2:2] and_10_out;

  not not_1 (not_1_out, in_1[3]);
  or or_1 (or_1_out, not_1_out, in_1[2]);
  and and_1 (and_1_out, or_1_out, in_1[1]);
  and and_2 (and_2_out, in_1[3], ~in_1[2], ~in_1[1]);  // AND_Gate
  and and_3 (DataR_W, in_1[1], in_1[0]);
  and and_4 (DataEn, in_1[1], in_1[2], in_1[3]);
  and and_5 (Halt, in_1[0], ~in_1[1], ~in_1[2], ~in_1[3]);  // AND_Gate
  and and_6 (ImmMux, in_1[1], in_1[2], in_1[3]);
  xnor xnor_1 (xnor_1_out, in_1[1], in_1[2]);
  or or_2 (or_2_out, in_1[1], in_1[2]);
  Adder #(.width(3)) adder_1 (.a(in_1[2:0]), .b(3'b110), .out(adder_1_out));  // open: cin, cout
  or or_3 (RegEn, and_1_out, and_2_out);
  and and_7 (and_7_out[1], in_1[0], in_1[2]);
  and and_8 (and_8_out[1], in_1[0], in_1[1]);
  Multiplexer #(.select(4), .width(2)) multiplexer_1 (
    .in2(2'b00), .in3(2'b00), .in4(2'b00), .in5(2'b00), .in6(2'b00), .in7(2'b00), .in8(2'b01), .in9(2'b01),
    .in14(2'b10), .in15(2'b11), .out(Wmux), .sel(in_1));  // open: in0, in1, in10, in11, in12, in13, en
  and and_9 (ALUMux, xnor_1_out, in_1[3]);
  and and_10 (and_10_out[2], or_2_out, ~in_1[3]);  // AND_Gate
  and and_11 (and_11_out, in_1[0], ~in_1[1], ~in_1[2], in_1[3]);  // AND_Gate
  assign xor_1_out = {and_7_out[1], in_1[3]} ^ {2{and_8_out[1]}};  // XOR_Gate xor_1, 2 bits wide
  or or_4 (Flag, and_10_out[2], and_11_out);
  assign ALUcode = {3{and_10_out[2]}} & adder_1_out;  // AND_Gate and_12, 3 bits wide
  and and_13 (Push_Pop, in_1[0], ~in_1[1], in_1[2], in_1[3]);  // AND_Gate
  and and_14 (StackEn, in_1[3], in_1[2], ~in_1[1]);  // AND_Gate
  Multiplexer #(.select(4), .width(2)) multiplexer_2 (
    .in2(2'b00), .in3(2'b00), .in4(2'b00), .in5(2'b00), .in6(2'b00), .in7(2'b00), .in8(2'b01), .in9(2'b00),
    .in14(2'b10), .out(Dmux), .sel(in_1));  // open: in0, in1, in10, in11, in12, in13, in15, en
  and and_15 (and_15_out, in_1[2], in_1[3], ~in_1[1]);  // AND_Gate
  or or_5 (or_5_out[1], and_15_out, and_16_out);
  and and_16 (and_16_out, in_1[3], in_1[1], ~in_1[2]);  // AND_Gate
  assign PCmux = {2{or_5_out[1]}} & xor_1_out;  // AND_Gate and_17, 2 bits wide
endmodule

module Controls (
  input  in_1,
  input  in_2,
  input  in_3,
  input  in_4,
  input  in_5,
  input  in_6,
  input  in_7,
  input  in_8,
  input  control,
  input  in_10,
  output [7:0] out_11
);

  wire and_1_out, nand_2_out, nand_4_out, nand_6_out, nand_8_out, nand_10_out, nand_12_out, nand_14_out,
       nand_16_out, not_1_out;

  not not_1 (not_1_out, in_10);
  and and_1 (and_1_out, control, not_1_out);
  nand nand_1 (out_11[7], ~in_1, nand_2_out);  // NAND_Gate
  nand nand_2 (nand_2_out, out_11[7], ~and_1_out);  // NAND_Gate
  nand nand_3 (out_11[6], ~in_2, nand_4_out);  // NAND_Gate
  nand nand_4 (nand_4_out, out_11[6], ~and_1_out);  // NAND_Gate
  nand nand_5 (out_11[5], ~in_3, nand_6_out);  // NAND_Gate
  nand nand_6 (nand_6_out, out_11[5], ~and_1_out);  // NAND_Gate
  nand nand_7 (out_11[4], ~in_4, nand_8_out);  // NAND_Gate
  nand nand_8 (nand_8_out, out_11[4], ~and_1_out);  // NAND_Gate
  nand nand_9 (out_11[3], ~in_5, nand_10_out);  // NAND_Gate
  nand nand_10 (nand_10_out, out_11[3], ~and_1_out);  // NAND_Gate
  nand nand_11 (out_11[2], ~in_6, nand_12_out);  // NAND_Gate
  nand nand_12 (nand_12_out, out_11[2], ~and_1_out);  // NAND_Gate
  nand nand_13 (out_11[1], ~in_7, nand_14_out);  // NAND_Gate
  nand nand_14 (nand_14_out, out_11[1], ~and_1_out);  // NAND_Gate
  nand nand_15 (out_11[0], ~in_8, nand_16_out);  // NAND_Gate
  nand nand_16 (nand_16_out, out_11[0], ~and_1_out);  // NAND_Gate
endmodule
